// Logisim project lutcomp.circ as structural Verilog: 7 circuits, main circuit main
// 10
module main (
  output halt
);

  wire and_1_out, clock_1_out, comparator_1_gt, decoder_1_out0, decoder_1_out1, decoder_1_out2,
       decoder_1_out3, decoder_1_out4, key_ctrl_1_key_clk, key_ctrl_1_key_read_en, key_ctrl_1_rdy,
       keyboard_1_avail, mmu_1_key_discard, mmu_1_ttyclk, or_1_out, or_2_out, undriven_2, undriven_3,
       undriven_5;
  wire [2:0] counter_1_q;
  wire [3:0] FLAGS_q, rom_2_data, rom_2_data_2, undriven_4;
  wire [4:0] rom_1_data;
  wire [6:0] keyboard_1_data, mmu_1_ttydata;
  wire [7:0] adder_1_out, mmu_1_data_out, multiplexer_1_out, register_1_q, undriven, uPC_q;
  wire [14:0] undriven_6;
  wire [23:0] ADDR_q;

  Clock clock_1 (.out(clock_1_out));
  Counter #(.width(3), .max('h4), .behavior("old")) counter_1 (
    .Q(counter_1_q), .clk(clock_1_out), .clr(halt));  // open: load, D, count, carry, preset
  Adder adder_1 (.a(uPC_q), .b(8'h1), .out(adder_1_out));  // open: cin, cout
  Decoder #(.select(3), .disabled(0)) decoder_1 (
    .out0(decoder_1_out0), .out1(decoder_1_out1), .out2(decoder_1_out2), .out3(decoder_1_out3),
    .out4(decoder_1_out4), .sel(counter_1_q), .en(comparator_1_gt));  // open: out5, out6, out7
  Multiplexer #(.width(8), .enable("false")) multiplexer_1 (
    .in0(adder_1_out), .in1(undriven), .out(multiplexer_1_out), .sel(undriven_2));
  Register #(.Select("low")) register_1 (
    .D(multiplexer_1_out), .Q(register_1_q), .clk(decoder_1_out3));  // open: en, clr
  Register #(.Select("low")) uPC (.D(register_1_q), .Q(uPC_q), .clk(decoder_1_out4));  // open: en, clr
  // Probe on rom_1_data[4]
  Comparator comparator_1 (.a(uPC_q), .b({8{1'b1}}), .gt(comparator_1_gt), .eq(halt));  // open: lt
  // Probe on rom_1_data[3:0]
  ROM #(.Select("high")) rom_1 (.addr(uPC_q), .data({undriven_6[14:12], rom_1_data}));
  // Probe on rom_1_data[3:0]
  Register #(.Select("low")) ADDR (.D(undriven), .en(undriven_3), .Q(ADDR_q[7:0]), .clk(decoder_1_out3));  // open: clr
  Keyboard keyboard_1 (
    .clk(key_ctrl_1_key_clk), .re(key_ctrl_1_key_read_en), .avail(keyboard_1_avail), .data(keyboard_1_data));  // open: clr
  assign undriven_6[7:4] = rom_1_data[4] ? rom_1_data[3:0] : 4'bz;  // Controlled_Buffer controlled_buffer_1
  key_ctrl key_ctrl_1 (
    .key_avail(keyboard_1_avail), .discard(mmu_1_key_discard), .key_clk(key_ctrl_1_key_clk),
    .key_read_en(key_ctrl_1_key_read_en), .rdy(key_ctrl_1_rdy));
  // Probe on undriven_6[14:12]
  assign undriven_6[7:4] = rom_1_data[4] ? undriven_4 : 4'bz;  // Controlled_Buffer controlled_buffer_2
  mmu mmu_1 (
    .data_in(undriven), .key_char(keyboard_1_data), .key_rdy(key_ctrl_1_rdy), .addr(ADDR_q),
    .store(and_1_out), .clk(or_2_out), .key_discard(mmu_1_key_discard), .ttydata(mmu_1_ttydata),
    .ttyclk(mmu_1_ttyclk), .data_out(mmu_1_data_out));
  // Probe on mmu_1_data_out
  TTY #(.trigger("falling")) tty_1 (.data(mmu_1_ttydata), .clk(mmu_1_ttyclk));  // open: we, clr
  // Probe on undriven_6[7:4]
  and and_1 (and_1_out, or_1_out, undriven_5);
  or or_1 (or_1_out, decoder_1_out2, decoder_1_out3);
  or or_2 (or_2_out, decoder_1_out3, decoder_1_out1);
  // Probe on undriven_6[3:0]
  Register #(.width(4), .Select("low")) FLAGS (.D(rom_2_data_2), .Q(FLAGS_q), .clk(decoder_1_out0));  // open: en, clr
  ROM #(.addrWidth(15), .Select("high")) rom_2 (
    .addr({undriven_6[14:12], FLAGS_q, undriven_6[7:0]}), .data({rom_2_data_2, rom_2_data}));
  Register #(.width(4), .Select("low")) LUT_OUT (.D(rom_2_data), .clk(decoder_1_out0));  // open: en, Q, clr
  // Pins of 8 and 24 bits meet at ADDR_q

  // Notes on the sheet:
  //   instructions
  //   out sel
  //   inst part2
  //   contents of rom_1 (hex, n*v repeats v):
  //   1 3e 0 ff 80 f9 1 ff 2 ff ff 7f 1 0 2e 1 1 1 ff 2 ff
  //   opcode
  //   operand2
  //   mem_data_out
  //   operand1/acc
  //   ALU LUT
  //   contents of rom_2 (hex, n*v repeats v):
  //   256*0 256*1 256*2 256*3 256*4 256*5 256*6 256*7 256*8 256*9 256*a 256*b 256*c 256*d 256*e 256*f
  //   256*10 256*11 256*12 256*13 256*14 256*15 256*16 256*17 256*18 256*19 256*1a 256*1b 256*1c 256*1d
  //   256*1e 256*1f 256*20 256*21 256*22 256*23 256*24 256*25 256*26 256*27 256*28 256*29 256*2a 256*2b
  //   256*2c 256*2d 256*2e 256*2f 256*30 256*31 256*32 256*33 256*34 256*35 256*36 256*37 256*38 256*39
  //   256*3a 256*3b 256*3c 256*3d 256*3e 256*3f 256*40 256*41 256*42 256*43 256*44 256*45 256*46 256*47
  //   256*48 256*49 256*4a 256*4b 256*4c 256*4d 256*4e 256*4f 256*50 256*51 256*52 256*53 256*54 256*55
  //   256*56 256*57 256*58 256*59 256*5a 256*5b 256*5c 256*5d 256*5e 256*5f 256*60 256*61 256*62 256*63
  //   256*64 256*65 256*66 256*67 256*68 256*69 256*6a 256*6b 256*6c 256*6d 256*6e 256*6f 256*70 256*71
  //   256*72 256*73 256*74 256*75 256*76 256*77 256*78 256*79 256*7a 256*7b 256*7c 256*7d 256*7e 256*7f
endmodule

module mmu (
  input  [7:0] data_in,
  input  [6:0] key_char,
  input  key_rdy,
  input  [23:0] addr,
  input  store,
  input  clk,
  output key_discard,
  output [6:0] ttydata,
  output ttyclk,
  output [7:0] data_out
);

  wire and_1_out, and_2_out, and_3_out, comparator_1_eq, comparator_1_gt, comparator_1_lt, not_1_out;
  wire [7:0] controlled_buffer_4_out;

  assign data_out = store ? data_in : 8'bz;  // Controlled_Buffer controlled_buffer_1
  Comparator #(.width(24)) comparator_1 (
    .a(24'h1), .b(addr), .gt(comparator_1_gt), .eq(comparator_1_eq), .lt(comparator_1_lt));
  not not_1 (not_1_out, store);
  assign data_out = and_1_out ? {key_rdy, key_char} : 8'bz;  // Controlled_Buffer controlled_buffer_2
  and and_1 (and_1_out, comparator_1_gt, not_1_out);
  assign data_out = and_2_out ? 8'hcc : 8'bz;  // Controlled_Buffer controlled_buffer_3
  and and_2 (and_2_out, comparator_1_eq, not_1_out);
  assign controlled_buffer_4_out = store ? data_out : 8'bz;  // Controlled_Buffer controlled_buffer_4
  RAM #(.addrWidth(24), .Select("high")) ram_1 (
    .addr(addr), .data(controlled_buffer_4_out), .clk(clk), .ld(not_1_out));  // open: sel, clr
  assign data_out = and_3_out ? controlled_buffer_4_out : 8'bz;  // Controlled_Buffer controlled_buffer_5
  and and_3 (and_3_out, comparator_1_lt, not_1_out);
  and and_4 (key_discard, data_out[7], store, clk, comparator_1_gt);
  and and_5 (ttyclk, comparator_1_eq, store, clk);

  assign ttydata = data_out[6:0];

  // Notes on the sheet:
  //   addr == 1
  //   addr > 1
  //   addr == 0
endmodule

module key_ctrl (
  input  key_avail,
  input  discard,
  output key_clk,
  output key_read_en,
  output rdy
);

  wire and_1_out, and_3_out, and_4_out, clock_1_out, d_ff_1_q, d_ff_2_q, decoder_1_out0, decoder_1_out1,
       decoder_1_out2, decoder_1_out3, decoder_1_out4;
  wire [2:0] counter_1_q;

  Clock clock_1 (.out(clock_1_out));
  Decoder #(.select(3), .disabled(0), .enable("false")) decoder_1 (
    .out0(decoder_1_out0), .out1(decoder_1_out1), .out2(decoder_1_out2), .out3(decoder_1_out3),
    .out4(decoder_1_out4), .sel(counter_1_q));  // open: out5, out6, out7
  Counter #(.width(3), .max('h4), .trigger("falling"), .behavior("old")) counter_1 (
    .Q(counter_1_q), .clk(clock_1_out));  // open: load, D, count, carry, clr, preset
  or or_1 (key_clk, decoder_1_out0, and_1_out);
  and and_1 (and_1_out, decoder_1_out2, d_ff_2_q);
  or or_2 (key_read_en, decoder_1_out1, decoder_1_out2);
  D_Flip_Flop d_ff_1 (.clk(and_1_out), .D(1'b1), .Q(d_ff_1_q), .reset(and_4_out));  // open: Qn, preset
  D_Flip_Flop d_ff_2 (.clk(discard), .D(1'b1), .Q(d_ff_2_q), .reset(and_4_out));  // open: Qn, preset
  and and_2 (rdy, key_avail, ~and_3_out);  // AND_Gate
  and and_3 (and_3_out, d_ff_1_q, decoder_1_out3);
  and and_4 (and_4_out, d_ff_1_q, decoder_1_out4);
endmodule

module regs (
  input  [3:0] D,
  input  [3:0] index,
  input  W,
  input  R,
  input  ADDR_CLK,
  output [3:0] QLO,
  output [3:0] QHI,
  output [3:0] Q,
  output [23:0] ADDR
);

  wire and_1_out, and_2_out, not_1_out, sn74ls156_1__1y0, sn74ls156_1__1y1, sn74ls156_1__1y2,
       sn74ls156_1__1y3, sn74ls156_1__2y0, sn74ls156_1__2y1, sn74ls156_1__2y2, sn74ls156_1__2y3;

  SN74LS156 sn74ls156_1 (
    .n1G(W), ._1C(1'b1), .SEL({index[3], index[0]}), .n2G(R), ._2C(1'b1), ._1Y0(sn74ls156_1__1y0),
    ._1Y1(sn74ls156_1__1y1), ._1Y2(sn74ls156_1__1y2), ._1Y3(sn74ls156_1__1y3), ._2Y0(sn74ls156_1__2y0),
    ._2Y1(sn74ls156_1__2y1), ._2Y2(sn74ls156_1__2y2), ._2Y3(sn74ls156_1__2y3));
  and and_1 (and_1_out, sn74ls156_1__2y0, sn74ls156_1__2y1);
  and and_2 (and_2_out, sn74ls156_1__2y2, sn74ls156_1__2y3);
  SN74LS670 sn74ls670_1 (.W(index[2:1]), .nGW(sn74ls156_1__1y0), .R(index[2:1]), .nGR(and_1_out), .D(D), .Q(QLO));
  SN74LS670 sn74ls670_2 (.W(index[2:1]), .nGW(sn74ls156_1__1y1), .R(index[2:1]), .nGR(and_1_out), .D(D), .Q(QHI));
  SN74LS670 sn74ls670_3 (.W(index[2:1]), .nGW(sn74ls156_1__1y2), .R(index[2:1]), .nGR(and_2_out), .D(D), .Q(QLO));
  SN74LS670 sn74ls670_4 (.W(index[2:1]), .nGW(sn74ls156_1__1y3), .R(index[2:1]), .nGR(and_2_out), .D(D), .Q(QHI));
  Multiplexer #(.width(4)) multiplexer_1 (.in0(QLO), .in1(QHI), .out(D), .sel(index[0]), .en(not_1_out));
  not not_1 (not_1_out, R);
  _74LS377 u_74ls377_1 (.D({QHI, QLO}), .nEN(sn74ls156_1__2y0), .CLK(ADDR_CLK), .Q(ADDR[7:0]));
  _74LS377 u_74ls377_2 (.D({QHI, QLO}), .nEN(sn74ls156_1__2y1), .CLK(ADDR_CLK), .Q(ADDR[15:8]));
  _74LS377 u_74ls377_3 (.D({QHI, QLO}), .nEN(sn74ls156_1__2y2), .CLK(ADDR_CLK), .Q(ADDR[23:16]));

  assign Q = D;

  // Notes on the sheet:
  //   R: pull=up
  //   W: pull=up
endmodule

module SN74LS670 (
  input  [1:0] W,
  input  nGW,
  input  [1:0] R,
  input  nGR,
  input  [3:0] D,
  output [3:0] Q
);

  wire decoder_1_out0, decoder_1_out1, decoder_1_out2, decoder_1_out3, decoder_2_out0, decoder_2_out1,
       decoder_2_out2, decoder_2_out3, not_1_out;
  wire [3:0] register_1_q, register_2_q, register_3_q, register_4_q;

  not not_1 (not_1_out, nGR);
  Decoder #(.select(2), .disabled(0), .enable("false")) decoder_1 (
    .out0(decoder_1_out0), .out1(decoder_1_out1), .out2(decoder_1_out2), .out3(decoder_1_out3), .sel(W));
  Decoder #(.select(2), .disabled(0)) decoder_2 (
    .out0(decoder_2_out0), .out1(decoder_2_out1), .out2(decoder_2_out2), .out3(decoder_2_out3), .sel(R),
    .en(not_1_out));
  Register #(.width(4), .Select("low")) register_1 (
    .D(D), .en(decoder_1_out0), .Q(register_1_q), .clk(nGW));  // open: clr
  Register #(.width(4), .Select("low")) register_2 (
    .D(D), .en(decoder_1_out1), .Q(register_2_q), .clk(nGW));  // open: clr
  Register #(.width(4), .Select("low")) register_3 (
    .D(D), .en(decoder_1_out2), .Q(register_3_q), .clk(nGW));  // open: clr
  Register #(.width(4), .Select("low")) register_4 (
    .D(D), .en(decoder_1_out3), .Q(register_4_q), .clk(nGW));  // open: clr
  assign Q = decoder_2_out0 ? register_1_q : 4'bz;  // Controlled_Buffer controlled_buffer_1
  assign Q = decoder_2_out1 ? register_2_q : 4'bz;  // Controlled_Buffer controlled_buffer_2
  assign Q = decoder_2_out2 ? register_3_q : 4'bz;  // Controlled_Buffer controlled_buffer_3
  assign Q = decoder_2_out3 ? register_4_q : 4'bz;  // Controlled_Buffer controlled_buffer_4
endmodule

module SN74LS156 (
  input  n1G,
  input  _1C,
  input  [1:0] SEL,
  input  n2G,
  input  _2C,
  output _1Y0,
  output _1Y1,
  output _1Y2,
  output _1Y3,
  output _2Y0,
  output _2Y1,
  output _2Y2,
  output _2Y3
);

  wire and_1_out, and_2_out, decoder_1_out0, decoder_1_out1, decoder_1_out2, decoder_1_out3, decoder_2_out0,
       decoder_2_out1, decoder_2_out2, decoder_2_out3;

  and and_1 (and_1_out, ~n1G, _1C);  // AND_Gate
  and and_2 (and_2_out, ~n2G, _2C);  // AND_Gate
  Decoder #(.select(2), .disabled(0), .enable("false")) decoder_1 (
    .out0(decoder_1_out0), .out1(decoder_1_out1), .out2(decoder_1_out2), .out3(decoder_1_out3), .sel(SEL));
  Decoder #(.select(2), .disabled(0), .enable("false")) decoder_2 (
    .out0(decoder_2_out0), .out1(decoder_2_out1), .out2(decoder_2_out2), .out3(decoder_2_out3), .sel(SEL));
  Pull_Resistor #(.pull(1)) pull_resistor_1 (.node(_1Y0));
  Pull_Resistor #(.pull(1)) pull_resistor_2 (.node(_1Y1));
  Pull_Resistor #(.pull(1)) pull_resistor_3 (.node(_1Y2));
  assign _1Y0 = and_1_out ? ~decoder_1_out0 : 1'bz;  // Controlled_Inverter controlled_inverter_1
  assign _1Y1 = and_1_out ? ~decoder_1_out1 : 1'bz;  // Controlled_Inverter controlled_inverter_2
  assign _1Y2 = and_1_out ? ~decoder_1_out2 : 1'bz;  // Controlled_Inverter controlled_inverter_3
  Pull_Resistor #(.pull(1)) pull_resistor_4 (.node(_2Y1));
  Pull_Resistor #(.pull(1)) pull_resistor_5 (.node(_2Y0));
  Pull_Resistor #(.pull(1)) pull_resistor_6 (.node(_2Y2));
  assign _2Y0 = and_2_out ? ~decoder_2_out0 : 1'bz;  // Controlled_Inverter controlled_inverter_4
  assign _2Y1 = and_2_out ? ~decoder_2_out1 : 1'bz;  // Controlled_Inverter controlled_inverter_5
  assign _2Y2 = and_2_out ? ~decoder_2_out2 : 1'bz;  // Controlled_Inverter controlled_inverter_6
  Pull_Resistor #(.pull(1)) pull_resistor_7 (.node(_1Y3));
  assign _1Y3 = and_1_out ? ~decoder_1_out3 : 1'bz;  // Controlled_Inverter controlled_inverter_7
  Pull_Resistor #(.pull(1)) pull_resistor_8 (.node(_2Y3));
  assign _2Y3 = and_2_out ? ~decoder_2_out3 : 1'bz;  // Controlled_Inverter controlled_inverter_8
endmodule

module _74LS377 (
  input  [7:0] D,
  input  nEN,
  input  CLK,
  output [7:0] Q
);

  wire not_1_out;

  not not_1 (not_1_out, nEN);
  Register #(.Select("low")) register_1 (.D(D), .en(not_1_out), .Q(Q), .clk(CLK));  // open: clr
endmodule
