// Logisim project echochar.circ as structural Verilog: 1 circuit, main circuit main
module main (
  output halt
);

  wire clock_1_out, comparator_1_eq, decoder_1_out0, decoder_1_out1, decoder_1_out2, decoder_1_out3, or_1_out;
  wire [1:0] counter_1_q;
  wire [6:0] keyboard_1_data;
  wire [7:0] register_1_q;
  wire [7:7] keyboard_1_avail;

  Keyboard keyboard_1 (
    .clk(decoder_1_out1), .re(register_1_q[7]), .avail(keyboard_1_avail[7]), .data(keyboard_1_data));  // open: clr
  Clock clock_1 (.out(clock_1_out));
  Decoder #(.select(2), .disabled(0), .enable("false")) decoder_1 (
    .out0(decoder_1_out0), .out1(decoder_1_out1), .out2(decoder_1_out2), .out3(decoder_1_out3),
    .sel(counter_1_q));
  Counter #(.width(2), .max('h3), .trigger("falling")) counter_1 (
    .Q(counter_1_q), .clk(or_1_out));  // open: load, D, count, carry, clr
  or or_1 (or_1_out, clock_1_out, halt);
  Register register_1 (
    .D({keyboard_1_avail[7], keyboard_1_data}), .Q(register_1_q), .clk(decoder_1_out0), .clr(decoder_1_out3));  // open: en
  TTY tty_1 (.data(register_1_q[6:0]), .clk(register_1_q[7]));  // open: we, clr
  Comparator #(.width(7)) comparator_1 (.a(register_1_q[6:0]), .b(7'b0101110), .eq(comparator_1_eq));  // open: gt, lt
  and and_1 (halt, comparator_1_eq, decoder_1_out2);
endmodule
