// Digital circuit HD44780U.dig as structural Verilog
module HD44780U (
  input  [7:0] DB,
  input  E,
  input  RW,
  input  RS,
  input  CLK,
  output [6:0] AC,
  output [2:0] State,
  output Busy,
  output CmdReadState,
  output [1:0] BitMode,
  output [7:0] Cmd
);

  wire and_1_out, comparator_1_gt, driver_1_out, driver_2_out, not_1_out, not_2_out, not_3_out, not_4_out,
       u_HD44780U_charcol, u_HD44780U_charrow, u_HD44780U_pix_addr, u_HD44780U_pix_clk, u_HD44780U_pix_val,
       u_HD44780U_pixcol, u_HD44780U_pixrow;
  wire [1:0] u_HD44780U_pixstatepeek;
  wire [4:0] CGROM_d;
  wire [7:0] driver_3_out, u_HD44780U_db_out;
  wire [10:0] u_HD44780U_cgrom_addr;

  and and_1 (and_1_out, comparator_1_gt, CLK);
  not not_1 (not_1_out, E);
  assign driver_1_out = E ? RW : 1'bz;  // Driver driver_1
  assign driver_2_out = E ? RS : 1'bz;  // Driver driver_2
  assign driver_3_out = E ? DB : 8'bz;  // Driver driver_3
  not not_2 (not_2_out, not_1_out);
  not not_3 (not_3_out, not_2_out);
  not not_4 (not_4_out, not_3_out);
  PullDown pulldown_1 (.out(driver_1_out));
  PullDown #(.Bits(8)) pulldown_2 (.out(driver_3_out));
  PullDown pulldown_3 (.out(driver_2_out));
  Comparator #(.Bits(3)) comparator_1 (.a(State), .b(3'b011), .gt(comparator_1_gt));  // open: eq, lt
  HD44780U #(.applicationType("GHDL"), .CodeFile("HD44780U.vhdl")) u_HD44780U (
    .clk(and_1_out), .en(not_4_out), .rw(driver_1_out), .rs(driver_2_out), .db_in(driver_3_out),
    .cgrom_data(CGROM_d), .db_out(u_HD44780U_db_out), .cgrom_addr(u_HD44780U_cgrom_addr),
    .pix_addr(u_HD44780U_pix_addr), .pix_val(u_HD44780U_pix_val), .pix_clk(u_HD44780U_pix_clk),
    .StatePeek(State), .PixStatePeek(u_HD44780U_pixstatepeek), .PixRow(u_HD44780U_pixrow),
    .PixCol(u_HD44780U_pixcol), .AC(AC), .CharCol(u_HD44780U_charcol), .CharRow(u_HD44780U_charrow),
    .busy(Busy), .Cmd(Cmd), .CmdReadStatePeek(CmdReadState), .BitModePeek(BitMode));
  ROM #(.AddrBits(11), .Bits(5)) CGROM (.A(u_HD44780U_cgrom_addr), .sel(1'b1), .D(CGROM_d));
  assign DB = driver_1_out ? u_HD44780U_db_out : 8'bz;  // Driver driver_4
  // Probe on u_HD44780U_db_out
  // Probe on u_HD44780U_pixstatepeek
  // Probe on u_HD44780U_pixrow
  // Probe on u_HD44780U_pixcol
  // Probe on u_HD44780U_charcol
  // Probe on u_HD44780U_charrow
  Break #(.Cycles(10000000)) break_1 (.brk(u_HD44780U_pix_clk));
  GraphicCard #(.graphicHeight(40), .graphicWidth(120)) graphiccard_1 (
    .A(u_HD44780U_pix_addr), .str(1'b1), .C(u_HD44780U_pix_clk), .ld(1'b0), .B(1'b0), .D(u_HD44780U_pix_val));

  // Notes on the sheet:
  //   DB: default 48
  //   RS: default 1
  //   sim optimization
  //   contents of CGROM (hex, n*v repeats v):
  //   330*0,4*4,0,0,4,0,0,0,a,a,a,7*0,a,a,1f,a,1f,a,a,0,0,0,4,f,14,e
  //   ,5,1e,4,0,0,0,18,19,2,4,8,13,3,0,0,0,c,12,14,8,15,12,d,0,0,0,c
  //   ,4,8,7*0,2,4,8,8,8,4,2,0,0,0,8,4,2,2,2,4,8,4*0,4,15,e,15,4,5*0
  //   ,4,4,1f,4,4,8*0,c,4,8,6*0,1f,11*0,c,c,4*0,1,2,4,8,10,4*0,e,11
  //   ,13,15,19,11,e,0,0,0,4,c,4*4,e,0,0,0,e,11,1,2,4,8,1f,0,0,0,1f
  //   ,2,4,2,1,11,e,0,0,0,2,6,a,12,1f,2,2,0,0,0,1f,10,1e,1,1,11,e,0,0,0
  //   ,6,8,10,1e,11,11,e,0,0,0,1f,11,1,2,4,4,4,0,0,0,e,11,11,e,11,11
  //   ,e,0,0,0,e,11,11,f,1,2,c,4*0,c,c,0,c,c,5*0,c,c,0,c,4,8,0,0,0,2
  //   ,4,8,10,8,4,2,5*0,1f,0,1f,5*0,8,4,2,1,2,4,8,0,0,0,e,11,1,2,4,0
  //   ,4,0,0,0,e,11,1,d,15,15,e,0,0,0,e,11,11,11,1f,11,11,0,0,0,1e,11,11
  //   ,1e,11,11,1e,0,0,0,e,11,10,10,10,11,e,0,0,0,1c,12,11,11,11,12
  //   ,1c,0,0,0,1f,10,10,1e,10,10,1f,0,0,0,1f,10,10,1e,10,10,10,0,0,0
  //   ,e,11,10,17,11,11,f,0,0,0,11,11,11,1f,11,11,11,0,0,0,e,5*4,e,0,0,0
  //   ,7,4*2,12,c,0,0,0,11,12,14,18,14,12,11,0,0,0,6*10,1f,0,0,0,11
  //   ,1b,15,15,11,11,11,0,0,0,11,11,19,15,13,11,11,0,0,0,e,5*11,e,0,0,0
  //   ,1e,11,11,1e,10,10,10,0,0,0,e,11,11,11,15,12,d,0,0,0,1e,11,11
  //   ,1e,14,12,11,0,0,0,f,10,10,e,1,1,1e,0,0,0,1f,6*4,0,0,0,6*11,e
  //   ,0,0,0,5*11,a,4,0,0,0,11,11,11,15,15,15,a,0,0,0,11,11,a,4,a,11,11
  //   ,0,0,0,11,11,11,a,4,4,4,0,0,0,1f,1,2,4,8,10,1f,0,0,0,1c,5*10,1c
  //   ,0,0,0,11,a,1f,4,1f,4,4,0,0,0,e,5*2,e,0,0,0,4,a,11,13*0,1f,0,0,0
  //   ,8,4,2,9*0,e,1,f,11,f,0,0,0,10,10,16,19,11,11,1e,5*0,e,10,10,11
  //   ,e,0,0,0,1,1,d,13,11,11,f,5*0,e,11,1f,10,e,0,0,0,6,9,8,1c,8,8,8
  //   ,4*0,f,11,11,f,1,e,0,0,0,10,10,16,19,11,11,11,0,0,0,4,0,c,4,4,4
  //   ,e,0,0,0,2,0,6,2,2,12,c,0,0,0,10,10,12,14,18,14,12,0,0,0,c,5*4
  //   ,e,5*0,1a,15,15,11,11,5*0,16,19,11,11,11,5*0,e,11,11,11,e,5*0
  //   ,1e,11,1e,10,10,5*0,d,13,f,1,1,5*0,16,19,10,10,10,5*0,e,10,e,1
  //   ,1e,0,0,0,8,8,1c,8,8,9,6,5*0,11,11,11,13,d,5*0,11,11,11,a,4,5*0
  //   ,11,15,15,15,a,5*0,11,a,4,a,11,5*0,11,11,f,1,e,5*0,1f,2,4,8,1f
  //   ,0,0,0,2,4,4,8,4,4,2,0,0,0,7*4,0,0,0,8,4,4,2,4,4,8,4*0,4,2,1f
  //   ,2,4,5*0,4,8,1f,8,4,338*0,1c,14,1c,0,0,0,7,4,4,4,9*0,4,4,4,1c
  //   ,7*0,10,8,4,6*0,c,c,6*0,1f,1,1f,1,2,4,5*0,1f,1,6,4,8,5*0,2,4,c
  //   ,14,4,5*0,4,1f,11,1,6,5*0,1f,4,4,4,1f,5*0,2,1f,6,a,12,5*0,8,1f
  //   ,9,a,8,6*0,e,2,2,1f,5*0,1e,2,1e,2,1e,6*0,15,15,1,6,6*0,1f,6*0
  //   ,1f,1,5,6,4,4,8,0,0,0,1,2,4,c,14,4,4,0,0,0,4,1f,11,11,1,2,4,4*0
  //   ,1f,4*4,1f,0,0,0,2,1f,2,6,a,12,2,0,0,0,8,1f,4*9,12,0,0,0,4,1f
  //   ,4,1f,4,4,4,4*0,f,9,11,1,2,c,0,0,0,8,f,12,2,2,2,4,4*0,1f,4*1,1f
  //   ,0,0,0,a,1f,a,a,2,4,8,4*0,18,1,19,1,2,1c,4*0,1f,1,2,4,a,11,0,0,0
  //   ,8,1f,9,a,8,8,7,4*0,11,11,9,1,2,c,4*0,f,9,15,3,2,c,0,0,0,2,1c
  //   ,4,1f,4,4,8,4*0,15,15,15,1,2,4,0,0,0,e,0,1f,4,4,4,8,0,0,0,8,8,8
  //   ,c,a,8,8,0,0,0,4,4,1f,4,4,8,10,4*0,e,4*0,1f,4*0,1f,1,a,4,a,10
  //   ,0,0,0,4,1f,2,4,e,15,4,0,0,0,5*2,4,8,4*0,4,2,4*11,0,0,0,10,10
  //   ,1f,10,10,10,f,4*0,1f,1,1,1,2,c
endmodule

/* Test case init_4:
CLK E RW RS DB   State CmdReadState BitMode Cmd  AC
0   C 0  0  0x30 1     0            0       X    X
0   C 0  0  0x20 1     1            1       X    X
0   C 0  0  0x80 2     0            1       X    X
0   C 0  0  0x20 2     1            1       X    X
0   C 0  0  0x80 3     0            1       X    X
0   C 0  0  0x80 3     1            1       X    X
0   C 0  0  0x10 4     0            1       0x81 X
C   0 0  0  0x10 3     0            1       0x00 1
*/

/* Test case init_8:
CLK E RW RS DB   State CmdReadState BitMode Cmd   AC
0   C 0  0  0x38 1     0            0       0x0   X
0   C 0  0  0x38 3     0            2       0x0   X
0   C 0  0  0x81 4     0            2       0x81  X
C   0 0  0  0x81 3     0            2       0x00  1
*/

/* Test case readbusy:
CLK E RW RS DB DB_out
0   0 0  0  Z  Z
0   1 1  0  Z  0x00
*/
