// Digital circuit SST39SF040.dig as structural Verilog
module SST39SF040 (
  input  CE,
  input  OE,
  input  WE,
  input  [18:0] A,
  input  [7:0] DQ
);

  wire and_1_out, and_2_out, and_5_out, and_6_out, comparator_1_eq, comparator_2_eq, comparator_3_eq,
       comparator_4_eq, comparator_5_eq, comparator_6_eq, comparator_7_eq, decoder_1_out_0, decoder_1_out_1,
       nor_1_out, not_1_out, not_2_out, or_1_out, or_2_out, ramdualport_1_d;
  wire [2:0] driver_1_out, STATE_2_q;
  wire [7:0] multiplexer_1_out, ROM_d;

  Comparator #(.Bits(19)) comparator_1 (.a(A), .b(19'h5555), .eq(comparator_1_eq));  // open: gt, lt
  Comparator #(.Bits(8)) comparator_2 (.a(DQ), .b(8'haa), .eq(comparator_2_eq));  // open: gt, lt
  Comparator #(.Bits(19)) comparator_3 (.a(A), .b(19'h2aaa), .eq(comparator_3_eq));  // open: gt, lt
  Comparator #(.Bits(8)) comparator_4 (.a(DQ), .b(8'h55), .eq(comparator_4_eq));  // open: gt, lt
  Comparator #(.Bits(19)) comparator_5 (.a(A), .b(19'h5555), .eq(comparator_5_eq));  // open: gt, lt
  Comparator #(.Bits(8)) comparator_6 (.a(DQ), .b(8'ha0), .eq(comparator_6_eq));  // open: gt, lt
  Comparator #(.Bits(8)) comparator_7 (.a(DQ), .b(8'h80), .eq(comparator_7_eq));  // open: gt, lt
  Comparator #(.Bits(8)) comparator_8 (.a(DQ), .b(8'h30));  // open: gt, eq, lt
  and and_1 (and_1_out, comparator_1_eq, comparator_2_eq);
  and and_2 (and_2_out, comparator_3_eq, comparator_4_eq);
  // And and_3 has open pins: In_1=comparator_5_eq, In_2=comparator_6_eq, out=open
  // And and_4 has open pins: In_1=comparator_5_eq, In_2=comparator_7_eq, out=open
  // Probe STATE on STATE_2_q
  Decoder #(.Selector_Bits(3)) decoder_1 (
    .sel(STATE_2_q), .out_0(decoder_1_out_0), .out_1(decoder_1_out_1));  // open: out_2, out_3, out_4, out_5, out_6, out_7
  or or_1 (or_1_out, CE, WE);
  and and_5 (and_5_out, decoder_1_out_0, and_1_out);
  and and_6 (and_6_out, decoder_1_out_1, and_2_out);
  not not_1 (not_1_out, CE);
  not not_2 (not_2_out, or_1_out);
  Register #(.Bits(3)) STATE_2 (.D(driver_1_out), .C(not_2_out), .en(1'b1), .Q(STATE_2_q));
  or or_2 (or_2_out, OE, CE);
  ROM #(.AddrBits(19), .isProgramMemory("true"), .Bits(8)) ROM (.A(A), .sel(not_1_out), .D(ROM_d));
  RAMSinglePortSel #(.AddrBits(19), .Bits(8)) ramsingleportsel_1 (.A(A), .CS(1'b0), .WE(1'b0), .OE(1'b0), .D(DQ));
  RAMDualPort #(.AddrBits(19)) ramdualport_1 (.A(A), .Din(1'b1), .str(1'b1), .C(1'b0), .ld(1'b1), .D(ramdualport_1_d));
  nor nor_1 (nor_1_out, and_6_out, and_5_out);
  assign driver_1_out = and_5_out ? 3'b001 : 3'bz;  // Driver driver_1
  assign driver_1_out = and_6_out ? 3'b010 : 3'bz;  // Driver driver_2
  Multiplexer #(.Bits(8)) multiplexer_1 (.sel(ramdualport_1_d), .in_0(ROM_d), .in_1(DQ), .out(multiplexer_1_out));
  assign driver_1_out = nor_1_out ? 3'b000 : 3'bz;  // Driver driver_3
  assign DQ = ~or_2_out ? multiplexer_1_out : 8'bz;  // DriverInvSel driverinvsel_1

  // Notes on the sheet:
  //   CE: default 1
  //   OE: default 1
  //   WE: default 1
  //   A: default 21845
  //   DQ: default 170
  //   https://ww1.microchip.com/downloads/en/DeviceDoc/20005022C.pdf
  //   ROM loads rom.hex
endmodule

/* Test case write:
CE_ OE_ WE_ A        DQ   STATE
0   1   1   0x00000  0x00 X
0   1   0   0x00000  0x00 0
0   1   1   0x05555  0xAA 0
0   1   0   0x05555  0xAA 1
*/

/* Test case read:
CE_ OE_ DQ DQ_out
1   X   Z  Z
X   1   Z  Z
*/
