// Digital circuit io.dig as structural Verilog
module io (
  input  [2:0] SEL,
  input  OE_IN,
  input  CP_IN,
  input  RTR_OE,
  input  [7:0] RTR,
  input  [7:0] DATA,
  input  RTW_OE,
  input  [7:0] RTW,
  output RTR_ANY,
  output [7:0] CP_OUT,
  output [7:0] OE_OUT
);

  wire _7432_1_pin3, _7432_1_pin6, _7432_1_pin8, _7432_2_pin3, _7432_2_pin6, _7432_2_pin8;

  _74238 _74238_1 (
    .pin1(SEL[0]), .pin2(SEL[1]), .pin3(SEL[2]), .pin4(1'b0), .pin5(1'b0), .pin6(CP_IN), .pin7(CP_OUT[7]),
    .pin8(1'b0), .pin9(CP_OUT[6]), .pin10(CP_OUT[5]), .pin11(CP_OUT[4]), .pin12(CP_OUT[3]),
    .pin13(CP_OUT[2]), .pin14(CP_OUT[1]), .pin15(CP_OUT[0]), .pin16(1'b1));
  _74138 _74138_1 (
    .pin1(SEL[0]), .pin2(SEL[1]), .pin3(SEL[2]), .pin4(OE_IN), .pin5(1'b0), .pin6(1'b1), .pin7(OE_OUT[7]),
    .pin8(1'b0), .pin9(OE_OUT[6]), .pin10(OE_OUT[5]), .pin11(OE_OUT[4]), .pin12(OE_OUT[3]),
    .pin13(OE_OUT[2]), .pin14(OE_OUT[1]), .pin15(OE_OUT[0]), .pin16(1'b1));
  _74541 _74541_1 (
    .pin1(RTW_OE), .pin2(RTW[0]), .pin3(RTW[1]), .pin4(RTW[2]), .pin5(RTW[3]), .pin6(RTW[4]), .pin7(RTW[5]),
    .pin8(RTW[6]), .pin9(RTW[7]), .pin10(1'b0), .pin11(DATA[7]), .pin12(DATA[6]), .pin13(DATA[5]),
    .pin14(DATA[4]), .pin15(DATA[3]), .pin16(DATA[2]), .pin17(DATA[1]), .pin18(DATA[0]), .pin19(1'b0),
    .pin20(1'b1));
  _74541 _74541_2 (
    .pin1(RTR_OE), .pin2(RTR[0]), .pin3(RTR[1]), .pin4(RTR[2]), .pin5(RTR[3]), .pin6(RTR[4]), .pin7(RTR[5]),
    .pin8(RTR[6]), .pin9(RTR[7]), .pin10(1'b0), .pin11(DATA[7]), .pin12(DATA[6]), .pin13(DATA[5]),
    .pin14(DATA[4]), .pin15(DATA[3]), .pin16(DATA[2]), .pin17(DATA[1]), .pin18(DATA[0]), .pin19(1'b0),
    .pin20(1'b1));
  _7432 _7432_1 (
    .pin1(RTR[0]), .pin2(RTR[1]), .pin3(_7432_1_pin3), .pin4(RTR[2]), .pin5(RTR[3]), .pin6(_7432_1_pin6),
    .pin7(1'b0), .pin8(_7432_1_pin8), .pin9(_7432_1_pin6), .pin10(_7432_1_pin3), .pin12(1'b1), .pin13(1'b1),
    .pin14(1'b1));  // open: pin11
  _7432 _7432_2 (
    .pin1(RTR[4]), .pin2(RTR[5]), .pin3(_7432_2_pin3), .pin4(RTR[6]), .pin5(RTR[7]), .pin6(_7432_2_pin6),
    .pin7(1'b0), .pin8(_7432_2_pin8), .pin9(_7432_2_pin6), .pin10(_7432_2_pin3), .pin11(RTR_ANY),
    .pin12(_7432_2_pin8), .pin13(_7432_1_pin8), .pin14(1'b1));

  // Notes on the sheet:
  //   OE_IN: default 1
  //   RTR_OE: default 1
  //   RTW_OE: default 1
endmodule

/* Test case io:
OE_IN DATA_out
1      Z
*/
