// Digital circuit lutcomp.dig as structural Verilog
module lutcomp (
  input  RESET,
  input  clk,
  output HALT
);

  wire and_1_out, and_3_out, and_5_out, bussplitter_1_d0, bussplitter_1_d1, bussplitter_1_d2,
       bussplitter_1_d3, bussplitter_1_d7, CLK_t, CLK_t_t, counter_1_ovf, decoder_1_out_0, decoder_1_out_1,
       decoder_1_out_2, decoder_1_out_3, decoder_1_out_4, decoder_1_out_5, decoder_1_out_6, decoder_1_out_7,
       io_1_rtr_any, not_1_out, not_3_out, not_4_out, not_5_out, not_6_out, not_7_out, not_8_out, or_1_out,
       ps2_encoder_1_ack, PS2_Keyboard_av, switch_1_b, uc_1_a0_cp, uc_1_a0_oe, uc_1_a1_cp, uc_1_a1_oe,
       uc_1_a2_cp, uc_1_a2_oe, uc_1_addr_oe, uc_1_alu_cp, uc_1_alu_oe, uc_1_in1_cp, uc_1_io_rtw_oe,
       uc_1_iox_cp, uc_1_iox_data_oe, uc_1_iox_rtr_oe, uc_1_mem_oe, uc_1_mem_we, uc_1_pc_inc, uc_1_pc_spe,
       uc_1_w_cp, uc_1_w_oe, uc_1_x_cp, uc_1_x_oe, uc_1_y_cp, uc_1_y_oe, uc_1_z_cp, uc_1_z_oe, undriven,
       undriven_2, undriven_3, undriven_4, undriven_5, undriven_6, undriven_8, undriven_9;
  wire [1:0] uc_1_stage;
  wire [2:0] bussplitter_1_d4, TTYIN_av, uc_1_alu_op, uc_1_io_sel;
  wire [3:0] bussplitter_2_d0, uc_1_uaddr_3;
  wire [6:0] uc_1_uaddr;
  wire [7:0] bussplitter_2_d, counter_4_out, io_1_cp_out, io_1_oe_out, ps2_decoder_1_data_peek, rom_1_d,
       uc_1_data, uc_1_ir0, uc_1_uaddr_2, uc_1_uir0, uc_1_uir1, uc_1_upc;
  wire [9:0] counter_1_out;
  wire [15:0] counter_3_out, TTYIN_d, uc_1_udata;
  wire [15:7] PS2_Keyboard_d;
  wire [23:0] pc_1_pc, undriven_7;
  wire [63:0] counter_2_out;

  Keyboard PS2_Keyboard (.C(counter_1_ovf), .en(1'b1), .D({PS2_Keyboard_d, counter_1_out[9:3]}), .av(PS2_Keyboard_av));
  Counter #(.Bits(3)) counter_1 (
    .en(PS2_Keyboard_av), .C(ps2_encoder_1_ack), .clr(1'b0), .out(counter_1_out[2:0]), .ovf(counter_1_ovf));
  ROM #(.AddrBits(10), .Bits(8)) rom_1 (.A(counter_1_out), .sel(1'b1), .D(rom_1_d));
  and and_1 (and_1_out, CLK_t, PS2_Keyboard_av);
  and and_2 (CLK_t, clk, HALT);
  Stop stop_1 (.stop(~HALT));
  not not_1 (not_1_out, HALT);
  ps2_encoder ps2_encoder_1 (
    .CLK(and_1_out), .DATA(rom_1_d), .PS2_CLK(undriven_9), .PS2_DATA(undriven_8), .ACK(ps2_encoder_1_ack));
  Break #(.Cycles(1000000000)) break_1 (.brk(not_1_out));
  Break #(.Cycles(1000000000)) break_2 (.brk(undriven_9));
  Break #(.Cycles(1000000000)) break_3 (.brk(undriven_8));
  not not_2 (CLK_t_t, CLK_t);
  // Probe TickCount on counter_2_out
  Counter #(.Bits(64)) counter_2 (.en(1'b1), .C(CLK_t), .clr(1'b0), .out(counter_2_out));  // open: ovf
  ps2_decoder ps2_decoder_1 (
    .PS2_CP(io_1_oe_out[2]), .DATA(uc_1_data), .PS2_OE(io_1_oe_out[2]), .PS2_CLK(undriven_9),
    .PS2_DATA(undriven_8), .CLK(1'b0), .PS2_READY(TTYIN_av[2]), .DATA_PEEK(ps2_decoder_1_data_peek));
  not not_3 (not_3_out, io_1_oe_out[2]);
  Break #(.Cycles(1000000000)) break_4 (.brk(not_3_out));
  uc uc_1 (
    .CLK(CLK_t_t), .RESET(RESET), .INT_PENDING(io_1_rtr_any), .DATA(uc_1_data), .ADDR_OE(uc_1_addr_oe),
    .ALU_OP(uc_1_alu_op), .PC_INC(uc_1_pc_inc), .IN1_CP(uc_1_in1_cp), .ALU_CP(uc_1_alu_cp),
    .MEM_WE(uc_1_mem_we), .W_CP(uc_1_w_cp), .X_CP(uc_1_x_cp), .Y_CP(uc_1_y_cp), .Z_CP(uc_1_z_cp),
    .A0_CP(uc_1_a0_cp), .A1_CP(uc_1_a1_cp), .A2_CP(uc_1_a2_cp), .HALT(HALT), .ALU_OE(uc_1_alu_oe),
    .MEM_OE(uc_1_mem_oe), .IO_RTW_OE(uc_1_io_rtw_oe), .PC_SPE(uc_1_pc_spe), .W_OE(uc_1_w_oe),
    .X_OE(uc_1_x_oe), .Y_OE(uc_1_y_oe), .Z_OE(uc_1_z_oe), .uIR0(uc_1_uir0), .uIR1(uc_1_uir1),
    .uAddr({uc_1_uaddr_3, uc_1_uaddr_2, uc_1_uaddr}), .uPC(uc_1_upc), .stage(uc_1_stage), .uData(uc_1_udata),
    .IOX_CP(uc_1_iox_cp), .IOX_RTR_OE(uc_1_iox_rtr_oe), .A0_OE(uc_1_a0_oe), .A1_OE(uc_1_a1_oe),
    .A2_OE(uc_1_a2_oe), .IO_SEL(uc_1_io_sel), .IOX_DATA_OE(uc_1_iox_data_oe), .IR0(uc_1_ir0));  // open: IR0_CP, UNUSED_F
  // Probe on ps2_decoder_1_data_peek
  Break #(.Cycles(1000000000)) break_5 (.brk(TTYIN_av[2]));
  not not_4 (not_4_out, uc_1_addr_oe);
  // Probe on uc_1_uir0
  // Probe on uc_1_uir1
  // Probe on uc_1_upc
  // Probe on uc_1_stage
  // Probe on uc_1_udata
  // Probe on uc_1_ir0
  PullDown #(.Bits(8)) pulldown_1 (.out(uc_1_data));
  and and_3 (and_3_out, uc_1_pc_inc, ~uc_1_pc_spe);  // And
  Switch switch_1 (.A(uc_1_pc_inc), .B(switch_1_b));
  pc pc_1 (.PC_INC(uc_1_pc_inc), .RESET(RESET), .PC_SPE(uc_1_pc_spe), .OE(not_4_out), .ADDR(undriven_7), .PC(pc_1_pc));
  Counter #(.Bits(16)) counter_3 (.en(1'b1), .C(uc_1_pc_inc), .clr(1'b0), .out(counter_3_out));  // open: ovf
  Break #(.Cycles(10000000)) break_6 (.brk(switch_1_b));
  PullDown pulldown_2 (.out(switch_1_b));
  // Probe $uPC on {uc_1_uaddr_3, uc_1_uaddr_2, uc_1_uaddr}
  // Probe on uc_1_uaddr
  // Probe $IR0 on uc_1_uaddr_2
  // Probe $FLAGS on uc_1_uaddr_3
  io io_1 (
    .SEL(uc_1_io_sel), .OE_IN(uc_1_iox_data_oe), .CP_IN(uc_1_iox_cp), .RTR_OE(uc_1_iox_rtr_oe),
    .RTR({{5{1'b0}}, TTYIN_av[2], 1'b0, TTYIN_av[0]}), .DATA(uc_1_data), .RTW_OE(uc_1_io_rtw_oe), .RTW(8'h1),
    .RTR_ANY(io_1_rtr_any), .CP_OUT(io_1_cp_out), .OE_OUT(io_1_oe_out));
  Counter #(.Bits(8)) counter_4 (.en(1'b1), .C(and_3_out), .clr(1'b0), .out(counter_4_out));  // open: ovf
  // Probe PC on pc_1_pc
  RAMDualPort #(.AddrBits(16), .Bits(24)) PC_LOG (
    .A(counter_3_out), .Din(pc_1_pc), .str(1'b1), .C(uc_1_pc_inc), .ld(1'b0));  // open: D
  RAMDualPort #(.AddrBits(8), .Bits(24)) JMP_LOG (
    .A(counter_4_out), .Din(pc_1_pc), .str(1'b1), .C(and_3_out), .ld(1'b0));  // open: D
  memory memory_1 (
    .MEM_WE(uc_1_mem_we), .ADDR_OE(uc_1_addr_oe), .A0_CP(uc_1_a0_cp), .A1_CP(uc_1_a1_cp), .A2_CP(uc_1_a2_cp),
    .MEM_OE(uc_1_mem_oe), .DATA(uc_1_data), .ADDR(undriven_7), .A0_OE(uc_1_a0_oe), .A1_OE(uc_1_a1_oe),
    .A2_OE(uc_1_a2_oe));
  // Probe ADDR on undriven_7
  // Probe DATA on uc_1_data
  Break #(.Cycles(1000000000)) break_7 (.brk(io_1_cp_out[1]));
  not not_5 (not_5_out, io_1_cp_out[1]);
  Break #(.Cycles(1000000000)) break_8 (.brk(not_5_out));
  BusSplitter #(.Bits(8)) bussplitter_1 (
    .D(uc_1_data), .OE(io_1_oe_out[1]), .D0(bussplitter_1_d0), .D1(bussplitter_1_d1), .D2(bussplitter_1_d2),
    .D3(bussplitter_1_d3), .D4(bussplitter_1_d4[0]), .D5(bussplitter_1_d4[1]), .D6(bussplitter_1_d4[2]),
    .D7(bussplitter_1_d7));
  Decoder #(.Selector_Bits(3)) decoder_1 (
    .sel(uc_1_alu_op), .out_0(decoder_1_out_0), .out_1(decoder_1_out_1), .out_2(decoder_1_out_2),
    .out_3(decoder_1_out_3), .out_4(decoder_1_out_4), .out_5(decoder_1_out_5), .out_6(decoder_1_out_6),
    .out_7(decoder_1_out_7));
  alu alu_1 (
    .ALU_OP(uc_1_alu_op), .ALU_OE(uc_1_alu_oe), .ALU_CP(uc_1_alu_cp), .IN1_CP(uc_1_in1_cp), .DATA(uc_1_data));  // open: IN1, ALU_REG, ALU_RESULT
  \reg  W (.OE(uc_1_w_oe), .CP(uc_1_w_cp), .IO(uc_1_data));
  \reg  X (.OE(uc_1_x_oe), .CP(uc_1_x_cp), .IO(uc_1_data));
  \reg  Y (.OE(uc_1_y_oe), .CP(uc_1_y_cp), .IO(uc_1_data));
  \reg  Z (.OE(uc_1_z_oe), .CP(uc_1_z_cp), .IO(uc_1_data));
  Keyboard TTYIN (.C(io_1_oe_out[0]), .en(1'b1), .D(TTYIN_d), .av(TTYIN_av[0]));
  or or_1 (or_1_out, not_6_out, io_1_cp_out[1]);
  not not_6 (not_6_out, io_1_oe_out[1]);
  // NotConnected on bussplitter_1_d4
  // Probe AddLo on decoder_1_out_0
  // Probe AddHiNC on decoder_1_out_2
  // Probe Or on decoder_1_out_4
  // Probe And on decoder_1_out_6
  Break #(.Cycles(1000000000)) break_9 (.brk(not_6_out));
  BusSplitter #(.Bits(8)) bussplitter_2 (
    .D(bussplitter_2_d), .OE(not_6_out), .D0(bussplitter_2_d0[0]), .D1(bussplitter_2_d0[1]),
    .D2(bussplitter_2_d0[2]), .D3(bussplitter_2_d0[3]), .D4(bussplitter_1_d0), .D5(bussplitter_1_d1),
    .D6(bussplitter_1_d2), .D7(bussplitter_1_d3));
  // NotConnected on bussplitter_2_d0
  and and_5 (and_5_out, io_1_oe_out[1], bussplitter_1_d7);
  assign uc_1_data = ~io_1_oe_out[0] ? TTYIN_d[7:0] : 8'bz;  // DriverInvSel driverinvsel_1
  // Probe MulHi on decoder_1_out_1
  // Probe AddHiC on decoder_1_out_3
  // Probe Div on decoder_1_out_5
  // Probe Special on decoder_1_out_7
  Terminal TTYOUT (.D(uc_1_data), .C(io_1_cp_out[0]), .en(1'b1));
  Break #(.Cycles(1000000000)) break_10 (.brk(or_1_out));
  not not_7 (not_7_out, or_1_out);
  Break #(.Cycles(1000000000)) break_11 (.brk(not_7_out));
  HD44780U hd44780u_1 (.DB(bussplitter_2_d), .E(or_1_out), .RW(not_6_out), .RS(and_5_out), .clk(CLK_t));  // open: CLK_2
  not not_8 (not_8_out, undriven_3);
  // Probe on undriven
  // Probe on undriven_2
  // Probe on undriven_3
  // Probe on undriven_6
  // Probe on undriven_4
  // Probe on undriven_5
  Break #(.Cycles(1000000000)) break_12 (.brk(not_8_out));
  Break #(.Cycles(1000000000)) break_13 (.brk(undriven_6));

  // Notes on the sheet:
  //   RESET: default 1
  //   clk: Hz: 100000
  //   PS2 Keyboard
  //   rom_1 loads ascii_to_ps2.hex
  //   4A
  //   4B
  //   4Y
  //   6A
  //   6Y
  //   3A
  //   3Y
  //   TTY
endmodule

/* Test case:
RESET_ HALT_
0      1
*/
