// Digital circuit memory.dig as structural Verilog
module memory (
  input  MEM_CP,
  input  ADDR_OE,
  input  A0_CP,
  input  A1_CP,
  input  A2_CP,
  input  MEM_OE,
  input  [7:0] DATA,
  input  [23:0] ADDR,
  input  A0_OE,
  input  A1_OE,
  input  A2_OE
);

  wire not_1_out, not_2_out, not_3_out, or_1_out;
  wire [7:0] ROM_d;

  // _74574 ADDR0: pin names not known; wires that end beside it: ADDR_OE, 1'b1
  // _74574 ADDR1: pin names not known; wires that end beside it: 1'b0, ADDR_OE, A0_CP, 1'b1
  // _74574 ADDR2: pin names not known; wires that end beside it: 1'b0, ADDR_OE, 1'b0, A1_CP, 1'b1, A2_CP
  not not_1 (not_1_out, MEM_CP);
  not not_2 (not_2_out, ADDR[19]);
  not not_3 (not_3_out, ADDR[19]);
  ram RAM (.CE(not_2_out), .OE(MEM_OE), .WE(not_1_out), .A(ADDR[18:0]), .D(DATA));
  or or_1 (or_1_out, MEM_OE, ADDR[19]);
  ROM #(.AddrBits(19), .isProgramMemory("true"), .Bits(8)) ROM (.A(ADDR[18:0]), .sel(not_3_out), .D(ROM_d));
  assign DATA = ~or_1_out ? ROM_d : 8'bz;  // DriverInvSel driverinvsel_1
  // _74541 _74541_1: pin names not known; wires that end beside it: A0_OE, 1'b1, 1'b0
  // _74541 _74541_2: pin names not known; wires that end beside it: 1'b0, A1_OE, 1'b1, 1'b0
  // _74541 _74541_3: pin names not known; wires that end beside it: 1'b0, A2_OE, 1'b0, 1'b1, 1'b0

  // Notes on the sheet:
  //   A0_OE: default 1
  //   A1_OE: default 1
  //   A2_OE: default 1
  //   5A
  //   5Y
  //   6A
  //   6Y
  //   ROM
  //   ROM loads rom.hex
endmodule

/* Test case mem-A*:
ADDR_out ADDR_OE_ MEM_OE_ DATA  A0_CP A1_CP A2_CP MEM_CP DATA_out
Z        1        1       0x00  C     0     0     0      0x00
Z        1        1       0x00  0     C     0     0      0x00
Z        1        1       0x00  0     0     C     0      0x00
0x0      0        0       Z     0     0     0     0      0x00
Z        1        1       0x08  0     0     C     0      0x08
0x80000  0        1       0xAA  0     0     0     C      0xAA
Z        1        1       0x02  C     0     0     0      0x02
0x80002  0        1       0xBB  0     0     0     C      0xBB
Z        1        1       0x00  C     0     0     0      0x00
0x80000  0        0       Z     0     0     0     0      0xAA
Z        1        1       0x02  C     0     0     0      0x02
0x80002  0        0       Z     0     0     0     0      0xBB
*/

/* Test case mem-ADDR:
ADDR     ADDR_OE_ MEM_OE_ DATA  MEM_CP ADDR_out DATA_out
0x80007  1        1       0xAB  C      0x80007  0xAB
0x90001  1        1       0x34  C      0x90001  0x34
0x80007  1        0       Z     0      0x80007  0xAB
0x90001  1        0       Z     0      0x90001  0x34
*/
