// Digital circuit ps2.dig as structural Verilog
module ps2 (
  input  CLK,
  input  TTYIN_CP,
  input  [7:0] DATA,
  input  TTYIN_OE
);

  wire _74299_1_pin18, AND_pin1, AND_pin2, AND_pin4, AND_pin5, AND_pin8, AND_pin12, AND_pin13, NOT_pin2,
       NOT_pin4, NOT_pin5, NOT_pin9, NOT_pin11, NOT_pin12, paralleltops2_1_ack, PS2_CLK, PS2_DATA;
  wire [3:0] _74161_1_pin3;
  wire [7:0] _74299_2_pin7, counter_1_out;

  Counter #(.Bits(8)) counter_1 (.en(1'b1), .C(paralleltops2_1_ack), .clr(1'b0), .out(counter_1_out));  // open: ovf
  ParallelToPS2 paralleltops2_1 (
    .CLK(CLK), .DATA(counter_1_out), .PS2_CLK(PS2_CLK), .PS2_DATA(PS2_DATA), .ACK(paralleltops2_1_ack));
  // Probe PS2_CLK on PS2_CLK
  // Probe PS2_DATA on PS2_DATA
  PullUp pullup_1 (.out(PS2_CLK));
  assign PS2_CLK = NOT_pin5 ? 1'b0 : 1'bz;  // Driver driver_1
  _7414 NOT (
    .pin1(TTYIN_CP), .pin2(NOT_pin2), .pin3(PS2_CLK), .pin4(NOT_pin4), .pin5(NOT_pin5), .pin7(1'b0),
    .pin9(NOT_pin9), .pin11(NOT_pin11), .pin12(NOT_pin12), .pin13(NOT_pin5), .pin14(1'b1));  // open: pin6, pin8, pin10
  _7408 AND (
    .pin1(AND_pin1), .pin2(AND_pin2), .pin4(AND_pin4), .pin5(AND_pin5), .pin7(1'b0), .pin8(AND_pin8),
    .pin9(NOT_pin4), .pin10(NOT_pin2), .pin12(AND_pin12), .pin13(AND_pin13), .pin14(1'b1));  // open: pin3, pin6, pin11
  // NotConnected on AND_pin1
  // NotConnected on AND_pin2
  // NotConnected on AND_pin4
  // NotConnected on AND_pin5
  // NotConnected on NOT_pin11
  // NotConnected on NOT_pin9
  // NotConnected on AND_pin13
  // NotConnected on AND_pin12
  PullUp pullup_2 (.out(PS2_DATA));
  _74161 _74161_1 (
    .pin1(1'b1), .pin2(AND_pin8), .pin3(_74161_1_pin3[0]), .pin4(_74161_1_pin3[1]), .pin5(_74161_1_pin3[2]),
    .pin6(_74161_1_pin3[3]), .pin7(1'b1), .pin8(1'b0), .pin9(NOT_pin12), .pin10(1'b1), .pin15(NOT_pin5),
    .pin16(1'b1));  // open: pin11, pin12, pin13, pin14
  // Probe PS2_ROF on NOT_pin5
  _74299 _74299_1 (
    .pin1(1'b0), .pin2(1'b0), .pin3(1'b0), .pin4(_74299_2_pin7[0]), .pin9(NOT_pin2), .pin10(1'b0),
    .pin11(1'b1), .pin12(NOT_pin4), .pin16(_74299_2_pin7[1]), .pin18(_74299_1_pin18), .pin19(1'b1),
    .pin20(1'b1));  // open: pin5, pin6, pin7, pin8, pin13, pin14, pin15, pin17
  _74299 _74299_2 (
    .pin1(1'b0), .pin2(1'b0), .pin3(1'b0), .pin5(_74299_2_pin7[6]), .pin6(_74299_2_pin7[4]),
    .pin7(_74299_2_pin7[2]), .pin8(_74299_1_pin18), .pin9(NOT_pin2), .pin10(1'b0), .pin11(1'b1),
    .pin12(NOT_pin4), .pin13(_74299_2_pin7[3]), .pin14(_74299_2_pin7[5]), .pin16(_74299_2_pin7[7]),
    .pin18(PS2_DATA), .pin19(1'b1), .pin20(1'b1));  // open: pin4, pin15, pin17
  // Probe PS2_READY on NOT_pin5
  // _74541 _74541_1: pin names not known; wires that end beside it: 1'b0, 1'b0, 1'b1, TTYIN_OE
  // also tied to GND on the sheet: {_74161_1_pin3[0], _74161_1_pin3[1], _74161_1_pin3[3]}
  // also tied to VCC on the sheet: _74161_1_pin3[2]

  // Notes on the sheet:
  //   TTYIN_OE: default 1
  //   NPN C
  //   NPN E
  //   NPN B
  //   100K
  //   R 2K
endmodule

/* Test case e2e:
            CLK PS2_CLK TTYIN_CP PS2_READY TTYIN_OE_ DATA_out
            C   1       0        0         1         Z
repeat(100) C   X       0        X         1         Z
repeat(100) C   0       0        1         1         Z
repeat(100) C   0       0        1         1         Z
loop(a,300)
            C   1       C        0         1         Z
            C   1       0        0         1         Z
repeat(40)  C   X       0        X         1         Z
repeat(40)  C   0       0        1         0         (0x80|(a+2))
end loop
*/
