// Digital circuit ps2_decoder.dig as structural Verilog
module ps2_decoder (
  input  PS2_CP,
  input  [7:0] DATA,
  input  PS2_OE,
  input  PS2_CLK,
  input  PS2_DATA,
  input  CLK,
  output PS2_READY,
  output [7:0] DATA_PEEK
);

  wire _74299_1_pin18, AND_pin1, AND_pin2, AND_pin4, AND_pin5, AND_pin8, AND_pin12, AND_pin13, NOT_pin1,
       NOT_pin4, NOT_pin9, NOT_pin11, NOT_pin12;
  wire [3:0] _74161_1_pin3, _74161_1_pin14;

  PullUp pullup_1 (.out(PS2_DATA));
  assign PS2_CLK = CLK ? 1'b0 : 1'bz;  // Driver driver_1
  PullUp pullup_2 (.out(PS2_CLK));
  assign PS2_CLK = PS2_READY ? 1'b0 : 1'bz;  // Driver driver_2
  _7414 NOT (
    .pin1(NOT_pin1), .pin3(PS2_CLK), .pin4(NOT_pin4), .pin5(PS2_READY), .pin7(1'b0), .pin9(NOT_pin9),
    .pin11(NOT_pin11), .pin12(NOT_pin12), .pin13(PS2_READY), .pin14(1'b1));  // open: pin2, pin6, pin8, pin10
  // NotConnected on NOT_pin1
  _7408 AND (
    .pin1(AND_pin1), .pin2(AND_pin2), .pin4(AND_pin4), .pin5(AND_pin5), .pin7(1'b0), .pin8(AND_pin8),
    .pin9(NOT_pin4), .pin10(PS2_CP), .pin12(AND_pin12), .pin13(AND_pin13), .pin14(1'b1));  // open: pin3, pin6, pin11
  // NotConnected on AND_pin1
  // NotConnected on AND_pin2
  // NotConnected on AND_pin4
  // NotConnected on AND_pin5
  // NotConnected on NOT_pin11
  // NotConnected on NOT_pin9
  // NotConnected on AND_pin13
  // NotConnected on AND_pin12
  _74161 _74161_1 (
    .pin1(1'b1), .pin2(AND_pin8), .pin3(_74161_1_pin3[0]), .pin4(_74161_1_pin3[1]), .pin5(_74161_1_pin3[2]),
    .pin6(_74161_1_pin3[3]), .pin7(1'b1), .pin8(1'b0), .pin9(NOT_pin12), .pin10(1'b1),
    .pin11(_74161_1_pin14[3]), .pin12(_74161_1_pin14[2]), .pin13(_74161_1_pin14[1]),
    .pin14(_74161_1_pin14[0]), .pin15(PS2_READY), .pin16(1'b1));
  // Probe PS2_ROF on PS2_READY
  // Probe CNT on _74161_1_pin14
  _74299 _74299_1 (
    .pin1(1'b0), .pin2(1'b0), .pin3(1'b0), .pin4(DATA_PEEK[0]), .pin9(1'b1), .pin10(1'b0), .pin11(1'b1),
    .pin12(NOT_pin4), .pin16(DATA_PEEK[1]), .pin18(_74299_1_pin18), .pin19(1'b1), .pin20(1'b1));  // open: pin5, pin6, pin7, pin8, pin13, pin14, pin15, pin17
  _74299 _74299_2 (
    .pin1(1'b0), .pin2(1'b0), .pin3(1'b0), .pin5(DATA_PEEK[6]), .pin6(DATA_PEEK[4]), .pin7(DATA_PEEK[2]),
    .pin8(_74299_1_pin18), .pin9(1'b1), .pin10(1'b0), .pin11(1'b1), .pin12(NOT_pin4), .pin13(DATA_PEEK[3]),
    .pin14(DATA_PEEK[5]), .pin15(DATA_PEEK[7]), .pin18(PS2_DATA), .pin19(1'b1), .pin20(1'b1));  // open: pin4, pin16, pin17
  // _74541 _74541_1: pin names not known; wires that end beside it: 1'b0, 1'b0, 1'b1, PS2_OE
  // also tied to GND on the sheet: {_74161_1_pin3[0], _74161_1_pin3[1], _74161_1_pin3[3]}
  // also tied to VCC on the sheet: _74161_1_pin3[2]

  // Notes on the sheet:
  //   PS2_OE: default 1
  //   FAKE
  //   REAL
  //   NPN C
  //   NPN E
  //   NPN B
  //   100K
  //   R 2K
endmodule

/* Test case OE:
PS2_OE_ DATA_out
1       Z
*/

/* Test case READ:
CLK_ PS2_DATA PS2_CP DATA_PEEK CNT PS2_READY PS2_CLK_out
loop(a,16)
C    0        1      X         X   X X
end loop
0    0        1      X         0xF 1 X

loop (a,256)
0    0        0      X         0xF 1 X
0    0        C      X         4   0 X
C    0        1      X         5   0 X
loop (b, 8)
C    ((a>>b)&0x1) 1  X         (6+b) 0 X
end loop
C    0        1      X         0xE 0 X
C    1        1      (a)       0xF 1 0
end loop
*/
