// Digital circuit ps2_encoder.dig as structural Verilog
module ps2_encoder (
  input  CLK,
  input  [7:0] DATA,
  input  PS2_CLK,
  input  PS2_DATA,
  output ACK
);

  wire and_1_out, and_2_out, and_3_out, comparator_1_eq, comparator_1_gt, counter_1_ovf, d_ff_1_q, not_2_out;
  wire [3:0] bitcount_1_out, counter_1_out;
  wire [9:9] not_1_out;
  wire [10:0] barrelshifter_1_out;

  Counter #(.Bits(4)) counter_1 (.en(1'b1), .C(CLK), .clr(1'b0), .out(counter_1_out), .ovf(counter_1_ovf));
  not not_1 (not_1_out[9], bitcount_1_out[0]);
  BitCount #(.Bits(8)) bitcount_1 (.in(DATA), .out(bitcount_1_out));
  not not_2 (not_2_out, CLK);
  D_FF d_ff_1 (.D(PS2_CLK), .C(counter_1_ovf), .Q(d_ff_1_q));  // open: nQ
  // Probe PS2_SENDBIT on counter_1_out
  Comparator #(.Bits(4)) comparator_1 (
    .a(4'b1011), .b(counter_1_out), .gt(comparator_1_gt), .eq(comparator_1_eq));  // open: lt
  BarrelShifter #(.Bits(11), .direction("right")) barrelshifter_1 (
    .in({1'b1, not_1_out[9], DATA, 1'b0}), .shift(counter_1_out), .out(barrelshifter_1_out));
  and and_1 (and_1_out, d_ff_1_q, comparator_1_eq);
  and and_2 (and_2_out, comparator_1_gt, d_ff_1_q, not_2_out);
  and and_3 (and_3_out, d_ff_1_q, ~barrelshifter_1_out[0]);  // And
  D_FF_AS d_ff_as_1 (.Set(1'b0), .D(1'b1), .C(and_1_out), .Clr(not_2_out), .Q(ACK));  // open: nQ
  assign PS2_CLK = and_2_out ? 1'b0 : 1'bz;  // Driver driver_1
  assign PS2_DATA = and_3_out ? 1'b0 : 1'bz;  // Driver driver_2
  PullUp pullup_1 (.out(PS2_CLK));
  PullUp pullup_2 (.out(PS2_DATA));
  // Probe on PS2_DATA
  // Probe on PS2_CLK

  // Notes on the sheet:
  //   CLK: Hz: 2
endmodule

/* Test case ps2_encoder:
CLK PS2_CLK_out PS2_DATA_out
0   1           1
*/
