// Digital circuit ps2_test.dig as structural Verilog
module ps2_test (
  input  CLK,
  input  TTYIN_CP,
  input  [7:0] DATA,
  input  TTYIN_OE
);

  wire ps2_decoder_1_ps2_ready, ps2_encoder_1_ack, undriven, undriven_2;
  wire [7:0] counter_1_out, ps2_decoder_1_data_peek;

  Counter #(.Bits(8)) counter_1 (.en(1'b1), .C(ps2_encoder_1_ack), .clr(1'b0), .out(counter_1_out));  // open: ovf
  // Probe PS2_CLK on undriven_2
  // Probe PS2_DATA on undriven
  // Probe SEND on counter_1_out
  ps2_encoder ps2_encoder_1 (
    .CLK(CLK), .DATA(counter_1_out), .PS2_CLK(undriven_2), .PS2_DATA(undriven), .ACK(ps2_encoder_1_ack));
  // Probe ACK on ps2_encoder_1_ack
  ps2_decoder ps2_decoder_1 (
    .PS2_CP(TTYIN_CP), .DATA(DATA), .PS2_OE(TTYIN_OE), .PS2_CLK(undriven_2), .PS2_DATA(undriven), .CLK(1'b0),
    .PS2_READY(ps2_decoder_1_ps2_ready), .DATA_PEEK(ps2_decoder_1_data_peek));
  // Probe on ps2_decoder_1_data_peek
  // Probe PS2_READY on ps2_decoder_1_ps2_ready

  // Notes on the sheet:
  //   CLK: Hz: 4
  //   TTYIN_OE: default 1
endmodule

/* Test case e2e:
            CLK PS2_CLK TTYIN_CP PS2_READY TTYIN_OE_ DATA_out
            C   1       1        0         1         Z
repeat(100) C   X       1        X         1         Z
repeat(100) C   0       1        1         1         Z
repeat(100) C   0       1        1         1         Z
loop(a,300)
            0   0       0        1         1         Z
            C   1       1        0         1         Z
repeat(40)  C   X       1        X         1         Z
repeat(40)  C   0       1        1         0         (a+2)
end loop
*/
