// Digital circuit reg.dig as structural Verilog
module \reg  (
  input  OE,
  input  CP,
  input  [7:0] IO
);

  wire _74299_1_pin4, _74299_1_pin5, _74299_1_pin6, _74299_1_pin7, _74299_1_pin13, _74299_1_pin14,
       _74299_1_pin15, _74299_1_pin16;

  _74299 _74299_1 (
    .pin1(OE), .pin2(OE), .pin3(OE), .pin4(_74299_1_pin4), .pin5(_74299_1_pin5), .pin6(_74299_1_pin6),
    .pin7(_74299_1_pin7), .pin9(1'b1), .pin10(1'b0), .pin11(1'b0), .pin12(CP), .pin13(_74299_1_pin13),
    .pin14(_74299_1_pin14), .pin15(_74299_1_pin15), .pin16(_74299_1_pin16), .pin18(1'b0), .pin19(OE),
    .pin20(1'b1));  // open: pin8, pin17
  BusSplitter #(.Bits(8)) bussplitter_1 (
    .D(IO), .OE(OE), .D0(_74299_1_pin7), .D1(_74299_1_pin13), .D2(_74299_1_pin6), .D3(_74299_1_pin14),
    .D4(_74299_1_pin5), .D5(_74299_1_pin15), .D6(_74299_1_pin4), .D7(_74299_1_pin16));
  // Probe on _74299_1_pin16

  // Notes on the sheet:
  //   OE: default 1
endmodule

/* Test case reg:
OE_ CP IO   IO_out
1   0  Z    Z
1   C  0xAB 0xAB
0   0  Z    0xAB
*/
