// Digital circuit serial_rom.dig as structural Verilog
module serial_rom (
  input  SCLK,
  input  SI,
  input  CE,
  input  HOLD,
  input  TEST,
  input  [7:0] ROM_D,
  output SO,
  output [2:0] \bit ,
  output [2:0] \byte ,
  output [19:0] ROM_ADDR
);

  wire and_1_out, and_2_out, bitselector_1_out, comparator_1_eq, comparator_2_lt, d_ff_as_1_q,
       decoder_1_out_0, decoder_1_out_1, decoder_1_out_2, decoder_1_out_3, nor_1_out, not_1_out, not_2_out,
       not_3_out;
  wire [2:0] sub_1_s;
  wire [7:0] multiplexer_1_out, shift_reg_1_q, shift_reg_2_q, shift_reg_3_q, shift_reg_4_q, TESTROM_q;
  wire [7:6] clks_out;
  wire [19:0] register_1_q;
  wire [22:0] counter_1_out;

  nor nor_1 (nor_1_out, not_1_out, CE);
  not not_1 (not_1_out, HOLD);
  PullUp pullup_1 (.out(TEST));
  and and_1 (and_1_out, nor_1_out, SCLK);
  Decoder #(.Selector_Bits(3)) decoder_1 (
    .sel(\byte ), .out_0(decoder_1_out_0), .out_1(decoder_1_out_1), .out_2(decoder_1_out_2),
    .out_3(decoder_1_out_3));  // open: out_4, out_5, out_6, out_7
  Counter #(.Bits(8)) clks (.en(1'b1), .C(and_1_out), .clr(CE), .out({clks_out, \byte , \bit }));  // open: ovf
  not not_2 (not_2_out, CE);
  Counter #(.Bits(23)) counter_1 (.en(d_ff_as_1_q), .C(not_3_out), .clr(CE), .out(counter_1_out));  // open: ovf
  // Probe on counter_1_out[22:3]
  shift_reg shift_reg_1 (
    .DS7(1'b0), .SCLK(and_1_out), .RST(not_2_out), .DS0(SI), .S1(1'b0), .S0(decoder_1_out_0),
    .Q(shift_reg_1_q));  // open: Q0, Q7
  shift_reg shift_reg_2 (
    .DS7(1'b0), .SCLK(and_1_out), .RST(not_2_out), .DS0(SI), .S1(1'b0), .S0(decoder_1_out_1),
    .Q(shift_reg_2_q));  // open: Q0, Q7
  shift_reg shift_reg_3 (
    .DS7(1'b0), .SCLK(and_1_out), .RST(not_2_out), .DS0(SI), .S1(1'b0), .S0(decoder_1_out_2),
    .Q(shift_reg_3_q));  // open: Q0, Q7
  shift_reg shift_reg_4 (
    .DS7(1'b0), .SCLK(and_1_out), .RST(not_2_out), .DS0(SI), .S1(1'b0), .S0(decoder_1_out_3),
    .Q(shift_reg_4_q));  // open: Q0, Q7
  Comparator #(.Bits(8)) comparator_1 (.a({clks_out, \byte , \bit }), .b(8'h20), .eq(comparator_1_eq));  // open: gt, lt
  Sub #(.Bits(3)) sub_1 (.a(3'b111), .b(counter_1_out[2:0]), .c_i(1'b0), .s(sub_1_s));  // open: c_o
  not not_3 (not_3_out, and_1_out);
  Comparator #(.Bits(3)) comparator_2 (.a(\byte ), .b(3'b100), .lt(comparator_2_lt));  // open: gt, eq
  // Probe opcode on shift_reg_1_q
  // Probe a2 on shift_reg_2_q
  // Probe a1 on shift_reg_3_q
  // Probe a0 on shift_reg_4_q
  and and_2 (and_2_out, comparator_1_eq, not_3_out);
  Register #(.Bits(20)) register_1 (
    .D({shift_reg_2_q[3:0], shift_reg_3_q, shift_reg_4_q[6:0], SI}), .C(and_1_out), .en(comparator_2_lt),
    .Q(register_1_q));
  Multiplexer #(.Bits(8)) multiplexer_1 (.sel(TEST), .in_0(TESTROM_q), .in_1(ROM_D), .out(multiplexer_1_out));
  D_FF_AS d_ff_as_1 (.Set(1'b0), .D(1'b1), .C(and_2_out), .Clr(CE), .Q(d_ff_as_1_q));  // open: nQ
  Add #(.Bits(20)) add_1 (.a(counter_1_out[22:3]), .b(register_1_q), .c_i(1'b0), .s(ROM_ADDR));  // open: c_o
  // Probe on {shift_reg_2_q[3:0], shift_reg_3_q, shift_reg_4_q[6:0], SI}
  // Probe addr on ROM_ADDR
  RAMAsync #(.AddrBits(20), .Bits(8)) TESTROM (.A(ROM_ADDR), .D({8{1'b0}}), .we(1'b0), .Q(TESTROM_q));
  BitSelector #(.Selector_Bits(3)) bitselector_1 (.in(multiplexer_1_out), .sel(sub_1_s), .out(bitselector_1_out));
  // Probe data on TESTROM_q
  assign SO = d_ff_as_1_q ? bitselector_1_out : 1'bz;  // Driver driver_1

  // Notes on the sheet:
  //   CE: default 1
  //   HOLD: default 1
endmodule

/* Test case opcode:
          TEST_ CE_ SCLK opcode SI                    a2   a1   a0   addr     data SO
          0     1   0    x      x                     x    x    x    x        0    x
repeat(8) 0     0   C    X      ((0x03 >> (7-n))&0x1) X    X    x    X        0    X
repeat(8) 0     0   C    0x3    ((0x12 >> (7-n))&0x1) X    X    x    X        0    X
repeat(8) 0     0   C    0x3    ((0x34 >> (7-n))&0x1) 0x12 X    x    X        0    X
repeat(8) 0     0   C    0x3    ((0x56 >> (7-n))&0x1) 0x12 0x34 x    X        X    X          
loop(n,8)
          0     0   0    0x3    0                     0x12 0x34 0x56 0x23456 0x96 ((0x96 >> (7-n)&0x1))   
          0     0   1    0x3    0                     0x12 0x34 0x56 0x23456 0x96 ((0x96 >> (7-n)&0x1))   
end loop
loop(n,8)
          0     0   0    0x3    0                     0x12 0x34 0x56 0x23457 0x5A ((0x5A >> (7-n)&0x1))   
          0     0   1    0x3    0                     0x12 0x34 0x56 0x23457 0x5A ((0x5A >> (7-n)&0x1))   
end loop
memory TESTROM(0x23456)=0x96;
memory TESTROM(0x23457)=0x5A;
*/
