// Digital circuit shift_reg.dig as structural Verilog
module shift_reg (
  input  DS7,
  input  SCLK,
  input  RST,
  input  DS0,
  input  S1,
  input  S0,
  output [7:0] Q,
  output Q0,
  output Q7
);

  _74299 _74299_1 (
    .pin1(S0), .pin2(1'b0), .pin3(1'b0), .pin4(Q[6]), .pin5(Q[4]), .pin6(Q[2]), .pin7(Q[0]), .pin8(Q0),
    .pin9(RST), .pin10(1'b0), .pin11(DS0), .pin12(SCLK), .pin13(Q[1]), .pin14(Q[3]), .pin15(Q[5]),
    .pin16(Q[7]), .pin17(Q7), .pin18(DS7), .pin19(S1), .pin20(1'b1));
endmodule

/* Test case zero:
RST_ DS0 DS7 S0 S1 Q0 Q7 Q
0    X   X   0  0  0  0  0
0    X   X   0  1  0  0  0
0    X   X   1  0  0  0  0
*/

/* Test case load msb-first via ds0:
          RST_ DS0                   DS7 S0 S1 SCLK Q0 Q7 Q
          0    X                     X   0  1  0    0  0  0
repeat(8) 1    ((0x56 >> (7-n))&0x1) 0   1  0  C    X  X  X
          1    X                     X   0  1  0    0  0  0x56
*/
