// Digital circuit spicomp.dig as structural Verilog
module spicomp (
  input  RST,
  input  CLK,
  input  TEST
);

  wire _74238_1_pin13, _74238_1_pin14, _74238_2_pin13, _74238_2_pin14, and_1_out, and_2_out, and_3_out,
       bitselector_1_out, comparator_1_eq, comparator_2_eq, decoder_1_out_1, decoder_1_out_2,
       decoder_2_out_1, decoder_2_out_2, IR_NEXT_pin18, not_1_out, not_2_out, not_3_out, not_4_out,
       notconnected_4_out, notconnected_5_out, notconnected_6_out, notconnected_7_out, or_1_out, or_2_out,
       or_3_out, or_4_out, ROM_so, X_pin11, X_pin17, X_pin18, Y_pin17, Y_pin18;
  wire [0:0] counter_1_out;
  wire [2:0] counter_1_out_2, counter_1_out_3, ROM_bit, ROM_byte;
  wire [7:0] _74238_1_pin1, _74273_1_pin2, IR_NEXT_pin4, multiplexer_1_out, multiplexer_3_out,
       notconnected_8_out, notconnected_9_out, notconnected_10_out, PROG_d, TESTPROG_q, X_pin4, Y_pin4;
  wire [19:0] ROM_rom_addr;

  not not_1 (not_1_out, RST);
  Counter #(.Bits(7)) counter_1 (
    .en(1'b1), .C(CLK), .clr(not_1_out), .out({counter_1_out_3, counter_1_out_2, counter_1_out[0]}));  // open: ovf
  // Probe S_R on _74238_1_pin1[2:0]
  Decoder #(.Selector_Bits(3)) decoder_1 (
    .sel(_74238_1_pin1[2:0]), .out_1(decoder_1_out_1), .out_2(decoder_1_out_2));  // open: out_0, out_3, out_4, out_5, out_6, out_7
  // Probe S_W on _74238_1_pin1[6:4]
  Decoder #(.Selector_Bits(3)) decoder_2 (
    .sel(_74238_1_pin1[6:4]), .out_1(decoder_2_out_1), .out_2(decoder_2_out_2));  // open: out_0, out_3, out_4, out_5, out_6, out_7
  not not_2 (not_2_out, counter_1_out[0]);
  _74238 _74238_1 (
    .pin1(_74238_1_pin1[0]), .pin2(_74238_1_pin1[1]), .pin3(_74238_1_pin1[2]), .pin4(CLK), .pin5(1'b0),
    .pin6(not_2_out), .pin8(1'b0), .pin13(_74238_1_pin13), .pin14(_74238_1_pin14), .pin16(1'b1));  // open: pin7, pin9, pin10, pin11, pin12, pin15
  _74238 _74238_2 (
    .pin1(_74238_1_pin1[4]), .pin2(_74238_1_pin1[5]), .pin3(_74238_1_pin1[6]), .pin4(CLK), .pin5(not_2_out),
    .pin6(1'b1), .pin8(1'b0), .pin13(_74238_2_pin13), .pin14(_74238_2_pin14), .pin16(1'b1));  // open: pin7, pin9, pin10, pin11, pin12, pin15
  // Probe read on counter_1_out[0]
  // Probe bit on counter_1_out_2
  // Probe byte on counter_1_out_3
  or or_1 (or_1_out, _74238_1_pin14, _74238_2_pin14);
  or or_2 (or_2_out, decoder_1_out_2, decoder_2_out_2);
  or or_3 (or_3_out, _74238_1_pin13, _74238_2_pin13);
  and and_1 (and_1_out, ~counter_1_out[0], ~CLK);  // And
  and and_2 (and_2_out, counter_1_out[0], ~CLK);  // And
  or or_4 (or_4_out, decoder_1_out_1, decoder_2_out_1);
  serial_rom ROM (
    .SCLK(and_2_out), .SI(X_pin11), .CE(_74238_1_pin1[3]), .HOLD(1'b1), .TEST(1'b1),
    .ROM_D(multiplexer_1_out), .SO(ROM_so), .\bit (ROM_bit), .\byte (ROM_byte), .ROM_ADDR(ROM_rom_addr));
  RAMAsync #(.AddrBits(20), .Bits(8)) TESTPROG (.A(ROM_rom_addr), .D({8{1'b0}}), .we(1'b0), .Q(TESTPROG_q));
  ROM #(.AddrBits(20), .Bits(8)) PROG (.A(ROM_rom_addr), .sel(1'b1), .D(PROG_d));
  _74299 X (
    .pin1(or_4_out), .pin2(1'b0), .pin3(1'b0), .pin4(X_pin4[6]), .pin5(X_pin4[4]), .pin6(X_pin4[2]),
    .pin7(X_pin4[0]), .pin9(RST), .pin10(1'b0), .pin11(X_pin11), .pin12(or_1_out), .pin13(X_pin4[1]),
    .pin14(X_pin4[3]), .pin15(X_pin4[5]), .pin16(X_pin4[7]), .pin17(X_pin17), .pin18(X_pin18), .pin19(1'b0),
    .pin20(1'b1));  // open: pin8
  _74299 Y (
    .pin1(or_2_out), .pin2(1'b0), .pin3(1'b0), .pin4(Y_pin4[6]), .pin5(Y_pin4[4]), .pin6(Y_pin4[2]),
    .pin7(Y_pin4[0]), .pin9(RST), .pin10(1'b0), .pin11(X_pin11), .pin12(or_3_out), .pin13(Y_pin4[1]),
    .pin14(Y_pin4[3]), .pin15(Y_pin4[5]), .pin16(Y_pin4[7]), .pin17(Y_pin17), .pin18(Y_pin18), .pin19(1'b0),
    .pin20(1'b1));  // open: pin8
  _74299 IR_NEXT (
    .pin1(_74238_1_pin1[7]), .pin2(1'b0), .pin3(1'b0), .pin4(IR_NEXT_pin4[6]), .pin5(IR_NEXT_pin4[4]),
    .pin6(IR_NEXT_pin4[2]), .pin7(IR_NEXT_pin4[0]), .pin9(RST), .pin10(1'b0), .pin11(ROM_so),
    .pin12(and_1_out), .pin13(IR_NEXT_pin4[1]), .pin14(IR_NEXT_pin4[3]), .pin15(IR_NEXT_pin4[5]),
    .pin16(IR_NEXT_pin4[7]), .pin18(IR_NEXT_pin18), .pin19(1'b0), .pin20(1'b1));  // open: pin8, pin17
  // NotConnected on X_pin18
  // NotConnected on Y_pin18
  // NotConnected on IR_NEXT_pin18
  // Probe on ROM_bit
  // Probe on ROM_byte
  Multiplexer #(.Bits(8)) multiplexer_1 (.sel(TEST), .in_0(TESTPROG_q), .in_1(PROG_d), .out(multiplexer_1_out));
  // Probe R_X on X_pin4
  // Probe R_Y on Y_pin4
  // Probe IR_SR on IR_NEXT_pin4
  // Probe PROG_ADDR on ROM_rom_addr
  // Probe PROG_DATA on multiplexer_1_out
  Comparator #(.Bits(3)) comparator_1 (.a(counter_1_out_2), .b(3'b111), .eq(comparator_1_eq));  // open: gt, lt
  and and_3 (and_3_out, counter_1_out[0], comparator_1_eq, not_4_out, _74238_1_pin1[7], not_3_out);
  not not_3 (not_3_out, and_1_out);
  not not_4 (not_4_out, CLK);
  // NotConnected on notconnected_4_out
  BitSelector #(.Selector_Bits(3)) bitselector_1 (.in(8'hc0), .sel(counter_1_out_2), .out(bitselector_1_out));
  // NotConnected on notconnected_5_out
  // NotConnected on notconnected_6_out
  // NotConnected on notconnected_7_out
  Multiplexer #(.Selector_Bits(3)) multiplexer_2 (
    .sel(_74238_1_pin1[6:4]), .in_0(notconnected_4_out), .in_1(X_pin17), .in_2(Y_pin17), .in_3(X_pin17),
    .in_4(notconnected_5_out), .in_5(notconnected_6_out), .in_6(bitselector_1_out),
    .in_7(notconnected_7_out), .out(X_pin11));
  // Probe SER_BUS on X_pin11
  _74273 _74273_1 (
    .pin1(RST), .pin2(_74273_1_pin2[0]), .pin3(IR_NEXT_pin4[0]), .pin4(IR_NEXT_pin4[1]),
    .pin5(_74273_1_pin2[1]), .pin6(_74273_1_pin2[2]), .pin7(IR_NEXT_pin4[2]), .pin8(IR_NEXT_pin4[3]),
    .pin9(_74273_1_pin2[3]), .pin10(1'b0), .pin11(and_3_out), .pin12(_74273_1_pin2[4]),
    .pin13(IR_NEXT_pin4[4]), .pin14(IR_NEXT_pin4[5]), .pin15(_74273_1_pin2[5]), .pin16(_74273_1_pin2[6]),
    .pin17(IR_NEXT_pin4[6]), .pin18(IR_NEXT_pin4[7]), .pin19(_74273_1_pin2[7]), .pin20(1'b1));
  // NotConnected on notconnected_8_out
  // NotConnected on notconnected_9_out
  // NotConnected on notconnected_10_out
  Multiplexer #(.Selector_Bits(3), .Bits(8)) multiplexer_3 (
    .sel(counter_1_out_3), .in_0(8'hf), .in_1(8'h60), .in_2(8'h10), .in_3(8'h20), .in_4(8'h30), .in_5(8'h87),
    .in_6(notconnected_8_out), .in_7(notconnected_9_out), .out(multiplexer_3_out));
  Comparator #(.Bits(8)) comparator_2 (.a({8{1'b0}}), .b(_74273_1_pin2), .eq(comparator_2_eq));  // open: gt, lt
  Multiplexer #(.Bits(8)) multiplexer_4 (
    .sel(comparator_2_eq), .in_0(_74273_1_pin2), .in_1(multiplexer_3_out), .out(_74238_1_pin1));
  // Probe IR on _74273_1_pin2
  // Probe IR_eff on _74238_1_pin1

  // Notes on the sheet:
  //   TEST: default 1
  //   contents of PROG (hex, n*v repeats v):
  //   ab
endmodule

/* Test case boot:
           RST_ CLK IR_eff R_X R_Y
init TEST_=0;
	   0    0   0x0F   0   0
loop(n,15)
           1    C   0x0F   0   0
end loop
loop(n,16)
           1    C   0x60   0   0
end loop
loop(n,16)
           1    C   0x10   0   0
end loop
loop(n,16)
           1    C   0x20   0   0
end loop
loop(n,16)
           1    C   0x30   0   0
end loop

loop(n,15)
           1    C   0x87   0   0
end loop
           1    0   0x87   0   0
           1    1   0xE1   0   0
           1    0   0xE1   0   0
loop(n,15)
           1    C   0xE1   X   0
end loop
           1    0   0xE1   3   0
           1    1   0x92   3   0
           1    0   0x92   3   0
loop(n,15)
           1    C   0x92   3   X
end loop
           1    0   0x92   3   3
           1    1   0x92   3   3
           1    0   0x92   3   3
# write 0x3 into X
memory TESTPROG(0x0)=0xE1;
# write X to Y
memory TESTPROG(0x1)=0x92;
*/
