// Digital circuit uc.dig as structural Verilog
module uc (
  input  CLK,
  input  RESET,
  input  INT_PENDING,
  output [7:0] DATA,
  output ADDR_OE,
  output [2:0] ALU_OP,
  output PC_INC,
  output IN1_CP,
  output ALU_CP,
  output MEM_WE,
  output IR0_CP,
  output W_CP,
  output X_CP,
  output Y_CP,
  output Z_CP,
  output A0_CP,
  output A1_CP,
  output A2_CP,
  output UNUSED_F,
  output HALT,
  output ALU_OE,
  output MEM_OE,
  output IO_RTW_OE,
  output PC_SPE,
  output W_OE,
  output X_OE,
  output Y_OE,
  output Z_OE,
  output [7:0] uIR0,
  output [7:0] uIR1,
  output [18:0] uAddr,
  output [7:0] uPC,
  output [1:0] stage,
  output [7:0] uData,
  output IOX_CP,
  output IOX_RTR_OE,
  output A0_OE,
  output A1_OE,
  output A2_OE,
  output [2:0] IO_SEL,
  output IOX_DATA_OE,
  output [7:0] IR0
);

  wire _74138_1_pin13, _74138_1_pin15, _74238_1_pin12, _74238_1_pin13, _74238_1_pin14, _74238_1_pin15,
       and_1_out, and_2_out, and_3_out, and_4_out, and_5_out, FLAGS_pin11, FLAGS_pin15, multiplexer_1_out,
       not_1_out, not_2_out, not_3_out, not_4_out, not_5_out, not_6_out, uPC1_pin10;

  not not_1 (not_1_out, and_1_out);
  and and_1 (and_1_out, not_2_out, _74238_1_pin14);
  not not_2 (not_2_out, _74138_1_pin15);
  and and_2 (and_2_out, RESET, not_1_out);
  // Probe INT_EN on FLAGS_pin15
  and and_3 (and_3_out, FLAGS_pin15, ~uAddr[18], INT_PENDING);  // And
  _74161 uPC1 (
    .pin1(and_2_out), .pin2(CLK), .pin3(1'b0), .pin4(1'b0), .pin5(1'b0), .pin6(1'b0), .pin7(1'b1),
    .pin8(1'b0), .pin9(1'b1), .pin10(uPC1_pin10), .pin11(uAddr[6]), .pin12(uAddr[5]), .pin13(uAddr[4]),
    .pin14(uAddr[3]), .pin16(1'b1));  // open: pin15
  _74161 uPC0 (
    .pin1(and_2_out), .pin2(CLK), .pin3(1'b0), .pin4(1'b0), .pin5(1'b0), .pin6(1'b0), .pin7(1'b1),
    .pin8(1'b0), .pin9(1'b1), .pin10(1'b1), .pin11(uAddr[2]), .pin12(uAddr[1]), .pin13(stage[1]),
    .pin14(stage[0]), .pin15(uPC1_pin10), .pin16(1'b1));
  // Probe INT_CHG on DATA[7]
  Multiplexer multiplexer_1 (.sel(DATA[7]), .in_0(FLAGS_pin15), .in_1(DATA[4]), .out(multiplexer_1_out));
  _74574 FLAGS (
    .pin1(1'b0), .pin2(DATA[0]), .pin3(DATA[1]), .pin4(DATA[2]), .pin5(DATA[3]), .pin6(multiplexer_1_out),
    .pin7(1'b0), .pin8(1'b0), .pin9(1'b0), .pin10(1'b0), .pin11(FLAGS_pin11), .pin15(FLAGS_pin15),
    .pin16(uAddr[18]), .pin17(uAddr[17]), .pin18(uAddr[16]), .pin19(uAddr[15]), .pin20(1'b1));  // open: pin12, pin13, pin14
  // _74574 IR0: pin names not known; wires that end beside it: 1'b0, and_3_out, 1'b0, 1'b1, IR0_CP
  not not_3 (not_3_out, stage[0]);
  not not_4 (not_4_out, stage[1]);
  and and_4 (and_4_out, not_3_out, not_4_out);
  _74238 _74238_1 (
    .pin1(stage[0]), .pin2(stage[1]), .pin3(1'b0), .pin4(1'b0), .pin5(CLK), .pin6(1'b1), .pin8(1'b0),
    .pin12(_74238_1_pin12), .pin13(_74238_1_pin13), .pin14(_74238_1_pin14), .pin15(_74238_1_pin15),
    .pin16(1'b1));  // open: pin7, pin9, pin10, pin11
  ROM #(.AddrBits(19), .Bits(8)) uROM (
    .A({uAddr[18:15], IR0[7:3], IO_SEL, uAddr[6:1], stage[1]}), .sel(1'b1), .D(uData));
  not not_5 (not_5_out, _74238_1_pin12);
  // _74574 uIR1: pin names not known; wires that end beside it: 1'b0, 1'b0, 1'b1, _74238_1_pin13
  // _74574 uIR0: pin names not known; wires that end beside it: 1'b0, 1'b0, 1'b1, _74238_1_pin15
  not not_6 (not_6_out, MEM_WE);
  and and_5 (and_5_out, and_4_out, not_6_out);
  assign DATA = ~_74138_1_pin13 ? {4'b0000, uIR1[7:4]} : 8'bz;  // DriverInvSel driverinvsel_1
  _74238 _74238_2 (
    .pin1(uIR1[0]), .pin2(uIR1[1]), .pin3(uIR1[2]), .pin4(not_5_out), .pin5(uIR1[3]), .pin6(1'b1),
    .pin7(FLAGS_pin11), .pin8(1'b0), .pin9(IOX_CP), .pin10(IR0_CP), .pin11(MEM_WE), .pin12(ALU_CP),
    .pin13(IN1_CP), .pin15(PC_INC), .pin16(1'b1));  // open: pin14
  _74238 _74238_3 (
    .pin1(uIR1[0]), .pin2(uIR1[1]), .pin3(uIR1[2]), .pin4(1'b0), .pin5(not_5_out), .pin6(uIR1[3]),
    .pin7(UNUSED_F), .pin8(1'b0), .pin9(A2_CP), .pin10(A1_CP), .pin11(A0_CP), .pin12(Z_CP), .pin13(Y_CP),
    .pin14(X_CP), .pin15(W_CP), .pin16(1'b1));
  _74138 _74138_1 (
    .pin1(uIR0[0]), .pin2(uIR0[1]), .pin3(uIR0[2]), .pin4(and_5_out), .pin5(uIR0[3]), .pin6(RESET),
    .pin7(IOX_DATA_OE), .pin8(1'b0), .pin9(PC_SPE), .pin10(IO_RTW_OE), .pin11(MEM_OE), .pin12(ALU_OE),
    .pin13(_74138_1_pin13), .pin14(HALT), .pin15(_74138_1_pin15), .pin16(1'b1));
  _74138 _74138_2 (
    .pin1(uIR0[0]), .pin2(uIR0[1]), .pin3(uIR0[2]), .pin4(and_5_out), .pin5(1'b0), .pin6(uIR0[3]),
    .pin7(IOX_RTR_OE), .pin8(1'b0), .pin9(A2_OE), .pin10(A1_OE), .pin11(A0_OE), .pin12(Z_OE), .pin13(Y_OE),
    .pin14(X_OE), .pin15(W_OE), .pin16(1'b1));

  assign IR0[2:0] = IO_SEL;
  assign {uAddr[14:7], uAddr[0]} = {IR0[7:3], IO_SEL, stage[1]};
  assign uIR0[7:4] = {ADDR_OE, ALU_OP};
  assign uPC = {uAddr[6:1], stage};

  // Notes on the sheet:
  //   RESET: default 1
  //   2B
  //   1A
  //   1B
  //   1Y
  //   2Y
  //   2A
  //   uROM loads ucode.hex
  //   5A
  //   5Y
endmodule

/* Test case uc-hlt:
CLK_ RESET_ HALT_ $uPC
C    0      1     0
C    0      1     0
C    0      1     0
*/
