// Digital circuit alu.dig as structural Verilog
module alu (
  input  [2:0] ALU_OP,
  input  ALU_OE,
  input  ALU_CP,
  input  IN1_CP,
  input  [7:0] DATA_2,
  input  DATA_OE,
  output [7:0] DATA
);

  wire [7:0] ALU_d, undriven;

  PullDown pulldown_1 (.out(DATA_OE));
  PullDown #(.Bits(8)) pulldown_2 (.out(DATA_2));
  assign DATA = DATA_OE ? DATA_2 : 8'bz;  // Driver driver_1
  // _74574 IN1: pin names not known; wires that end beside it: 1'b0, 1'b0, 1'b1, IN1_CP
  ROM #(.AddrBits(19), .Bits(8)) ALU (.A({ALU_OP, undriven, DATA}), .sel(1'b1), .D(ALU_d));
  // _74574 ALU_2: pin names not known; wires that end beside it: ALU_OE, 1'b0, 1'b1, ALU_CP

  // Notes on the sheet:
  //   ALU loads alu.hex
endmodule

/* Test case:
$DATA $DATA_OE ALU_OP IN1_CP ALU_CP ALU_OE_ DATA
0x1   1        X      C      0      1       0X1
0x2   1        0      0      C      1       0x2
X     0        X      0      0      0       0x3
*/
