// Digital circuit io.dig as structural Verilog
module io (
  input  [7:0] DATA,
  input  TTYIN_CP,
  input  TTYIN_OE,
  input  TTYOUT_CP,
  input  [15:0] KEY_D,
  input  KEY_AV,
  output TERM_CLK,
  output KEY_CLK,
  output [1:0] IN_SOURCE,
  output [7:0] IN_VALUE
);

  wire demultiplexer_1_out_1, demultiplexer_1_out_2, nor_1_out, not_1_out, rs_ff_as_1_nq, rs_ff_as_1_q,
       telnet_1_av;
  wire [1:0] priorityencoder_1_num;
  wire [6:0] multiplexer_1_out;
  wire [7:0] counter_1_out, rom_1_d, telnet_1_out;
  wire [7:7] priorityencoder_1_any;

  Counter #(.Bits(8)) counter_1 (.en(1'b1), .C(demultiplexer_1_out_2), .clr(1'b0), .out(counter_1_out));  // open: ovf
  nor nor_1 (nor_1_out, demultiplexer_1_out_1, TTYOUT_CP);
  not not_1 (not_1_out, TTYIN_OE);
  ROM #(.AddrBits(8), .Bits(8)) rom_1 (.A(counter_1_out), .sel(1'b1), .D(rom_1_d));
  RS_FF_AS rs_ff_as_1 (.S(TTYOUT_CP), .R(TTYIN_CP), .Q(rs_ff_as_1_q), .nQ(rs_ff_as_1_nq));
  Telnet #(.telnetEscape("false"), .port(45454)) telnet_1 (
    .in(DATA), .C(nor_1_out), .wr(rs_ff_as_1_q), .rd(rs_ff_as_1_nq), .out(telnet_1_out), .av(telnet_1_av));
  PriorityEncoder #(.Selector_Bits(2)) priorityencoder_1 (
    .in0(KEY_AV), .in1(telnet_1_av), .in2(rom_1_d[7]), .in3(1'b0), .num(priorityencoder_1_num),
    .any(priorityencoder_1_any[7]));
  Multiplexer #(.Selector_Bits(2), .Bits(7)) multiplexer_1 (
    .sel(priorityencoder_1_num), .in_0(KEY_D[6:0]), .in_1(telnet_1_out[6:0]), .in_2(rom_1_d[6:0]),
    .in_3({7{1'b0}}), .out(multiplexer_1_out));
  D_FF #(.Bits(8)) d_ff_1 (.D({priorityencoder_1_any[7], multiplexer_1_out}), .C(not_1_out), .Q(IN_VALUE));  // open: nQ
  D_FF #(.Bits(2)) d_ff_2 (.D(priorityencoder_1_num), .C(not_1_out), .Q(IN_SOURCE));  // open: nQ
  assign DATA = ~TTYIN_OE ? IN_VALUE : 8'bz;  // DriverInvSel driverinvsel_1
  Demultiplexer #(.Selector_Bits(2)) demultiplexer_1 (
    .sel(IN_SOURCE), .in(TTYIN_CP), .out_0(KEY_CLK), .out_1(demultiplexer_1_out_1),
    .out_2(demultiplexer_1_out_2));  // open: out_3

  assign TERM_CLK = TTYOUT_CP;
endmodule

/* Test case:
DATA KEY_D KEY_AV TTYIN_CP TTYIN_OE_ DATA_out $IN_SOURCE KEY_CLK
Z    0x61  1      0        1         Z        X          0
Z    0x61  1      0        0         0xE1     0          0
Z    0x61  1      0        1         Z        0          0
Z    0x61  1      1        1         Z        0          1
*/
