// Logisim project lutcomp.circ as structural Verilog: 16 circuits, main circuit main
// 10
module main (
  input  RESET,
  output halt
);

  wire A0_CP, A1_CP, A2_CP, ALU_CP, and_1_out, and_2_out, and_4_out, and_5_out, BKPT, CLK, clock_1_out,
       comparator_1_eq, comparator_1_gt, comparator_1_lt, comparator_2_eq, dipswitch_1_p1, FLAGS_CP, IN1_CP,
       IR0_CP, key_ctrl_1_key_clk, key_ctrl_1_key_read_en, keyboard_1_avail, MEM_CP, n74hct138_1_ny0,
       n74hct238_1_ny0, n74hct238_1_ny1, n74hct238_1_ny2, n74hct238_1_ny3, nADDR_OE, nALU_OE, nCLK, nHALT,
       nIMM_OE, nMEM_OE, not_3_out, not_4_out, not_6_out, not_7_out, not_8_out, not_9_out, nPC_SPE, nRESET,
       nTTYIN_OE, nW_OE, nX_OE, nY_OE, nZ_OE, or_1_out, PC0_tc, PC1_tc, PC2_tc, PC3_tc, PC4_tc, PC_INC,
       TTYIN_CP, TTYOUT_CP, uPC0_tc, W_CP, X_CP, Y_CP, Z_CP;
  wire [2:0] ALU_OP;
  wire [3:0] PC0_q, PC1_q, PC2_q, PC3_q, PC4_q, PC5_q, uIR0_q, uIR1_q, uIR1_q_2, uPC0_q, uPC1_q;
  wire [6:0] keyboard_1_data;
  wire [7:0] ALU_LUT_data, ALU_zpeek, as6c4008_1_peek, bit_extender_1_out, controlled_buffer_3_out, DATA,
       FLAGS_q, IN1_2_q, IR0_q, ROM_data, TTYOUT_q, uROM_data, W_peek, X_peek, Y_peek, Z_peek;
  wire [7:7] key_ctrl_1_rdy;
  wire [23:0] ADDR, JMPS_q0, JMPS_q1, JMPS_q2, JMPS_q3, JMPS_q4, JMPS_q5, JMPS_q6, JMPS_q7;

  Clock clock_1 (.out(clock_1_out));
  Comparator comparator_1 (.a(DATA), .b({8{1'b0}}), .gt(comparator_1_gt), .eq(comparator_1_eq), .lt(comparator_1_lt));
  not not_1 (nRESET, RESET);
  and and_1 (and_1_out, clock_1_out, ~BKPT);  // AND_Gate
  or or_1 (or_1_out, comparator_1_gt, comparator_1_eq, comparator_1_lt);
  not not_2 (halt, nHALT);
  not not_3 (not_3_out, and_2_out);
  and and_2 (and_2_out, not_4_out, n74hct238_1_ny1);
  not not_4 (not_4_out, n74hct138_1_ny0);
  and and_3 (CLK, nHALT, and_1_out);
  and and_4 (and_4_out, nRESET, not_3_out);
  not not_5 (nCLK, CLK);
  _74HCT161 uPC1 (
    .SPE__nPE(1'b1), .CP(nCLK), .PE_CEP(1'b1), .TE_CET(uPC0_tc), .nMR(and_4_out), .Q(uPC1_q));  // open: P, TC
  _74HCT161 uPC0 (
    .SPE__nPE(1'b1), .CP(nCLK), .PE_CEP(1'b1), .TE_CET(1'b1), .nMR(and_4_out), .Q(uPC0_q), .TC(uPC0_tc));  // open: P
  _74HCT574 FLAGS (.D(DATA), .CP(FLAGS_CP), .nOE(1'b0), .Q(FLAGS_q));  // open: Zpeek
  _74HCT574 IR0 (.D(DATA), .CP(IR0_CP), .nOE(1'b0), .Q(IR0_q));  // open: Zpeek
  // Probe on {FLAGS_q[3:0], IR0_q, uPC1_q, uPC0_q[3:1]}
  // Probe on uPC0_q[1:0]
  // Probe on {uPC1_q, uPC0_q[3:1]}
  // Probe on IR0_q
  // Probe on FLAGS_q[3:0]
  _74HCT238 u_74hct238_1 (
    .nE1(1'b0), .nE2(nCLK), .E3(1'b1), .A({1'b0, uPC0_q[1:0]}), .nY0(n74hct238_1_ny0), .nY1(n74hct238_1_ny1),
    .nY2(n74hct238_1_ny2), .nY3(n74hct238_1_ny3));  // open: nY4, nY5, nY6, nY7
  // Probe on FLAGS_q[0]
  // Probe on FLAGS_q[2]
  ROM #(.addrWidth(19), .Select("high")) uROM (.addr({FLAGS_q[3:0], IR0_q, uPC1_q, uPC0_q[3:1]}), .data(uROM_data));
  // Probe on FLAGS_q[1]
  _74HCT161 PC0 (
    .SPE__nPE(nPC_SPE), .P(ADDR[3:0]), .CP(PC_INC), .PE_CEP(1'b1), .TE_CET(1'b1), .nMR(nRESET), .Q(PC0_q),
    .TC(PC0_tc));
  _74HCT161 PC1 (
    .SPE__nPE(nPC_SPE), .P(ADDR[7:4]), .CP(PC_INC), .PE_CEP(PC0_tc), .TE_CET(1'b1), .nMR(nRESET), .Q(PC1_q),
    .TC(PC1_tc));
  _74HCT161 PC2 (
    .SPE__nPE(nPC_SPE), .P(ADDR[11:8]), .CP(PC_INC), .PE_CEP(PC0_tc), .TE_CET(PC1_tc), .nMR(nRESET),
    .Q(PC2_q), .TC(PC2_tc));
  _74HCT161 PC3 (
    .SPE__nPE(nPC_SPE), .P(ADDR[15:12]), .CP(PC_INC), .PE_CEP(PC0_tc), .TE_CET(PC2_tc), .nMR(nRESET),
    .Q(PC3_q), .TC(PC3_tc));
  _74HCT161 PC4 (
    .SPE__nPE(nPC_SPE), .P(ADDR[19:16]), .CP(PC_INC), .PE_CEP(PC0_tc), .TE_CET(PC3_tc), .nMR(nRESET),
    .Q(PC4_q), .TC(PC4_tc));
  _74HCT161 PC5 (
    .SPE__nPE(nPC_SPE), .P(ADDR[23:20]), .CP(PC_INC), .PE_CEP(PC0_tc), .TE_CET(PC4_tc), .nMR(nRESET),
    .Q(PC5_q));  // open: TC
  assign DATA = ~nIMM_OE ? bit_extender_1_out : 8'bz;  // Controlled_Buffer controlled_buffer_1
  assign bit_extender_1_out = {{4{1'b0}}, uIR1_q_2};  // Bit_Extender bit_extender_1
  // Probe on bit_extender_1_out
  _74HCT574 uIR1 (.D(uROM_data), .CP(n74hct238_1_ny2), .nOE(1'b0), .Q({uIR1_q_2, uIR1_q}));  // open: Zpeek
  _74HCT574 uIR0 (.D(uROM_data), .CP(n74hct238_1_ny0), .nOE(1'b0), .Q({nADDR_OE, ALU_OP, uIR0_q}));  // open: Zpeek
  // Probe on {uIR1_q_2, uIR1_q}
  // Probe on {nADDR_OE, ALU_OP, uIR0_q}
  not not_6 (not_6_out, n74hct238_1_ny3);
  // Probe on PC0_q
  // Probe on PC1_q
  // Probe on PC2_q
  // Probe on PC3_q
  // Probe on PC4_q
  // Probe on PC5_q
  not not_7 (not_7_out, nADDR_OE);
  // DipSwitch #(.NSwitches(1)) dipswitch_1: pin names not known; wires that end beside it: dipswitch_1_p1
  Comparator #(.width(24)) comparator_2 (
    .a(24'hda4), .b({PC5_q, PC4_q, PC3_q, PC2_q, PC1_q, PC0_q}), .eq(comparator_2_eq));  // open: gt, lt
  // Probe on {PC5_q, PC4_q, PC3_q, PC2_q, PC1_q, PC0_q}
  Shift_Register #(.width(24)) JMPS (
    .in({PC5_q, PC4_q, PC3_q, PC2_q, PC1_q, PC0_q}), .clk(and_5_out), .q0(JMPS_q0), .q1(JMPS_q1),
    .q2(JMPS_q2), .q3(JMPS_q3), .q4(JMPS_q4), .q5(JMPS_q5), .q6(JMPS_q6), .q7(JMPS_q7));  // open: shift, out, load, clr, d0, d1, d2, d3, d4, d5, d6, d7
  and and_5 (and_5_out, PC_INC, ~nPC_SPE);  // AND_Gate
  // Probe on JMPS_q0
  // Probe on JMPS_q1
  // Probe on JMPS_q2
  // Probe on JMPS_q3
  // Probe on JMPS_q4
  // Probe on JMPS_q5
  // Probe on JMPS_q6
  // Probe on JMPS_q7
  assign ADDR = ~not_7_out ? {PC5_q, PC4_q, PC3_q, PC2_q, PC1_q, PC0_q} : 24'bz;  // Controlled_Buffer controlled_buffer_2
  _74HCT238 u_74hct238_2 (
    .nE1(not_6_out), .nE2(uIR1_q[3]), .E3(1'b1), .A(uIR1_q[2:0]), .nY0(PC_INC), .nY1(IR0_CP), .nY2(IN1_CP),
    .nY3(ALU_CP), .nY4(MEM_CP), .nY5(TTYIN_CP), .nY7(FLAGS_CP));  // open: nY6
  _74HCT238 u_74hct238_3 (
    .nE1(1'b0), .nE2(not_6_out), .E3(uIR1_q[3]), .A(uIR1_q[2:0]), .nY0(W_CP), .nY1(X_CP), .nY2(Y_CP),
    .nY3(Z_CP), .nY4(A0_CP), .nY5(A1_CP), .nY6(A2_CP), .nY7(TTYOUT_CP));
  _74HCT138 u_74hct138_1 (
    .nE1(1'b0), .nE2(uIR0_q[3]), .E3(nRESET), .A(uIR0_q[2:0]), .nY0(n74hct138_1_ny0), .nY1(nHALT),
    .nY2(nIMM_OE), .nY3(nALU_OE), .nY4(nMEM_OE), .nY5(nTTYIN_OE), .nY6(nPC_SPE));  // open: nY7
  _74HCT138 u_74hct138_2 (
    .nE1(1'b0), .nE2(1'b0), .E3(uIR0_q[3]), .A(uIR0_q[2:0]), .nY0(nW_OE), .nY1(nX_OE), .nY2(nY_OE),
    .nY3(nZ_OE));  // open: nY4, nY5, nY6, nY7
  and and_6 (BKPT, dipswitch_1_p1, comparator_2_eq);
  _74HCT574 ADDR0 (.D(DATA), .CP(A0_CP), .nOE(nADDR_OE), .Q(ADDR[7:0]));  // open: Zpeek
  _74HCT574 ADDR1 (.D(DATA), .CP(A1_CP), .nOE(nADDR_OE), .Q(ADDR[15:8]));  // open: Zpeek
  _74HCT574 ADDR2 (.D(DATA), .CP(A2_CP), .nOE(nADDR_OE), .Q(ADDR[23:16]));  // open: Zpeek
  _74HCT299_simplified W (.IO(DATA), .nOE(nW_OE), .CP(W_CP), .IO_2(DATA), .peek(W_peek));
  _74HCT299_simplified X (.IO(DATA), .nOE(nX_OE), .CP(X_CP), .IO_2(DATA), .peek(X_peek));
  _74HCT299_simplified Y (.IO(DATA), .nOE(nY_OE), .CP(Y_CP), .IO_2(DATA), .peek(Y_peek));
  _74HCT299_simplified Z (.IO(DATA), .nOE(nZ_OE), .CP(Z_CP), .IO_2(DATA), .peek(Z_peek));
  not not_8 (not_8_out, MEM_CP);
  not not_9 (not_9_out, ADDR[19]);
  // Probe on ADDR
  // Probe on W_peek
  // Probe on X_peek
  // Probe on Y_peek
  // Probe on Z_peek
  AS6C4008 as6c4008_1 (
    .D(DATA), .A(ADDR[18:0]), .nCE(not_9_out), .nOE(nMEM_OE), .nWE(not_8_out), .peek(as6c4008_1_peek),
    .D_2(DATA));
  SST39SF040 sst39sf040_1 (.ROM_D(ROM_data), .nCE(ADDR[19]), .nOE(nMEM_OE), .DQ(DATA));
  // Probe on as6c4008_1_peek
  // Probe on ROM_data
  ROM #(.addrWidth(19), .Select("high")) ROM (.addr(ADDR[18:0]), .data(ROM_data));
  // Probe on DATA
  // Probe on IN1_2_q
  _74HCT574 IN1_2 (.D(DATA), .CP(IN1_CP), .nOE(1'b0), .Q(IN1_2_q));  // open: Zpeek
  assign controlled_buffer_3_out = TTYIN_CP ? DATA : 8'bz;  // Controlled_Buffer controlled_buffer_3
  Keyboard keyboard_1 (
    .clk(key_ctrl_1_key_clk), .re(key_ctrl_1_key_read_en), .avail(keyboard_1_avail), .data(keyboard_1_data));  // open: clr
  TTY #(.trigger("falling")) tty_1 (.data(DATA[6:0]), .clk(TTYOUT_CP));  // open: we, clr
  Pull_Resistor pull_resistor_1 (.node(controlled_buffer_3_out[7]));
  _74HCT574 TTYOUT (.D(DATA), .CP(TTYOUT_CP), .nOE(1'b0), .Q(TTYOUT_q));  // open: Zpeek
  key_ctrl key_ctrl_1 (
    .key_avail(keyboard_1_avail), .discard(controlled_buffer_3_out[7]), .key_clk(key_ctrl_1_key_clk),
    .key_read_en(key_ctrl_1_key_read_en), .rdy(key_ctrl_1_rdy[7]));
  // Probe on TTYOUT_q
  ROM #(.addrWidth(19), .Select("high")) ALU_LUT (.addr({ALU_OP, IN1_2_q, DATA}), .data(ALU_LUT_data));
  assign DATA = ~nTTYIN_OE ? {key_ctrl_1_rdy[7], keyboard_1_data} : 8'bz;  // Controlled_Buffer controlled_buffer_4
  _74HCT574 ALU (.D(ALU_LUT_data), .CP(ALU_CP), .nOE(nALU_OE), .Q(DATA), .Zpeek(ALU_zpeek));
  // Probe on ALU_zpeek

  // Notes on the sheet:
  //   LOGISIM TEST
  //   Arudino2
  //   REAL
  //   Arduino3
  //   1A
  //   1B
  //   1Y
  //   1A
  //   2Y
  //   2B
  //   2A
  //   2Y
  //   2A
  //   4A
  //   4Y
  //   4B
  //   1Y
  //   6A
  //   6Y
  //   Arduino4
  //   [UPSIDE DOWN]
  //   contents of uROM (hex, n*v repeats v):
  //   84 1 82 8e 82 d 88 0 84 c 88 0 84 8 8 4 88 0 80 6 108*1 84 1 1 1 88 0 80 6 120*1 84 1 1 1 88 0 80 6
  //   120*1 84 1 82 8e 82 d 88 0 84 c 4 2 f2 73 3 4 83 2 a2 3 83 2 e2 63 83 2 c2 3 83 7 88 0 80 6 94*1 84
  //   1 82 8e 82 d 88 0 84 c 4 2 f2 73 83 2 82 13 3 4 a2 13 83 7 88 0 80 6 100*1 84 1 1 1 88 0 80 6 120*1
  //   84 1 1 1 88 0 80 6 120*1 84 1 1 1 88 0 80 6 120*1 84 1 1 1 88 0 80 6 120*1 84 1 1 1 88 0 80 6 120*1
  //   84 1 1 1 88 0 80 6 120*1 84 1 1 1 88 0 80 6 120*1 84 1 1 1 88 0 80 6 120*1 84 1 1 1 88 0 80 6 120*1
  //   84 1 82 7 88 0 80 6 120*1 84 1 82 7 82 8 82 9 82 a 82 b 82 2 82 c 82 d 82 e 88 0 80 6 104*1 84 1 82
  //   8e 82 d 88 0 84 c 4 8 84 2 82 13 83 c 4 9 84 2 82 23 83 c 4 a 88 c 89 d 8a e 4 8 82 8e 82 d 88 0 84
  //   c 8 4 88 0 80 6 78*1 84 1 82 8e 82 d 88 0 84 c 4 b 88 0 84 c 4 8 84 2 82 13 83 c 4 9 84 2 82 23 83 c
  //   4 a 88 c 89 d 8a e b 4 88 0 80 6 82*1 84 1 82 8e 82 d 88 0 84 c 5 4 4 5 88 0 80 6 110*1 84 1 82 8e
  //   82 d 88 0 84 c 4 f 88 0 80 6 112*1 84 1 82 8e 82 d 82 2 f2 73 83 2 82 cc 4 3 83 8 24 3 83 7 8 4 82
  //   dc 4 3 83 9 24 3 83 7 9 4 82 ec 4 3 83 a 24 3 83 7 a 4 82 fc 4 3 83 b b 4 88 0 84 c 4 b 88 c 89 d 8a
  //   e b 4 88 0 80 6 54*1 84 1 82 8e 82 d 82 cc 4 8 82 dc 4 9 82 ec 4 a 88 c 89 d 8a e 4 b 88 0 82 8e 82
  //   d 84 c b 4 82 cc 4 2 a2 13 83 7 82 13 3 4 82 dc 4 2 a2 3 83 7 82 3 3 4 82 ec 4 2 a2 3 83 7 82 3 3 4
  //   88 0 80 6 52*1 84 1 82 8e 82 d 88 0 84 c 4 b 88 0 84 c b 4 88 0 80 6 106*1 84 1 1 1 88 0 80 6 120*1
  //   84 1 1 1 88 0 80 6 120*1 84 1 1 1 88 0 80 6 120*1 84 1 1 1 88 0 80 6 120*1 84 1 1 1 88 0 80 6 120*1
  //   84 1 1 1 88 0 80 6 120*1 84 1 1 1 88 0 80 6 120*1 84 1 1 1 88 0 80 6 120*1 84 1 1 1 88 0 80 6 120*1
  //   84 1 82 8e 82 d 88 0 84 c 4 9 88 0 84 c 4 a 89 2 da 3 83 2 a2 3 83 7 89 2 9a 3 88 0 84 c 3 4 88 0 80
  //   6 86*1 84 1 82 8e 82 d 88 0 84 c 4 9 88 0 84 c 4 a 88 0 84 b 89 2 da 3 83 2 a2 3 83 7 89 2 9a 3 8b c
  //   3 4 8b 2 82 13 83 b 8a 2 f2 43 83 2 99 3 8b c 3 4 8a 2 a2 3 83 7 88 0 80 6 60*1 84 1 82 8e 82 d 88 0
  //   84 c 4 2 88 0 84 c 4 8 88 0 84 c a8 3 83 7 88 3 83 2 82 3 3 4 88 0 80 6 90*1 84 1 82 8e 82 d 88 0 84
  //   c 4 2 88 0 84 c 4 8 88 0 84 c 88 3 3 4 a8 3 83 2 e2 63 83 2 c2 3 83 7 88 0 80 6 86*1 84 1 82 8e 82 d
  //   88 0 84 c 4 2 88 0 84 c 4 8 88 0 84 c 88 3 3 4 a8 3 83 7 88 0 80 6 94*1 84 1 82 8e 82 d 88 0 84 c 4
  //   2 f2 73 83 2 82 13 83 8 a2 13 83 2 e2 13 83 b 88 0 84 c 4 2 a8 3 83 2 cb 3 83 7 88 0 80 6 82*1 84 1
  //   88 0 88 0 88 0 80 6 82 7 82 7 82 7 82 7 82 7 82 7 82 7 82 7 82 7 82 7 82 7 82 7 82 7 82 7 82 7 82 7
  //   88 0 80 6 82*1 84 1 82 8e 82 d 88 0 84 c 4 2 88 0 84 c 4 8 88 0 84 c d8 3 83 8 8 4 82 2 a8 3 83 2 e2
  //   23 83 2 c2 3 83 7 88 0 80 6 82*1 84 1 1 1 88 0 80 6 120*1 84 1 1 1 88 0 80 6 120*1 84 1 1 1 88 0 80
  //   6 120*1 84 1 1 1 88 0 80 6 120*1 84 1 1 1 88 0 80 6 120*1 84 1 1 1 88 0 80 6 120*1 84 1 1 1 88 0 80
  //   6 120*1 84 1 1 1 88 0 80 6 120*1 84 1 82 8e 82 d 88 0 84 c 4 2 88 0 e4 3 3 4 83 2 a2 3 83 7 88 0 80
  //   6 100*1 84 1 82 8e 82 d 88 0 84 c 4 2 88 0 c4 3 3 4 83 2 a2 3 83 7 88 0 80 6 100*1 84 1 82 8e 82 d
  //   88 0 84 c 4 2 88 0 c4 3 83 8 e4 3 83 2 f2 73 83 2 e8 3 3 4 83 2 a2 3 83 7 88 0 80 6 88*1 84 1 82 8e
  //   82 d 88 0 84 c 4 2 88 0 84 c 64 3 88 0 84 c 3 4 83 2 a2 3 83 7 88 0 80 6 94*1 84 1 82 8e 82 d 88 0
  //   84 c 4 2 88 0 84 c 44 3 88 0 84 c 3 4 83 2 a2 3 83 7 88 0 80 6 94*1 84 1 82 8e 82 d 88 0 84 c 4 8 88
  //   0 84 c 4 9 88 0 84 c 88 2 c9 3 3 4 e9 3 83 2 f2 73 83 2 64 3 3 4 83 2 a2 3 83 7 88 0 80 6 78*1 84 1
  //   88 0 82 8e 82 d 84 2 e2 33 83 2 c2 43 83 2 f2 33 83 b 84 2 e2 43 83 2 a2 3 83 2 e2 23 83 2 c2 3 83 7
  //   88 0 84 c 4 2 f2 53 83 2 e2 f3 83 2 cb 3 83 b 88 0 84 c 4 2 fb 3 88 0 84 c 3 4 83 2 a2 3 83 7 88 0
  //   80 6 46*1 84 1 1 1 88 0 80 6 120*1 84 1 1 1 88 0 80 6 120*1 84 1 1 1 88 0 80 6 120*1 84 1 1 1 88 0
  //   80 6 120*1 84 1 1 1 88 0 80 6 120*1 84 1 1 1 88 0 80 6 120*1 84 1 1 1 88 0 80 6 120*1 84 1 1 1 88 0
  //   80 6 120*1 84 1 1 1 88 0 80 6 120*1 84 1 88 0 84 c 88 0 84 d 88 0 84 e 6 0 80 6 110*1 84 1 88 0 88 0
  //   88 0 88 0 80 6 116*1 84 1 88 0 88 0 88 0 88 0 80 6 116*1 84 1 88 0 88 0 88 0 88 0 80 6 116*1 84 1 1
  //   1 88 0 80 6 120*1 84 1 1 1 88 0 80 6 120*1 84 1 1 1 88 0 80 6 120*1 84 1 1 1 88 0 80 6 120*1 84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
  //   5A
  //   5Y
  //   3Y
  //   3A
  //   6A
  //   5A
  //   5Y
  //   6Y
  //   contents of ROM (hex, n*v repeats v):
  //   f 80 c fc ff f 0 a4 c fc ff ff ff 94 c 17 0 0 0 40 9b 11 0 a4 c 4 0 0 0 ff 0 0 0 0 81 0 18 16 4 1c
  //   81 18 10 81 10 40 0 10 0 0 14 0 0 45 2b 25 1c 45 42 42 0 0 40 49 0 0 0 44 2 40 a0 0 0 0 45 2d 25 1c
  //   45 42 57 0 0 40 5e 0 0 0 44 2 40 a0 0 0 0 45 2a 25 1c 45 42 6c 0 0 40 73 0 0 0 44 2 40 a0 0 0 0 45
  //   2f 25 1c 45 42 81 0 0 40 88 0 0 0 44 2 40 a0 0 0 0 45 73 25 1c 45 42 96 0 0 40 9d 0 0 0 44 2 40 a0 0
  //   0 0 44 0 16 44 45 0 34 0 25 45 34 41 61 1 0 81 18 20 80 24 48 0 0 0 e a2 20 24 24 a3 10 24 34 0 35 0
  //   25 34 35 42 5d 1 0 81 20 28 80 24 44 0 0 0 e a2 20 24 24 a3 90 24 24 81 28 2c 80 30 40 0 0 0 e a2 28
  //   30 30 a3 90 30 30 e a2 30 30 30 a3 e a2 30 30 30 a3 e a2 2c 30 2c a3 92 24 2c 93 81 28 24 80 2c 40 0
  //   0 0 e a2 24 2c 24 a3 80 2c 40 0 0 0 e a2 28 2c 28 a3 90 28 28 80 2c 1 0 0 0 e a2 28 2c 28 a3 92 28
  //   24 93 80 24 44 0 0 0 e a2 20 24 24 a3 80 28 0 0 0 0 92 28 24 93 80 24 48 0 0 0 e a2 20 24 20 a3 0 34
  //   0 11 34 20 40 5d 1 0 40 61 1 0 81 40 20 80 24 40 0 0 0 e a2 20 24 20 a3 90 20 20 16 20 3e 16 44 45
  //   16 3e 34 25 45 34 41 a3 1 0 0 1d 45 13 1d 0 1d 52 13 1d 0 1d 52 13 1d 0 1d a 13 1d 0 1d 1 16 1d 0 49
  //   c 40 a3 1 0 16 44 45 0 34 0 25 45 34 41 1a 2 0 81 40 10 80 20 40 0 0 0 e a2 10 20 20 a3 80 24 40 0 0
  //   0 e a2 10 24 24 a3 90 24 24 80 28 1 0 0 0 81 28 0 3 0 3 1 3 2 3 3 a4 0 1 0 0 0 e a2 24 0 24 a3 92 24
  //   20 93 81 10 20 80 24 40 0 0 0 e a2 10 24 10 a3 90 10 10 e a2 10 10 10 a3 e a2 10 10 10 a3 e a2 20 10
  //   10 a3 90 10 10 40 1a 2 0 16 44 45 0 34 1 25 45 34 41 91 2 0 81 40 14 80 20 40 0 0 0 e a2 14 20 20 a3
  //   80 24 40 0 0 0 e a2 14 24 24 a3 90 24 24 80 28 1 0 0 0 81 28 0 3 0 3 1 3 2 3 3 a4 0 1 0 0 0 e a2 24
  //   0 24 a3 92 24 20 93 81 14 20 80 24 40 0 0 0 e a2 14 24 14 a3 90 14 14 e a2 14 14 14 a3 e a2 14 14 14
  //   a3 e a2 20 14 14 a3 90 14 14 40 91 2 0 0 45 2b 25 1c 45 42 9f 2 0 40 20 3 0 e a2 14 10 10 a3 81 10 0
  //   a4 c fc ff ff ff 94 c b8 2 0 0 40 4c 17 0 a4 c 4 0 0 0 0 3c a 13 3c 81 40 14 81 14 18 80 38 40 0 0 0
  //   e a2 14 38 38 a3 90 38 38 e a2 38 38 38 a3 e a2 38 38 38 a3 e a2 18 38 18 a3 92 10 18 93 81 14 10 80
  //   18 40 0 0 0 e a2 10 18 10 a3 80 18 40 0 0 0 e a2 14 18 14 a3 90 14 14 80 18 1 0 0 0 e a2 14 18 14 a3
  //   92 14 10 93 40 4d b 0 0 45 2d 25 1c 45 42 2e 3 0 40 c0 3 0 81 10 0 3 0 3 1 3 2 3 3 a4 0 1 0 0 0 e a2
  //   14 0 10 a3 81 10 0 a4 c fc ff ff ff 94 c 58 3 0 0 40 4c 17 0 a4 c 4 0 0 0 0 3c a 13 3c 81 40 14 81
  //   14 18 80 38 40 0 0 0 e a2 14 38 38 a3 90 38 38 e a2 38 38 38 a3 e a2 38 38 38 a3 e a2 18 38 18 a3 92
  //   10 18 93 81 14 10 80 18 40 0 0 0 e a2 10 18 10 a3 80 18 40 0 0 0 e a2 14 18 14 a3 90 14 14 80 18 1 0
  //   0 0 e a2 14 18 14 a3 92 14 10 93 40 4d b 0 0 45 2a 25 1c 45 42 ce 3 0 40 92 6 0 81 10 18 81 14 10 81
  //   10 14 81 18 38 21 14 38 20 0 22 0 0 23 0 16 15 3c 80 24 0 0 0 0 16 3c 24 16 39 1c 80 28 0 0 0 0 16
  //   1c 28 21 24 28 24 0 26 0 0 27 0 16 25 34 16 34 27 16 24 34 16 34 26 0 35 0 16 35 25 0 35 0 16 35 24
  //   e a2 20 24 20 a3 16 39 1c 80 24 0 0 0 0 16 1c 24 21 14 24 24 0 26 0 0 27 0 16 15 3c 80 14 0 0 0 0 16
  //   3c 14 21 14 38 14 0 16 0 0 17 0 81 24 38 e a2 38 14 24 a3 16 26 3c 16 3c 27 16 25 3c 16 3c 26 16 24
  //   3c 16 3c 25 0 3c 0 16 3c 24 81 20 14 81 24 38 e a2 14 38 14 a3 81 14 20 80 14 0 0 0 0 16 13 1d 16 1d
  //   15 16 12 1d 16 1d 14 80 38 0 0 0 0 16 1b 3d 16 3d 39 16 1a 3d 16 3d 38 21 14 18 24 0 26 0 0 27 0 16
  //   15 3c 80 28 0 0 0 0 16 3c 28 16 19 3d 80 2c 0 0 0 0 16 3d 2c 21 28 2c 28 0 2a 0 0 2b 0 16 29 35 16
  //   35 2b 16 28 35 16 35 2a 0 3e 0 16 3e 29 0 3e 0 16 3e 28 e a2 24 28 24 a3 16 19 3d 80 28 0 0 0 0 16
  //   3d 28 21 14 28 28 0 2a 0 0 2b 0 16 15 3c 80 14 0 0 0 0 16 3c 14 21 14 18 14 0 16 0 0 17 0 81 28 18 e
  //   a2 18 14 28 a3 16 2a 3c 16 3c 2b 16 29 3c 16 3c 2a 16 28 3c 16 3c 29 0 3c 0 16 3c 28 81 24 14 81 28
  //   18 e a2 14 18 14 a3 81 14 28 81 38 14 21 10 14 18 0 1a 0 0 1b 0 16 11 1d 80 38 0 0 0 0 16 1d 38 16
  //   15 3c 80 24 0 0 0 0 16 3c 24 21 38 24 38 0 3a 0 0 3b 0 16 39 1c 16 1c 3b 16 38 1c 16 1c 3a 0 34 0 16
  //   34 39 0 34 0 16 34 38 e a2 18 38 18 a3 16 15 3c 80 38 0 0 0 0 16 3c 38 21 10 38 38 0 3a 0 0 3b 0 16
  //   11 1d 80 10 0 0 0 0 16 1d 10 21 10 14 10 0 12 0 0 13 0 81 38 14 e a2 14 10 38 a3 16 3a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
  //   contents of ALU_LUT (hex, n*v repeats v):
  //   0 1 2 3 4 5 6 7 8 9 a b c d e f 10 11 12 13 14 15 16 17 18 19 1a 1b 1c 1d 1e 1f 20 21 22 23 24 25 26
  //   27 28 29 2a 2b 2c 2d 2e 2f 30 31 32 33 34 35 36 37 38 39 3a 3b 3c 3d 3e 3f 40 41 42 43 44 45 46 47
  //   48 49 4a 4b 4c 4d 4e 4f 50 51 52 53 54 55 56 57 58 59 5a 5b 5c 5d 5e 5f 60 61 62 63 64 65 66 67 68
  //   69 6a 6b 6c 6d 6e 6f 70 71 72 73 74 75 76 77 78 79 7a 7b 7c 7d 7e 7f 80 81 82 83 84 85 86 87 88 89
  //   8a 8b 8c 8d 8e 8f 90 91 92 93 94 95 96 97 98 99 9a 9b 9c 9d 9e 9f a0 a1 a2 a3 a4 a5 a6 a7 a8 a9 aa
  //   ab ac ad ae af b0 b1 b2 b3 b4 b5 b6 b7 b8 b9 ba bb bc bd be bf c0 c1 c2 c3 c4 c5 c6 c7 c8 c9 ca cb
  //   cc cd ce cf d0 d1 d2 d3 d4 d5 d6 d7 d8 d9 da db dc dd de df e0 e1 e2 e3 e4 e5 e6 e7 e8 e9 ea eb ec
  //   ed ee ef f0 f1 f2 f3 f4 f5 f6 f7 f8 f9 fa fb fc fd fe ff 1 2 3 4 5 6 7 8 9 a b c d e f 10 11 12 13
  //   14 15 16 17 18 19 1a 1b 1c 1d 1e 1f 20 21 22 23 24 25 26 27 28 29 2a 2b 2c 2d 2e 2f 30 31 32 33 34
  //   35 36 37 38 39 3a 3b 3c 3d 3e 3f 40 41 42 43 44 45 46 47 48 49 4a 4b 4c 4d 4e 4f 50 51 52 53 54 55
  //   56 57 58 59 5a 5b 5c 5d 5e 5f 60 61 62 63 64 65 66 67 68 69 6a 6b 6c 6d 6e 6f 70 71 72 73 74 75 76
  //   77 78 79 7a 7b 7c 7d 7e 7f 80 81 82 83 84 85 86 87 88 89 8a 8b 8c 8d 8e 8f 90 91 92 93 94 95 96 97
  //   98 99 9a 9b 9c 9d 9e 9f a0 a1 a2 a3 a4 a5 a6 a7 a8 a9 aa ab ac ad ae af b0 b1 b2 b3 b4 b5 b6 b7 b8
  //   b9 ba bb bc bd be bf c0 c1 c2 c3 c4 c5 c6 c7 c8 c9 ca cb cc cd ce cf d0 d1 d2 d3 d4 d5 d6 d7 d8 d9
  //   da db dc dd de df e0 e1 e2 e3 e4 e5 e6 e7 e8 e9 ea eb ec ed ee ef f0 f1 f2 f3 f4 f5 f6 f7 f8 f9 fa
  //   fb fc fd fe ff 0 2 3 4 5 6 7 8 9 a b c d e f 10 11 12 13 14 15 16 17 18 19 1a 1b 1c 1d 1e 1f 20 21
  //   22 23 24 25 26 27 28 29 2a 2b 2c 2d 2e 2f 30 31 32 33 34 35 36 37 38 39 3a 3b 3c 3d 3e 3f 40 41 42
  //   43 44 45 46 47 48 49 4a 4b 4c 4d 4e 4f 50 51 52 53 54 55 56 57 58 59 5a 5b 5c 5d 5e 5f 60 61 62 63
  //   64 65 66 67 68 69 6a 6b 6c 6d 6e 6f 70 71 72 73 74 75 76 77 78 79 7a 7b 7c 7d 7e 7f 80 81 82 83 84
  //   85 86 87 88 89 8a 8b 8c 8d 8e 8f 90 91 92 93 94 95 96 97 98 99 9a 9b 9c 9d 9e 9f a0 a1 a2 a3 a4 a5
  //   a6 a7 a8 a9 aa ab ac ad ae af b0 b1 b2 b3 b4 b5 b6 b7 b8 b9 ba bb bc bd be bf c0 c1 c2 c3 c4 c5 c6
  //   c7 c8 c9 ca cb cc cd ce cf d0 d1 d2 d3 d4 d5 d6 d7 d8 d9 da db dc dd de df e0 e1 e2 e3 e4 e5 e6 e7
  //   e8 e9 ea eb ec ed ee ef f0 f1 f2 f3 f4 f5 f6 f7 f8 f9 fa fb fc fd fe ff 0 1 3 4 5 6 7 8 9 a b c d e
  //   f 10 11 12 13 14 15 16 17 18 19 1a 1b 1c 1d 1e 1f 20 21 22 23 24 25 26 27 28 29 2a 2b 2c 2d 2e 2f 30
  //   31 32 33 34 35 36 37 38 39 3a 3b 3c 3d 3e 3f 40 41 42 43 44 45 46 47 48 49 4a 4b 4c 4d 4e 4f 50 51
  //   52 53 54 55 56 57 58 59 5a 5b 5c 5d 5e 5f 60 61 62 63 64 65 66 67 68 69 6a 6b 6c 6d 6e 6f 70 71 72
  //   73 74 75 76 77 78 79 7a 7b 7c 7d 7e 7f 80 81 82 83 84 85 86 87 88 89 8a 8b 8c 8d 8e 8f 90 91 92 93
  //   94 95 96 97 98 99 9a 9b 9c 9d 9e 9f a0 a1 a2 a3 a4 a5 a6 a7 a8 a9 aa ab ac ad ae af b0 b1 b2 b3 b4
  //   b5 b6 b7 b8 b9 ba bb bc bd be bf c0 c1 c2 c3 c4 c5 c6 c7 c8 c9 ca cb cc cd ce cf d0 d1 d2 d3 d4 d5
  //   d6 d7 d8 d9 da db dc dd de df e0 e1 e2 e3 e4 e5 e6 e7 e8 e9 ea eb ec ed ee ef f0 f1 f2 f3 f4 f5 f6
  //   f7 f8 f9 fa fb fc fd fe ff 0 1 2 4 5 6 7 8 9 a b c d e f 10 11 12 13 14 15 16 17 18 19 1a 1b 1c 1d
  //   1e 1f 20 21 22 23 24 25 26 27 28 29 2a 2b 2c 2d 2e 2f 30 31 32 33 34 35 36 37 38 39 3a 3b 3c 3d 3e
  //   3f 40 41 42 43 44 45 46 47 48 49 4a 4b 4c 4d 4e 4f 50 51 52 53 54 55 56 57 58 59 5a 5b 5c 5d 5e 5f
  //   60 61 62 63 64 65 66 67 68 69 6a 6b 6c 6d 6e 6f 70 71 72 73 74 75 76 77 78 79 7a 7b 7c 7d 7e 7f 80
  //   81 82 83 84 85 86 87 88 89 8a 8b 8c 8d 8e 8f 90 91 92 93 94 95 96 97 98 99 9a 9b 9c 9d 9e 9f a0 a1
  //   a2 a3 a4 a5 a6 a7 a8 a9 aa ab ac ad ae af b0 b1 b2 b3 b4 b5 b6 b7 b8 b9 ba bb bc bd be bf c0 c1 c2
  //   c3 c4 c5 c6 c7 c8 c9 ca cb cc cd ce cf d0 d1 d2 d3 d4 d5 d6 d7 d8 d9 da db dc dd de df e0 e1 e2 e3
  //   e4 e5 e6 e7 e8 e9 ea eb ec ed ee ef f0 f1 f2 f3 f4 f5 f6 f7 f8 f9 fa fb fc fd fe ff 0 1 2 3 5 6 7 8
  //   9 a b c d e f 10 11 12 13 14 15 16 17 18 19 1a 1b 1c 1d 1e 1f 20 21 22 23 24 25 26 27 28 29 2a 2b 2c
  //   2d 2e 2f 30 31 32 33 34 35 36 37 38 39 3a 3b 3c 3d 3e 3f 40 41 42 43 44 45 46 47 48 49 4a 4b 4c 4d
  //   4e 4f 50 51 52 53 54 55 56 57 58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
endmodule

module mmu (
  input  [7:0] data_in,
  input  [6:0] key_char,
  input  key_rdy,
  input  [23:0] addr,
  input  store,
  input  clk,
  output key_discard,
  output [6:0] ttydata,
  output ttyclk,
  output [7:0] data_out
);

  wire and_1_out, and_2_out, and_3_out, comparator_1_eq, comparator_1_gt, comparator_1_lt, not_1_out;
  wire [7:0] controlled_buffer_4_out;

  assign data_out = store ? data_in : 8'bz;  // Controlled_Buffer controlled_buffer_1
  Comparator #(.width(24)) comparator_1 (
    .a(24'h1), .b(addr), .gt(comparator_1_gt), .eq(comparator_1_eq), .lt(comparator_1_lt));
  not not_1 (not_1_out, store);
  assign data_out = and_1_out ? {key_rdy, key_char} : 8'bz;  // Controlled_Buffer controlled_buffer_2
  and and_1 (and_1_out, comparator_1_gt, not_1_out);
  assign data_out = and_2_out ? 8'hcc : 8'bz;  // Controlled_Buffer controlled_buffer_3
  and and_2 (and_2_out, comparator_1_eq, not_1_out);
  assign controlled_buffer_4_out = store ? data_out : 8'bz;  // Controlled_Buffer controlled_buffer_4
  RAM #(.addrWidth(24), .Select("high"), .simpleMode("false")) ram_1 (
    .addr(addr), .data(controlled_buffer_4_out), .clk(clk), .ld(not_1_out));  // open: sel, clr
  assign data_out = and_3_out ? controlled_buffer_4_out : 8'bz;  // Controlled_Buffer controlled_buffer_5
  and and_3 (and_3_out, comparator_1_lt, not_1_out);
  and and_4 (key_discard, data_out[7], store, clk, comparator_1_gt);
  and and_5 (ttyclk, comparator_1_eq, store, clk);

  assign ttydata = data_out[6:0];

  // Notes on the sheet:
  //   addr == 1
  //   addr > 1
  //   addr == 0
endmodule

module key_ctrl (
  input  key_avail,
  input  discard,
  output key_clk,
  output key_read_en,
  output rdy
);

  wire and_1_out, and_3_out, and_4_out, clock_1_out, d_ff_1_q, d_ff_2_q, decoder_1_out0, decoder_1_out1,
       decoder_1_out2, decoder_1_out3, decoder_1_out4;
  wire [2:0] counter_1_q;

  Clock clock_1 (.out(clock_1_out));
  Decoder #(.select(3), .disabled(0), .enable("false")) decoder_1 (
    .out0(decoder_1_out0), .out1(decoder_1_out1), .out2(decoder_1_out2), .out3(decoder_1_out3),
    .out4(decoder_1_out4), .sel(counter_1_q));  // open: out5, out6, out7
  Counter #(.width(3), .max('h4), .trigger("falling"), .behavior("old")) counter_1 (
    .Q(counter_1_q), .clk(clock_1_out));  // open: load, D, count, carry, clr, preset
  or or_1 (key_clk, decoder_1_out0, and_1_out);
  and and_1 (and_1_out, decoder_1_out2, d_ff_2_q);
  or or_2 (key_read_en, decoder_1_out1, decoder_1_out2);
  D_Flip_Flop d_ff_1 (.clk(and_1_out), .D(1'b1), .Q(d_ff_1_q), .reset(and_4_out));  // open: Qn, preset
  D_Flip_Flop d_ff_2 (.clk(discard), .D(1'b1), .Q(d_ff_2_q), .reset(and_4_out));  // open: Qn, preset
  and and_2 (rdy, key_avail, ~and_3_out);  // AND_Gate
  and and_3 (and_3_out, d_ff_1_q, decoder_1_out3);
  and and_4 (and_4_out, d_ff_1_q, decoder_1_out4);
endmodule

module regs (
  input  [3:0] D,
  input  [3:0] index,
  input  W,
  input  R,
  input  ADDR_CLK,
  output [3:0] QLO,
  output [3:0] QHI,
  output [3:0] Q,
  output [23:0] extADDR,
  output [7:0] ADDR
);

  wire and_1_out, and_2_out, n74ls156_1__1y0, n74ls156_1__1y1, n74ls156_1__1y2, n74ls156_1__1y3,
       n74ls156_1__2y0, n74ls156_1__2y1, n74ls156_1__2y2, n74ls156_1__2y3, not_1_out;

  _74LS156 u_74ls156_1 (
    .n1G(W), ._1C(1'b1), .SEL({index[3], index[0]}), .n2G(R), ._2C(1'b1), ._1Y0(n74ls156_1__1y0),
    ._1Y1(n74ls156_1__1y1), ._1Y2(n74ls156_1__1y2), ._1Y3(n74ls156_1__1y3), ._2Y0(n74ls156_1__2y0),
    ._2Y1(n74ls156_1__2y1), ._2Y2(n74ls156_1__2y2), ._2Y3(n74ls156_1__2y3));
  and and_1 (and_1_out, n74ls156_1__2y0, n74ls156_1__2y1);
  and and_2 (and_2_out, n74ls156_1__2y2, n74ls156_1__2y3);
  _74LS670 LO1 (.W(index[2:1]), .nGW(n74ls156_1__1y0), .R(index[2:1]), .nGR(and_1_out), .IO(D), .IO_2(QLO));
  _74LS670 HI1 (.W(index[2:1]), .nGW(n74ls156_1__1y1), .R(index[2:1]), .nGR(and_1_out), .IO(D), .IO_2(QHI));
  _74LS670 LO2 (.W(index[2:1]), .nGW(n74ls156_1__1y2), .R(index[2:1]), .nGR(and_2_out), .IO(D), .IO_2(QLO));
  _74LS670 HI2 (.W(index[2:1]), .nGW(n74ls156_1__1y3), .R(index[2:1]), .nGR(and_2_out), .IO(D), .IO_2(QHI));
  Multiplexer #(.width(4)) multiplexer_1 (.in0(QLO), .in1(QHI), .out(D), .sel(index[0]), .en(not_1_out));
  not not_1 (not_1_out, R);
  _74HCT377 u_74hct377_1 (.D({QHI, QLO}), .nEN(n74ls156_1__2y0), .CLK(ADDR_CLK), .Q(extADDR[7:0]));
  _74HCT377 u_74hct377_2 (.D({QHI, QLO}), .nEN(n74ls156_1__2y1), .CLK(ADDR_CLK), .Q(extADDR[15:8]));
  _74HCT377 u_74hct377_3 (.D({QHI, QLO}), .nEN(n74ls156_1__2y2), .CLK(ADDR_CLK), .Q(extADDR[23:16]));
  _74HCT377 u_74hct377_4 (.D({QHI, QLO}), .nEN(n74ls156_1__2y3), .CLK(ADDR_CLK), .Q(ADDR));

  assign Q = D;

  // Notes on the sheet:
  //   W: pull=up
  //   R: pull=up
endmodule

module _74LS670 (
  input  [1:0] W,
  input  nGW,
  input  [1:0] R,
  input  nGR,
  input  [3:0] IO,
  output [3:0] IO_2
);

  wire decoder_1_out0, decoder_1_out1, decoder_1_out2, decoder_1_out3, decoder_2_out0, decoder_2_out1,
       decoder_2_out2, decoder_2_out3, not_1_out;
  wire [3:0] register_1_q, register_2_q, register_3_q, register_4_q;

  not not_1 (not_1_out, nGR);
  Decoder #(.select(2), .disabled(0), .enable("false")) decoder_1 (
    .out0(decoder_1_out0), .out1(decoder_1_out1), .out2(decoder_1_out2), .out3(decoder_1_out3), .sel(W));
  Decoder #(.select(2), .disabled(0)) decoder_2 (
    .out0(decoder_2_out0), .out1(decoder_2_out1), .out2(decoder_2_out2), .out3(decoder_2_out3), .sel(R),
    .en(not_1_out));
  Register #(.width(4), .Select("low")) register_1 (
    .D(IO), .en(decoder_1_out0), .Q(register_1_q), .clk(nGW));  // open: clr
  Register #(.width(4), .Select("low")) register_2 (
    .D(IO), .en(decoder_1_out1), .Q(register_2_q), .clk(nGW));  // open: clr
  Register #(.width(4), .Select("low")) register_3 (
    .D(IO), .en(decoder_1_out2), .Q(register_3_q), .clk(nGW));  // open: clr
  Register #(.width(4), .Select("low")) register_4 (
    .D(IO), .en(decoder_1_out3), .Q(register_4_q), .clk(nGW));  // open: clr
  assign IO = decoder_2_out0 ? register_1_q : 4'bz;  // Controlled_Buffer controlled_buffer_1
  assign IO = decoder_2_out1 ? register_2_q : 4'bz;  // Controlled_Buffer controlled_buffer_2
  assign IO = decoder_2_out2 ? register_3_q : 4'bz;  // Controlled_Buffer controlled_buffer_3
  assign IO = decoder_2_out3 ? register_4_q : 4'bz;  // Controlled_Buffer controlled_buffer_4

  assign IO_2 = IO;
endmodule

module _74LS156 (
  input  n1G,
  input  _1C,
  input  [1:0] SEL,
  input  n2G,
  input  _2C,
  output _1Y0,
  output _1Y1,
  output _1Y2,
  output _1Y3,
  output _2Y0,
  output _2Y1,
  output _2Y2,
  output _2Y3
);

  wire and_1_out, and_2_out, decoder_1_out0, decoder_1_out1, decoder_1_out2, decoder_1_out3, decoder_2_out0,
       decoder_2_out1, decoder_2_out2, decoder_2_out3;

  and and_1 (and_1_out, ~n1G, _1C);  // AND_Gate
  and and_2 (and_2_out, ~n2G, _2C);  // AND_Gate
  Decoder #(.select(2), .disabled(0), .enable("false")) decoder_1 (
    .out0(decoder_1_out0), .out1(decoder_1_out1), .out2(decoder_1_out2), .out3(decoder_1_out3), .sel(SEL));
  Decoder #(.select(2), .disabled(0), .enable("false")) decoder_2 (
    .out0(decoder_2_out0), .out1(decoder_2_out1), .out2(decoder_2_out2), .out3(decoder_2_out3), .sel(SEL));
  Pull_Resistor #(.pull(1)) pull_resistor_1 (.node(_1Y2));
  Pull_Resistor #(.pull(1)) pull_resistor_2 (.node(_1Y1));
  Pull_Resistor #(.pull(1)) pull_resistor_3 (.node(_1Y0));
  assign _1Y0 = and_1_out ? ~decoder_1_out0 : 1'bz;  // Controlled_Inverter controlled_inverter_1
  assign _1Y1 = and_1_out ? ~decoder_1_out1 : 1'bz;  // Controlled_Inverter controlled_inverter_2
  assign _1Y2 = and_1_out ? ~decoder_1_out2 : 1'bz;  // Controlled_Inverter controlled_inverter_3
  Pull_Resistor #(.pull(1)) pull_resistor_4 (.node(_2Y2));
  Pull_Resistor #(.pull(1)) pull_resistor_5 (.node(_2Y1));
  Pull_Resistor #(.pull(1)) pull_resistor_6 (.node(_2Y0));
  assign _2Y0 = and_2_out ? ~decoder_2_out0 : 1'bz;  // Controlled_Inverter controlled_inverter_4
  assign _2Y1 = and_2_out ? ~decoder_2_out1 : 1'bz;  // Controlled_Inverter controlled_inverter_5
  assign _2Y2 = and_2_out ? ~decoder_2_out2 : 1'bz;  // Controlled_Inverter controlled_inverter_6
  Pull_Resistor #(.pull(1)) pull_resistor_7 (.node(_1Y3));
  assign _1Y3 = and_1_out ? ~decoder_1_out3 : 1'bz;  // Controlled_Inverter controlled_inverter_7
  Pull_Resistor #(.pull(1)) pull_resistor_8 (.node(_2Y3));
  assign _2Y3 = and_2_out ? ~decoder_2_out3 : 1'bz;  // Controlled_Inverter controlled_inverter_8
endmodule

module _74HCT377 (
  input  [7:0] D,
  input  nEN,
  input  CLK,
  output [7:0] Q
);

  wire not_1_out;

  not not_1 (not_1_out, nEN);
  Register #(.Select("low")) register_1 (.D(D), .en(not_1_out), .Q(Q), .clk(CLK));  // open: clr
endmodule

module _74HCT299 (
  input  [7:0] IO,
  input  S0,
  input  S1,
  input  CP,
  input  nMR,
  input  nOE1,
  input  nOE2,
  output [7:0] IO_2,
  output [7:0] peek
);

  wire and_1_out, nor_1_out, not_1_out;

  Pull_Resistor #(.pull(1)) pull_resistor_1 (.node(S0));
  Pull_Resistor #(.pull(1)) pull_resistor_2 (.node(S1));
  Pull_Resistor #(.pull(1)) pull_resistor_3 (.node(CP));
  Pull_Resistor #(.pull(1)) pull_resistor_4 (.node(nMR));
  Pull_Resistor #(.pull(1)) pull_resistor_5 (.node(nOE1));
  Pull_Resistor #(.pull(1)) pull_resistor_6 (.node(nOE2));
  and and_1 (and_1_out, S0, S1);
  not not_1 (not_1_out, nMR);
  nor nor_1 (nor_1_out, nOE1, and_1_out, nOE2);
  Register #(.Select("low")) register_1 (.D(IO), .en(and_1_out), .Q(peek), .clk(CP), .clr(not_1_out));
  assign IO_2 = nor_1_out ? peek : 8'bz;  // Controlled_Buffer controlled_buffer_1
endmodule

// 74593
module _74LS593 (
  input  CCK,
  input  CCKEN,
  input  nCCKEN,
  input  nCCLR,
  input  nCLOAD,
  input  [7:0] IO_I,
  input  nRCKEN,
  input  RCK,
  input  G,
  input  nG,
  output [7:0] rpeek,
  output [7:0] IO_O,
  output nRCO,
  output [7:0] peek
);

  wire and_1_out, and_2_out, and_3_out, and_4_out, and_5_out, and_6_out, and_7_out, and_8_out, and_9_out,
       and_10_out, and_11_out, and_12_out, and_13_out, and_14_out, and_15_out, and_16_out, comparator_1_eq,
       not_1_out, not_2_out, or_1_out, or_2_out, or_3_out, or_4_out, or_5_out, or_6_out, or_7_out, or_8_out,
       or_9_out, or_10_out;
  wire [7:0] adder_1_out;

  Pull_Resistor #(.pull(1)) pull_resistor_1 (.node(nCLOAD));
  Pull_Resistor #(.pull(1)) pull_resistor_2 (.node(nRCKEN));
  not not_1 (not_1_out, nRCKEN);
  Pull_Resistor #(.pull(1)) pull_resistor_3 (.node(RCK));
  Register #(.Select("low")) register_1 (.D(IO_I), .en(not_1_out), .Q(rpeek), .clk(RCK));  // open: clr
  Pull_Resistor #(.pull(1)) pull_resistor_4 (.node(CCKEN));
  Pull_Resistor #(.pull(1)) pull_resistor_5 (.node(nCCKEN));
  Pull_Resistor #(.pull(1)) pull_resistor_6 (.node(nCCLR));
  and and_1 (and_1_out, rpeek[0], ~nCLOAD);  // AND_Gate
  and and_2 (and_2_out, ~rpeek[0], ~nCLOAD);  // AND_Gate
  and and_3 (and_3_out, rpeek[1], ~nCLOAD);  // AND_Gate
  and and_4 (and_4_out, ~rpeek[1], ~nCLOAD);  // AND_Gate
  and and_5 (and_5_out, rpeek[2], ~nCLOAD);  // AND_Gate
  and and_6 (and_6_out, ~rpeek[2], ~nCLOAD);  // AND_Gate
  and and_7 (and_7_out, rpeek[3], ~nCLOAD);  // AND_Gate
  and and_8 (and_8_out, ~rpeek[3], ~nCLOAD);  // AND_Gate
  and and_9 (and_9_out, rpeek[4], ~nCLOAD);  // AND_Gate
  and and_10 (and_10_out, ~rpeek[4], ~nCLOAD);  // AND_Gate
  and and_11 (and_11_out, rpeek[5], ~nCLOAD);  // AND_Gate
  and and_12 (and_12_out, ~rpeek[5], ~nCLOAD);  // AND_Gate
  and and_13 (and_13_out, rpeek[6], ~nCLOAD);  // AND_Gate
  and and_14 (and_14_out, ~rpeek[6], ~nCLOAD);  // AND_Gate
  and and_15 (and_15_out, rpeek[7], ~nCLOAD);  // AND_Gate
  and and_16 (and_16_out, ~rpeek[7], ~nCLOAD);  // AND_Gate
  Pull_Resistor #(.pull(1)) pull_resistor_7 (.node(CCK));
  or or_1 (or_1_out, CCKEN, ~nCCKEN);  // OR_Gate
  not not_2 (not_2_out, nCCLR);
  or or_2 (or_2_out, and_2_out, not_2_out);
  or or_3 (or_3_out, and_4_out, not_2_out);
  or or_4 (or_4_out, and_6_out, not_2_out);
  or or_5 (or_5_out, and_8_out, not_2_out);
  or or_6 (or_6_out, and_10_out, not_2_out);
  or or_7 (or_7_out, and_12_out, not_2_out);
  or or_8 (or_8_out, and_14_out, not_2_out);
  or or_9 (or_9_out, and_16_out, not_2_out);
  Register #(.width(1), .Select("low")) register_2 (
    .D(adder_1_out[0]), .en(or_1_out), .Q(peek[0]), .clk(CCK), .clr(or_2_out), .preset(and_1_out));  // open: cs
  Register #(.width(1), .Select("low")) register_3 (
    .D(adder_1_out[1]), .en(or_1_out), .Q(peek[1]), .clk(CCK), .clr(or_3_out), .preset(and_3_out));  // open: cs
  Register #(.width(1), .Select("low")) register_4 (
    .D(adder_1_out[2]), .en(or_1_out), .Q(peek[2]), .clk(CCK), .clr(or_4_out), .preset(and_5_out));  // open: cs
  Register #(.width(1), .Select("low")) register_5 (
    .D(adder_1_out[3]), .en(or_1_out), .Q(peek[3]), .clk(CCK), .clr(or_5_out), .preset(and_7_out));  // open: cs
  Register #(.width(1), .Select("low")) register_6 (
    .D(adder_1_out[4]), .en(or_1_out), .Q(peek[4]), .clk(CCK), .clr(or_6_out), .preset(and_9_out));  // open: cs
  Register #(.width(1), .Select("low")) register_7 (
    .D(adder_1_out[5]), .en(or_1_out), .Q(peek[5]), .clk(CCK), .clr(or_7_out), .preset(and_11_out));  // open: cs
  Register #(.width(1), .Select("low")) register_8 (
    .D(adder_1_out[6]), .en(or_1_out), .Q(peek[6]), .clk(CCK), .clr(or_8_out), .preset(and_13_out));  // open: cs
  Register #(.width(1), .Select("low")) register_9 (
    .D(adder_1_out[7]), .en(or_1_out), .Q(peek[7]), .clk(CCK), .clr(or_9_out), .preset(and_15_out));  // open: cs
  Adder adder_1 (.a(peek), .b(8'h1), .out(adder_1_out));  // open: cin, cout
  Pull_Resistor #(.pull(1)) pull_resistor_8 (.node(G));
  Pull_Resistor #(.pull(1)) pull_resistor_9 (.node(nG));
  assign IO_O = or_10_out ? peek : 8'bz;  // Controlled_Buffer controlled_buffer_1
  or or_10 (or_10_out, G, ~nG);  // OR_Gate
  Comparator comparator_1 (.a(peek), .b({8{1'b1}}), .eq(comparator_1_eq));  // open: gt, lt
  not not_3 (nRCO, comparator_1_eq);

  // Notes on the sheet:
  //   rpeek: pull=up
  //   G: pull=up
  //   nCCLR: pull=up
  //   nRCKEN: pull=up
  //   IO_O: pull=up
  //   RCK: pull=up
  //   nCCKEN: pull=up
  //   CCKEN: pull=up
  //   nG: pull=up
  //   nCLOAD: pull=up
  //   peek: pull=up
  //   CCK: pull=up
endmodule

// 574
module _74HCT574 (
  input  [7:0] D,
  input  CP,
  input  nOE,
  output [7:0] Q,
  output [7:0] Zpeek
);

  wire not_1_out;

  not not_1 (not_1_out, nOE);
  Register #(.Select("low")) register_1 (.D(D), .Q(Zpeek), .clk(CP));  // open: en, clr
  assign Q = not_1_out ? Zpeek : 8'bz;  // Controlled_Buffer controlled_buffer_1
endmodule

// RAM
module AS6C4008 (
  input  [7:0] D,
  input  [18:0] A,
  input  nCE,
  input  nOE,
  input  nWE,
  output [7:0] peek,
  output [7:0] D_2
);

  wire and_1_out, and_2_out, and_3_out, not_1_out, not_2_out;
  wire [7:0] controlled_buffer_1_out;

  not not_1 (not_1_out, nOE);
  and and_1 (and_1_out, nOE, ~nCE, not_2_out);  // AND_Gate
  not not_2 (not_2_out, nWE);
  assign controlled_buffer_1_out = ~and_3_out ? D : 8'bz;  // Controlled_Buffer controlled_buffer_1
  RAM #(.addrWidth(19), .Select("high"), .simpleMode("false")) RAM (
    .addr(A), .data(controlled_buffer_1_out), .sel(1'b1), .clk(and_1_out), .ld(and_2_out), .clr(1'b0));
  and and_2 (and_2_out, not_1_out, ~nCE);  // AND_Gate
  and and_3 (and_3_out, ~nCE, not_1_out);  // AND_Gate
  assign peek = controlled_buffer_1_out;  // Buffer buffer_1, 8 bits wide
  assign D_2 = and_3_out ? controlled_buffer_1_out : 8'bz;  // Controlled_Buffer controlled_buffer_2
endmodule

// 74138
module _74HCT138 (
  input  nE1,
  input  nE2,
  input  E3,
  input  [2:0] A,
  output nY0,
  output nY1,
  output nY2,
  output nY3,
  output nY4,
  output nY5,
  output nY6,
  output nY7
);

  wire and_1_out, decoder_1_out0, decoder_1_out1, decoder_1_out2, decoder_1_out3, decoder_1_out4,
       decoder_1_out5, decoder_1_out6, decoder_1_out7;

  and and_1 (and_1_out, ~nE1, ~nE2, E3);  // AND_Gate
  not not_1 (nY0, decoder_1_out0);
  not not_2 (nY1, decoder_1_out1);
  not not_3 (nY2, decoder_1_out2);
  not not_4 (nY3, decoder_1_out3);
  not not_5 (nY4, decoder_1_out4);
  not not_6 (nY5, decoder_1_out5);
  not not_7 (nY6, decoder_1_out6);
  not not_8 (nY7, decoder_1_out7);
  Decoder #(.select(3), .disabled(0)) decoder_1 (
    .out0(decoder_1_out0), .out1(decoder_1_out1), .out2(decoder_1_out2), .out3(decoder_1_out3),
    .out4(decoder_1_out4), .out5(decoder_1_out5), .out6(decoder_1_out6), .out7(decoder_1_out7), .sel(A),
    .en(and_1_out));
endmodule

// 74238
module _74HCT238 (
  input  nE1,
  input  nE2,
  input  E3,
  input  [2:0] A,
  output nY0,
  output nY1,
  output nY2,
  output nY3,
  output nY4,
  output nY5,
  output nY6,
  output nY7
);

  wire and_1_out;

  and and_1 (and_1_out, ~nE1, ~nE2, E3);  // AND_Gate
  Decoder #(.select(3), .disabled(0)) decoder_1 (
    .out0(nY0), .out1(nY1), .out2(nY2), .out3(nY3), .out4(nY4), .out5(nY5), .out6(nY6), .out7(nY7), .sel(A),
    .en(and_1_out));
endmodule

// 299
module _74HCT299_simplified (
  input  [7:0] IO,
  input  nOE,
  input  CP,
  output [7:0] IO_2,
  output [7:0] peek
);

  Pull_Resistor #(.pull(1)) pull_resistor_1 (.node(nOE));
  _74HCT299 u_74hct299_1 (
    .IO(IO), .S0(nOE), .S1(nOE), .CP(CP), .nMR(1'b1), .nOE1(nOE), .nOE2(nOE), .IO_2(IO_2), .peek(peek));
endmodule

module SST39SF040 (
  input  [7:0] ROM_D,
  input  nCE,
  input  nOE,
  output [7:0] DQ
);

  wire and_1_out;

  and and_1 (and_1_out, ~nCE, ~nOE);  // AND_Gate
  assign DQ = and_1_out ? ROM_D : 8'bz;  // Controlled_Buffer controlled_buffer_1
endmodule

module _74HCT161 (
  input  SPE__nPE,
  input  [3:0] P,
  input  CP,
  input  PE_CEP,
  input  TE_CET,
  input  nMR,
  output [3:0] Q,
  output TC
);

  wire and_1_out, and_2_out, counter_1_carry, not_1_out, not_2_out, or_1_out;

  not not_1 (not_1_out, SPE__nPE);
  Pull_Resistor #(.pull(1)) pull_resistor_1 (.node(SPE__nPE));
  Pull_Resistor #(.pull(1)) pull_resistor_2 (.node(nMR));
  not not_2 (not_2_out, nMR);
  and and_1 (and_1_out, PE_CEP, TE_CET);
  or or_1 (or_1_out, and_1_out, not_1_out);
  and and_2 (and_2_out, ~not_2_out, or_1_out);  // AND_Gate
  Counter #(.width(4), .max('hf)) counter_1 (
    .load(not_1_out), .D(P), .count(and_2_out), .Q(Q), .carry(counter_1_carry), .clk(CP), .clr(not_2_out));  // open: preset, down
  and and_3 (TC, counter_1_carry, TE_CET);
endmodule
