// Digital circuit lutcomp.dig as structural Verilog
module lutcomp (
  input  RESET,
  input  clk,
  output HALT
);

  wire and_2_out, CLK_t, CLK_t_t, decoder_1_out_0, decoder_1_out_1, decoder_1_out_2, decoder_1_out_3,
       decoder_1_out_4, decoder_1_out_5, decoder_1_out_6, decoder_1_out_7, io_1_key_clk, io_1_term_clk,
       keyboard_1_av, not_1_out, not_3_out, switch_1_b, uc_1_a0_cp, uc_1_a1_cp, uc_1_a2_cp, uc_1_addr_oe,
       uc_1_alu_cp, uc_1_alu_oe, uc_1_in1_cp, uc_1_mem_cp, uc_1_mem_oe, uc_1_pc_inc, uc_1_pc_spe,
       uc_1_ttyin_cp, uc_1_ttyin_oe, uc_1_ttyout_cp, uc_1_w_cp, uc_1_w_oe, uc_1_x_cp, uc_1_x_oe, uc_1_y_cp,
       uc_1_y_oe, uc_1_z_cp, uc_1_z_oe;
  wire [1:0] io_1_in_source, uc_1_stage;
  wire [2:0] uc_1_alu_op;
  wire [3:0] uc_1_uaddr_3;
  wire [6:0] uc_1_uaddr;
  wire [7:0] counter_3_out, io_1_in_value, uc_1_data, uc_1_uaddr_2, uc_1_udata, uc_1_uir0, uc_1_uir1,
       uc_1_upc;
  wire [15:0] counter_2_out, keyboard_1_d;
  wire [23:0] pc_1_pc, undriven;
  wire [63:0] counter_1_out;

  and and_1 (CLK_t, clk, HALT);
  Stop stop_1 (.stop(~HALT));
  not not_1 (not_1_out, HALT);
  Break #(.Cycles(1000000000)) break_1 (.brk(not_1_out));
  not not_2 (CLK_t_t, CLK_t);
  // Probe TickCount on counter_1_out
  Counter #(.Bits(64)) counter_1 (.en(1'b1), .C(CLK_t), .clr(1'b0), .out(counter_1_out));  // open: ovf
  uc uc_1 (
    .CLK(CLK_t_t), .RESET(RESET), .DATA(uc_1_data), .ADDR_OE(uc_1_addr_oe), .ALU_OP(uc_1_alu_op),
    .PC_INC(uc_1_pc_inc), .IN1_CP(uc_1_in1_cp), .ALU_CP(uc_1_alu_cp), .MEM_CP(uc_1_mem_cp),
    .TTYIN_CP(uc_1_ttyin_cp), .W_CP(uc_1_w_cp), .X_CP(uc_1_x_cp), .Y_CP(uc_1_y_cp), .Z_CP(uc_1_z_cp),
    .A0_CP(uc_1_a0_cp), .A1_CP(uc_1_a1_cp), .A2_CP(uc_1_a2_cp), .TTYOUT_CP(uc_1_ttyout_cp), .HALT(HALT),
    .ALU_OE(uc_1_alu_oe), .MEM_OE(uc_1_mem_oe), .TTYIN_OE(uc_1_ttyin_oe), .PC_SPE(uc_1_pc_spe),
    .W_OE(uc_1_w_oe), .X_OE(uc_1_x_oe), .Y_OE(uc_1_y_oe), .Z_OE(uc_1_z_oe), .uIR0(uc_1_uir0),
    .uIR1(uc_1_uir1), .uAddr({uc_1_uaddr_3, uc_1_uaddr_2, uc_1_uaddr}), .uPC(uc_1_upc), .stage(uc_1_stage),
    .uData(uc_1_udata));
  not not_3 (not_3_out, uc_1_addr_oe);
  // Probe on uc_1_uir0
  // Probe on uc_1_uir1
  // Probe on uc_1_upc
  // Probe on uc_1_stage
  // Probe on uc_1_udata
  and and_2 (and_2_out, uc_1_pc_inc, ~uc_1_pc_spe);  // And
  Switch switch_1 (.A(uc_1_pc_inc), .B(switch_1_b));
  pc pc_1 (.PC_INC(uc_1_pc_inc), .RESET(RESET), .PC_SPE(uc_1_pc_spe), .OE(not_3_out), .ADDR(undriven), .PC(pc_1_pc));
  // Probe $uPC on {uc_1_uaddr_3, uc_1_uaddr_2, uc_1_uaddr}
  // Probe on uc_1_uaddr
  // Probe $IR0 on uc_1_uaddr_2
  // Probe $FLAGS on uc_1_uaddr_3
  Counter #(.Bits(16)) counter_2 (.en(1'b1), .C(uc_1_pc_inc), .clr(1'b0), .out(counter_2_out));  // open: ovf
  Break #(.Cycles(10000000)) break_2 (.brk(switch_1_b));
  PullDown pulldown_1 (.out(switch_1_b));
  Counter #(.Bits(8)) counter_3 (.en(1'b1), .C(and_2_out), .clr(1'b0), .out(counter_3_out));  // open: ovf
  // Probe PC on pc_1_pc
  io io_1 (
    .DATA(uc_1_data), .TTYIN_CP(uc_1_ttyin_cp), .TTYIN_OE(uc_1_ttyin_oe), .TTYOUT_CP(uc_1_ttyout_cp),
    .KEY_D(keyboard_1_d), .KEY_AV(keyboard_1_av), .TERM_CLK(io_1_term_clk), .KEY_CLK(io_1_key_clk),
    .IN_SOURCE(io_1_in_source), .IN_VALUE(io_1_in_value));
  RAMDualPort #(.AddrBits(16), .Bits(24)) PC_LOG (
    .A(counter_2_out), .Din(pc_1_pc), .str(1'b1), .C(uc_1_pc_inc), .ld(1'b0));  // open: D
  RAMDualPort #(.AddrBits(8), .Bits(24)) JMP_LOG (
    .A(counter_3_out), .Din(pc_1_pc), .str(1'b1), .C(and_2_out), .ld(1'b0));  // open: D
  Keyboard keyboard_1 (.C(io_1_key_clk), .en(1'b1), .D(keyboard_1_d), .av(keyboard_1_av));
  Terminal terminal_1 (.D(uc_1_data), .C(io_1_term_clk), .en(1'b1));
  memory memory_1 (
    .MEM_CP(uc_1_mem_cp), .ADDR_OE(uc_1_addr_oe), .A0_CP(uc_1_a0_cp), .A1_CP(uc_1_a1_cp), .A2_CP(uc_1_a2_cp),
    .MEM_OE(uc_1_mem_oe), .DATA(uc_1_data), .ADDR(undriven));
  \reg  W (.OE(uc_1_w_oe), .CP(uc_1_w_cp), .DATA(uc_1_data));  // open: IO
  \reg  X (.OE(uc_1_x_oe), .CP(uc_1_x_cp), .DATA(uc_1_data));  // open: IO
  \reg  Y (.OE(uc_1_y_oe), .CP(uc_1_y_cp), .DATA(uc_1_data));  // open: IO
  \reg  Z (.OE(uc_1_z_oe), .CP(uc_1_z_cp), .DATA(uc_1_data));  // open: IO
  // Probe on io_1_in_source
  // Probe on io_1_in_value
  // Probe ADDR on undriven
  // Probe DATA on uc_1_data
  Decoder #(.Selector_Bits(3)) decoder_1 (
    .sel(uc_1_alu_op), .out_0(decoder_1_out_0), .out_1(decoder_1_out_1), .out_2(decoder_1_out_2),
    .out_3(decoder_1_out_3), .out_4(decoder_1_out_4), .out_5(decoder_1_out_5), .out_6(decoder_1_out_6),
    .out_7(decoder_1_out_7));
  alu alu_1 (
    .ALU_OP(uc_1_alu_op), .ALU_OE(uc_1_alu_oe), .ALU_CP(uc_1_alu_cp), .IN1_CP(uc_1_in1_cp), .DATA(uc_1_data));  // open: IN1, ALU_REG, ALU_RESULT
  // Probe AddLo on decoder_1_out_0
  // Probe AddHiNC on decoder_1_out_2
  // Probe Or on decoder_1_out_4
  // Probe And on decoder_1_out_6
  // Probe MulHi on decoder_1_out_1
  // Probe AddHiC on decoder_1_out_3
  // Probe Div on decoder_1_out_5
  // Probe Special on decoder_1_out_7

  // Notes on the sheet:
  //   RESET: default 1
  //   clk: Hz: 1000000
  //   4A
  //   4B
  //   4Y
  //   6A
  //   6Y
  //   3A
  //   3Y
endmodule

/* Test case:
RESET_ HALT
0      1
*/
