// Logisim project lutcomp_ev.circ as structural Verilog: 16 circuits, main circuit main
// 10
module main (
  input  RESET,
  output halt
);

  wire A0_CP, A1_CP, A2_CP, ADDR_OE_9c665616, ALU_CP, ALU_OE_ef57a1f8, and_1_out, and_3_out, CLK,
       CLK_d7055d95, clock_1_out, FLAGS_CP, HALT_f88f21d2, IMM_OE_044a29d3, IN1_CP, IR0_CP,
       key_ctrl_1_key_clk, key_ctrl_1_key_read_en, keyboard_1_avail, l_74hct138_ff2bfe81_1_y0_36f069fd,
       l_74hct161_263709e2_1_tc, l_74hct238_2e8277f3_1_y0_36f069fd, l_74hct238_2e8277f3_1_y1_bf899b0a,
       l_74hct238_2e8277f3_1_y2_4c64a680, l_74hct238_2e8277f3_1_y3_0d3b75c7, MEM_CP, MEM_OE_af581b0c,
       not_3_out, not_4_out, not_6_out, not_7_out, not_8_out, not_9_out, PC0_tc, PC1_tc, PC3_tc, PC4_tc,
       PC_INC, PC_SPE_e3ae0a14, RESET_df644a32, TTYIN_CP, TTYIN_OE_9c2f62ee, TTYOUT_CP, uPC0_tc, W_CP,
       W_OE_698a1e7c, X_CP, X_OE_a5699d28, Y_CP, Y_OE_ddd7bf0b, Z_CP, Z_OE_07b1abca;
  wire [2:0] ALU_OP;
  wire [3:0] l_74hct161_263709e2_1_q, PC0_q, PC1_q, PC3_q, PC4_q, PC5_q, uIR0_q, uIR1_q, uIR1_q_2, uPC0_q,
       uPC1_q;
  wire [6:0] keyboard_1_data;
  wire [7:0] ALU_LUT_27d44971_data, as6c4008_1_peek, bit_extender_1_out, controlled_buffer_3_out, DATA,
       IN1_q, IR0_q, l_74hct299_simplified_1381c5be_1_peek, l_74hct574_611e6db7_1_q,
       l_74hct574_611e6db7_2_zpeek, rom_1_data, TTYOUT_q, uROM_data, W_peek, X_peek, Y_peek;
  wire [7:7] key_ctrl_1_rdy;
  wire [23:0] ADDR;

  not not_1 (RESET_df644a32, RESET);
  Clock clock_1 (.out(clock_1_out));
  not not_2 (halt, HALT_f88f21d2);
  not not_3 (not_3_out, and_1_out);
  and and_1 (and_1_out, not_4_out, l_74hct238_2e8277f3_1_y1_bf899b0a);
  not not_4 (not_4_out, l_74hct138_ff2bfe81_1_y0_36f069fd);
  and and_2 (CLK, HALT_f88f21d2, clock_1_out);
  and and_3 (and_3_out, RESET_df644a32, not_3_out);
  not not_5 (CLK_d7055d95, CLK);
  L_74HCT161_263709e2 uPC1 (
    .SPE_b95b37ae(1'b1), .CP(CLK_d7055d95), .PE(1'b1), .TE(uPC0_tc), .MR_30eafd07(and_3_out), .Q(uPC1_q));  // open: P, TC
  L_74HCT161_263709e2 uPC0 (
    .SPE_b95b37ae(1'b1), .CP(CLK_d7055d95), .PE(1'b1), .TE(1'b1), .MR_30eafd07(and_3_out), .Q(uPC0_q),
    .TC(uPC0_tc));  // open: P
  L_74HCT574_611e6db7 l_74hct574_611e6db7_1 (
    .Q(l_74hct574_611e6db7_1_q), .CP(FLAGS_CP), .OE_83629f7f(1'b0), .D(DATA));  // open: Zpeek
  L_74HCT574_611e6db7 IR0 (.Q(IR0_q), .CP(IR0_CP), .OE_83629f7f(1'b0), .D(DATA));  // open: Zpeek
  // Probe on {l_74hct574_611e6db7_1_q[3:0], IR0_q, uPC1_q, uPC0_q[3:1]}
  // Probe on uPC0_q[1:0]
  // Probe on {uPC1_q, uPC0_q[3:1]}
  // Probe on IR0_q
  // Probe on l_74hct574_611e6db7_1_q[3:0]
  L_74HCT238_2e8277f3 l_74hct238_2e8277f3_1 (
    .E1_8073e2cf(1'b0), .E2_3ccbccd8(CLK_d7055d95), .E3(1'b1), .A({1'b0, uPC0_q[1:0]}),
    .Y0_36f069fd(l_74hct238_2e8277f3_1_y0_36f069fd), .Y1_bf899b0a(l_74hct238_2e8277f3_1_y1_bf899b0a),
    .Y2_4c64a680(l_74hct238_2e8277f3_1_y2_4c64a680), .Y3_0d3b75c7(l_74hct238_2e8277f3_1_y3_0d3b75c7));  // open: Y4_fc72c967, Y5_164c4e51, Y6_decf6708, Y7_23027958
  ROM #(.addrWidth(19)) uROM (.addr({l_74hct574_611e6db7_1_q[3:0], IR0_q, uPC1_q, uPC0_q[3:1]}), .data(uROM_data));
  // Probe on l_74hct574_611e6db7_1_q[0]
  // Probe on l_74hct574_611e6db7_1_q[2]
  // Probe on l_74hct574_611e6db7_1_q[1]
  L_74HCT161_263709e2 PC0 (
    .SPE_b95b37ae(PC_SPE_e3ae0a14), .P(ADDR[3:0]), .CP(PC_INC), .PE(1'b1), .TE(1'b1),
    .MR_30eafd07(RESET_df644a32), .Q(PC0_q), .TC(PC0_tc));
  L_74HCT161_263709e2 PC1 (
    .SPE_b95b37ae(PC_SPE_e3ae0a14), .P(ADDR[7:4]), .CP(PC_INC), .PE(1'b1), .TE(PC0_tc),
    .MR_30eafd07(RESET_df644a32), .Q(PC1_q), .TC(PC1_tc));
  L_74HCT161_263709e2 l_74hct161_263709e2_1 (
    .SPE_b95b37ae(PC_SPE_e3ae0a14), .P(ADDR[11:8]), .CP(PC_INC), .PE(1'b1), .TE(PC1_tc),
    .MR_30eafd07(RESET_df644a32), .Q(l_74hct161_263709e2_1_q), .TC(l_74hct161_263709e2_1_tc));
  L_74HCT161_263709e2 PC3 (
    .SPE_b95b37ae(PC_SPE_e3ae0a14), .P(ADDR[15:12]), .CP(PC_INC), .PE(1'b1), .TE(l_74hct161_263709e2_1_tc),
    .MR_30eafd07(RESET_df644a32), .Q(PC3_q), .TC(PC3_tc));
  L_74HCT161_263709e2 PC4 (
    .SPE_b95b37ae(PC_SPE_e3ae0a14), .P(ADDR[19:16]), .CP(PC_INC), .PE(1'b1), .TE(PC3_tc),
    .MR_30eafd07(RESET_df644a32), .Q(PC4_q), .TC(PC4_tc));
  L_74HCT161_263709e2 PC5 (
    .SPE_b95b37ae(PC_SPE_e3ae0a14), .P(ADDR[23:20]), .CP(PC_INC), .PE(1'b1), .TE(PC4_tc),
    .MR_30eafd07(RESET_df644a32), .Q(PC5_q));  // open: TC
  assign bit_extender_1_out = {{4{uIR1_q_2[3]}}, uIR1_q_2};  // Bit_Extender bit_extender_1
  assign DATA = IMM_OE_044a29d3 ? bit_extender_1_out : 8'bz;  // Controlled_Buffer controlled_buffer_1
  // Probe on bit_extender_1_out
  L_74HCT574_611e6db7 uIR1 (
    .Q({uIR1_q_2, uIR1_q}), .CP(l_74hct238_2e8277f3_1_y2_4c64a680), .OE_83629f7f(1'b0), .D(uROM_data));  // open: Zpeek
  L_74HCT574_611e6db7 uIR0 (
    .Q({ADDR_OE_9c665616, ALU_OP, uIR0_q}), .CP(l_74hct238_2e8277f3_1_y0_36f069fd), .OE_83629f7f(1'b0),
    .D(uROM_data));  // open: Zpeek
  // Probe on {uIR1_q_2, uIR1_q}
  // Probe on {ADDR_OE_9c665616, ALU_OP, uIR0_q}
  not not_6 (not_6_out, l_74hct238_2e8277f3_1_y3_0d3b75c7);
  // Probe on PC0_q
  // Probe on PC1_q
  // Probe on l_74hct161_263709e2_1_q
  // Probe on PC3_q
  // Probe on PC4_q
  not not_7 (not_7_out, ADDR_OE_9c665616);
  // Probe on PC5_q
  // Probe on {PC5_q, PC4_q, PC3_q, l_74hct161_263709e2_1_q, PC1_q, PC0_q}
  assign ADDR = not_7_out ? {PC5_q, PC4_q, PC3_q, l_74hct161_263709e2_1_q, PC1_q, PC0_q} : 24'bz;  // Controlled_Buffer controlled_buffer_2
  L_74HCT238_2e8277f3 l_74hct238_2e8277f3_2 (
    .E1_8073e2cf(not_6_out), .E2_3ccbccd8(uIR1_q[3]), .E3(1'b1), .A(uIR1_q[2:0]), .Y0_36f069fd(PC_INC),
    .Y1_bf899b0a(IR0_CP), .Y2_4c64a680(IN1_CP), .Y3_0d3b75c7(ALU_CP), .Y4_fc72c967(MEM_CP),
    .Y5_164c4e51(TTYIN_CP), .Y7_23027958(FLAGS_CP));  // open: Y6_decf6708
  L_74HCT238_2e8277f3 l_74hct238_2e8277f3_3 (
    .E1_8073e2cf(1'b0), .E2_3ccbccd8(not_6_out), .E3(uIR1_q[3]), .A(uIR1_q[2:0]), .Y0_36f069fd(W_CP),
    .Y1_bf899b0a(X_CP), .Y2_4c64a680(Y_CP), .Y3_0d3b75c7(Z_CP), .Y4_fc72c967(A0_CP), .Y5_164c4e51(A1_CP),
    .Y6_decf6708(A2_CP), .Y7_23027958(TTYOUT_CP));
  L_74HCT138_ff2bfe81 l_74hct138_ff2bfe81_1 (
    .Y0_36f069fd(l_74hct138_ff2bfe81_1_y0_36f069fd), .Y1_bf899b0a(HALT_f88f21d2),
    .Y2_4c64a680(IMM_OE_044a29d3), .Y3_0d3b75c7(ALU_OE_ef57a1f8), .Y4_fc72c967(MEM_OE_af581b0c),
    .Y5_164c4e51(TTYIN_OE_9c2f62ee), .Y6_decf6708(PC_SPE_e3ae0a14), .E1_8073e2cf(1'b0),
    .E2_3ccbccd8(uIR0_q[3]), .E3(RESET_df644a32), .A(uIR0_q[2:0]));  // open: Y7_23027958
  L_74HCT138_ff2bfe81 l_74hct138_ff2bfe81_2 (
    .Y0_36f069fd(W_OE_698a1e7c), .Y1_bf899b0a(X_OE_a5699d28), .Y2_4c64a680(Y_OE_ddd7bf0b),
    .Y3_0d3b75c7(Z_OE_07b1abca), .E1_8073e2cf(1'b0), .E2_3ccbccd8(1'b0), .E3(uIR0_q[3]), .A(uIR0_q[2:0]));  // open: Y4_fc72c967, Y5_164c4e51, Y6_decf6708, Y7_23027958
  L_74HCT574_611e6db7 ADDR0 (.Q(ADDR[7:0]), .CP(A0_CP), .OE_83629f7f(ADDR_OE_9c665616), .D(DATA));  // open: Zpeek
  L_74HCT574_611e6db7 ADDR1 (.Q(ADDR[15:8]), .CP(A1_CP), .OE_83629f7f(ADDR_OE_9c665616), .D(DATA));  // open: Zpeek
  L_74HCT574_611e6db7 ADDR2 (.Q(ADDR[23:16]), .CP(A2_CP), .OE_83629f7f(ADDR_OE_9c665616), .D(DATA));  // open: Zpeek
  L_74HCT299_simplified_1381c5be W (.Q(DATA), .peek(W_peek), .L_OE_25175598(W_OE_698a1e7c), .CP(W_CP), .D(DATA));
  L_74HCT299_simplified_1381c5be X (.Q(DATA), .peek(X_peek), .L_OE_25175598(X_OE_a5699d28), .CP(X_CP), .D(DATA));
  L_74HCT299_simplified_1381c5be Y (.Q(DATA), .peek(Y_peek), .L_OE_25175598(Y_OE_ddd7bf0b), .CP(Y_CP), .D(DATA));
  L_74HCT299_simplified_1381c5be l_74hct299_simplified_1381c5be_1 (
    .Q(DATA), .peek(l_74hct299_simplified_1381c5be_1_peek), .L_OE_25175598(Z_OE_07b1abca), .CP(Z_CP), .D(DATA));
  ROM #(.addrWidth(19)) rom_1 (.addr(ADDR[18:0]), .data(rom_1_data));
  not not_8 (not_8_out, MEM_CP);
  not not_9 (not_9_out, ADDR[19]);
  // Probe on ADDR
  // Probe on W_peek
  // Probe on X_peek
  // Probe on Y_peek
  // Probe on l_74hct299_simplified_1381c5be_1_peek
  AS6C4008 as6c4008_1 (
    .A(ADDR[18:0]), .D(DATA), .CE_0dd5e992(not_9_out), .OE_83629f7f(MEM_OE_af581b0c),
    .WE_09c3d0b5(not_8_out), .peek(as6c4008_1_peek), .Q(DATA));
  SST39SF040 sst39sf040_1 (.ROM_D(rom_1_data), .CE_0dd5e992(ADDR[19]), .OE_83629f7f(MEM_OE_af581b0c), .DQ(DATA));
  // Probe on as6c4008_1_peek
  // Probe on rom_1_data
  // Probe on DATA
  L_74HCT574_611e6db7 IN1 (.Q(IN1_q), .CP(IN1_CP), .OE_83629f7f(1'b0), .D(DATA));  // open: Zpeek
  assign controlled_buffer_3_out = TTYIN_CP ? DATA : 8'bz;  // Controlled_Buffer controlled_buffer_3
  Keyboard keyboard_1 (
    .clk(key_ctrl_1_key_clk), .re(key_ctrl_1_key_read_en), .avail(keyboard_1_avail), .data(keyboard_1_data));  // open: clr
  ROM #(.addrWidth(19)) ALU_LUT_27d44971 (.addr({ALU_OP, IN1_q, DATA}), .data(ALU_LUT_27d44971_data));
  TTY #(.trigger("falling")) tty_1 (.data(DATA[6:0]), .clk(TTYOUT_CP));  // open: we, clr
  Pull_Resistor pull_resistor_1 (.node(controlled_buffer_3_out[7]));
  L_74HCT574_611e6db7 TTYOUT (.Q(TTYOUT_q), .CP(TTYOUT_CP), .OE_83629f7f(1'b0), .D(DATA));  // open: Zpeek
  key_ctrl key_ctrl_1 (
    .key_avail(keyboard_1_avail), .discard(controlled_buffer_3_out[7]), .key_clk(key_ctrl_1_key_clk),
    .key_read_en(key_ctrl_1_key_read_en), .rdy(key_ctrl_1_rdy[7]));
  // Probe on TTYOUT_q
  assign DATA = TTYIN_OE_9c2f62ee ? {key_ctrl_1_rdy[7], keyboard_1_data} : 8'bz;  // Controlled_Buffer controlled_buffer_4
  L_74HCT574_611e6db7 l_74hct574_611e6db7_2 (
    .Q(DATA), .Zpeek(l_74hct574_611e6db7_2_zpeek), .CP(ALU_CP), .OE_83629f7f(ALU_OE_ef57a1f8),
    .D(ALU_LUT_27d44971_data));
  // Probe on l_74hct574_611e6db7_2_zpeek

  // Notes on the sheet:
  //   LOGISIM TEST
  //   Arduino3
  //   Arudino2
  //   REAL
  //   1A
  //   1B
  //   1Y
  //   1A
  //   2Y
  //   2B
  //   2A
  //   2Y
  //   2A
  //   4A
  //   4Y
  //   4B
  //   1Y
  //   6Y
  //   6A
  //   Arduino4
  //   [UPSIDE DOWN]
  //   contents of uROM (hex, n*v repeats v):
  //   84 1 82 8e 82 d 88 0 84 c 88 0 84 8 8 4 88 0 80 8 108*1 84 1 88 0 84 c 88 0 84 d 88 0 84 e 6 0 80 8
  //   110*1 84 1 88 0 88 0 88 0 88 0 80 8 116*1 84 1 82 8e 82 d 88 0 84 c 4 2 f2 73 3 4 83 2 a2 3 83 2 e2
  //   23 83 2 c2 3 83 7 88 0 80 8 94*1 84 1 82 8e 82 d 88 0 84 c 4 2 f2 73 83 2 82 13 3 4 83 2 a2 3 83 2
  //   e2 23 83 2 c2 3 83 7 88 0 80 8 90*1 84 1 82 8e 82 d 88 0 84 2 84 c 4 8 82 13 83 2 83 c 4 9 82 13 83
  //   2 83 c 4 a 88 c 89 d 8a e 6 0 80 8 88*1 84 1 88 0 88 0 88 0 88 0 80 8 116*1 84 1 82 8e 82 d 88 0 84
  //   2 84 c 4 8 82 13 83 2 83 c 4 9 82 13 83 2 83 c 4 a 88 c 89 d 8a e 88 2 4 8 82 13 83 2 83 c 4 9 82 13
  //   83 2 83 c 4 a 88 c 89 d 8a e 6 0 80 8 62*1 84 1 1 1 88 0 80 8 120*1 84 1 1 1 88 0 80 8 120*1 84 1 1
  //   1 88 0 80 8 120*1 84 1 1 1 88 0 80 8 120*1 84 1 1 1 88 0 80 8 120*1 84 1 1 1 88 0 80 8 120*1 84 1 1
  //   1 88 0 80 8 120*1 84 1 82 8e 82 d 88 0 84 c 4 8 88 0 84 c 8 4 88 0 80 8 106*1 84 1 82 8e 82 d 88 0
  //   84 c 4 8 84 2 82 13 83 c 4 9 84 2 82 23 83 c 4 a 88 c 89 d 8a e 4 8 82 8e 82 d 88 0 84 c 8 4 88 0 80
  //   8 78*1 84 1 82 8e 82 d 88 0 84 c 4 b 88 0 84 c 4 8 84 2 82 13 83 c 4 9 84 2 82 23 83 c 4 a 88 c 89 d
  //   8a e b 4 88 0 80 8 82*1 84 1 82 8e 82 d 88 0 84 c 5 4 4 5 88 0 80 8 110*1 84 1 82 8e 82 d 88 0 84 c
  //   4 f 88 0 80 8 112*1 84 1 82 8e 82 d 82 2 f2 73 83 2 82 cc 4 3 83 8 24 3 83 7 8 4 82 dc 4 3 83 9 24 3
  //   83 7 9 4 82 ec 4 3 83 a 24 3 83 7 a 4 82 fc 4 3 83 b b 4 88 0 84 c 4 b 88 c 89 d 8a e b 4 88 0 80 8
  //   54*1 84 1 82 8e 82 d 82 cc 4 8 82 dc 4 9 82 ec 4 a 88 c 89 d 8a e 4 b 88 0 82 8e 82 d 84 c b 4 82 cc
  //   4 2 82 13 83 8 a2 13 83 7 8 4 82 dc 4 2 82 3 83 9 a2 3 83 7 9 4 82 ec 4 2 82 3 83 a a2 3 83 7 a 4 88
  //   0 80 8 46*1 84 1 1 1 88 0 80 8 120*1 84 1 1 1 88 0 80 8 120*1 84 1 1 1 88 0 80 8 120*1 84 1 1 1 88 0
  //   80 8 120*1 84 1 1 1 88 0 80 8 120*1 84 1 1 1 88 0 80 8 120*1 84 1 1 1 88 0 80 8 120*1 84 1 1 1 88 0
  //   80 8 120*1 84 1 1 1 88 0 80 8 120*1 84 1 1 1 88 0 80 8 120*1 84 1 82 8e 82 d 88 0 84 c 4 8 82 9 88 0
  //   84 c 4 a 82 1c 2 4 82 c 2 4 88 0 80 8 96*1 84 1 8a 2 a2 3 83 7 82 7 82 7 82 c 8a 2 f2 3 83 b 88 2 eb
  //   3 83 2 24 3 83 7 4 3 3 4 82 1c 89 2 eb 3 83 2 4 3 3 4 82 42 f2 33 83 2 c2 13 83 b 89 2 fb 3 83 9 88
  //   2 fb 3 83 8 82 12 f2 73 83 b 89 2 eb 3 83 9 88 2 e2 13 83 2 c9 3 83 9 88 2 eb 3 83 8 8a 2 f2 23 83 a
  //   80 8 24*1 84 1 82 8e 82 d 88 0 84 c 4 2 88 0 84 c 4 8 88 0 84 c 88 3 3 4 a8 3 83 7 88 0 80 8 94*1 84
  //   1 82 8e 82 d 88 0 84 c 4 2 88 0 84 c 4 8 88 0 84 c 88 3 3 4 a8 3 83 2 e2 23 83 2 c2 3 83 7 88 0 80 8
  //   86*1 84 1 1 1 88 0 80 8 120*1 84 1 1 1 88 0 80 8 120*1 84 1 1 1 88 0 80 8 120*1 84 1 1 1 88 0 80 8
  //   120*1 84 1 1 1 88 0 80 8 120*1 84 1 1 1 88 0 80 8 120*1 84 1 1 1 88 0 80 8 120*1 84 1 1 1 88 0 80 8
  //   120*1 84 1 1 1 88 0 80 8 120*1 84 1 1 1 88 0 80 8 120*1 84 1 1 1 88 0 80 8 120*1 84 1 1 1 88 0 80 8
  //   120*1 84 1 82 8e 82 d 88 0 84 c 4 2 88 0 e4 3 3 4 83 2 a2 3 83 7 88 0 80 8 100*1 84 1 82 8e 82 d 88
  //   0 84 c 4 2 88 0 c4 3 3 4 83 2 a2 3 83 7 88 0 80 8 100*1 84 1 82 8e 82 d 88 0 84 c 4 2 88 0 c4 3 83 8
  //   e4 3 83 2 f2 73 83 2 e8 3 3 4 83 2 a2 3 83 7 88 0 80 8 88*1 84 1 82 8e 82 d 88 0 84 c 4 2 88 0 84 c
  //   64 3 88 0 84 c 3 4 83 2 a2 3 83 7 88 0 80 8 94*1 84 1 82 8e 82 d 88 0 84 c 4 2 88 0 84 c 44 3 88 0
  //   84 c 3 4 83 2 a2 3 83 7 88 0 80 8 94*1 84 1 82 8e 82 d 88 0 84 c 4 8 88 0 84 c 4 9 88 0 84 c 88 2 c9
  //   3 3 4 e9 3 83 2 f2 73 83 2 64 3 3 4 83 2 a2 3 83 7 88 0 80 8 78*1 84 1 1 1 88 0 80 8 120*1 84 1 1 1
  //   88 0 80 8 120*1 84 1 1 1 88 0 80 8 120*1 84 1 1 1 88 0 80 8 120*1 84 1 1 1 88 0 80 8 120*1 84 1 1 1
  //   88 0 80 8 120*1 84 1 1 1 88 0 80 8 120*1 84 1 1 1 88 0 80 8 120*1 84 1 1 1 88 0 80 8 120*1 84 1 1 1
  //   88 0 80 8 120*1 84 1 1 1 88 0 80 8 120*1 84 1 1 1 88 0 80 8 120*1 84 1 1 1 88 0 80 8 120*1 84 1 1 1
  //   88 0 80 8 120*1 84 1 1 1 88 0 80 8 120*1 84 1 1 1 88 0 80 8 120*1 84 1 1 1 88 0 80 8 120*1 84 1 1 1
  //   88 0 80 8 120*1 84 1 1 1 88 0 80 8 120*1 84 1 1 1 88 0 80 8 120*1 84 1 1 1 88 0 80 8 120*1 84 1 1 1
  //   88 0 80 8 120*1 84 1 1 1 88 0 80 8 120*1 84 1 1 1 88 0 80 8 120*1 84 1 1 1 88 0 80 8 120*1 84 1 1 1
  //   88 0 80 8 120*1 84 1 1 1 88 0 80 8 120*1 84 1 1 1 88 0 80 8 120*1 84 1 1 1 88 0 80 8 120*1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
  //   5A
  //   5Y
  //   3A
  //   3Y
  //   6A
  //   contents of rom_1 (hex, n*v repeats v):
  //   0 1 48 13 1 0 1 69 13 1 0 1 21 13 1 0 1 a 13 1 0 1 3e 13 1 0 1 3a 13 1 12 1 f 1 2 30 2 80 2 1e 0 0
  //   30 1 7f 13 1 f 1 2 32 2 71 2 47 0 0 f 1 2 32 2 a 2 14 0 0 1 1e 0 0 ff
  //   5A
  //   5Y
  //   6Y
  //   contents of ALU_LUT_27d44971 (hex, n*v repeats v):
  //   0 1 2 3 4 5 6 7 8 9 a b c d e f 10 11 12 13 14 15 16 17 18 19 1a 1b 1c 1d 1e 1f 20 21 22 23 24 25 26
  //   27 28 29 2a 2b 2c 2d 2e 2f 30 31 32 33 34 35 36 37 38 39 3a 3b 3c 3d 3e 3f 40 41 42 43 44 45 46 47
  //   48 49 4a 4b 4c 4d 4e 4f 50 51 52 53 54 55 56 57 58 59 5a 5b 5c 5d 5e 5f 60 61 62 63 64 65 66 67 68
  //   69 6a 6b 6c 6d 6e 6f 70 71 72 73 74 75 76 77 78 79 7a 7b 7c 7d 7e 7f 80 81 82 83 84 85 86 87 88 89
  //   8a 8b 8c 8d 8e 8f 90 91 92 93 94 95 96 97 98 99 9a 9b 9c 9d 9e 9f a0 a1 a2 a3 a4 a5 a6 a7 a8 a9 aa
  //   ab ac ad ae af b0 b1 b2 b3 b4 b5 b6 b7 b8 b9 ba bb bc bd be bf c0 c1 c2 c3 c4 c5 c6 c7 c8 c9 ca cb
  //   cc cd ce cf d0 d1 d2 d3 d4 d5 d6 d7 d8 d9 da db dc dd de df e0 e1 e2 e3 e4 e5 e6 e7 e8 e9 ea eb ec
  //   ed ee ef f0 f1 f2 f3 f4 f5 f6 f7 f8 f9 fa fb fc fd fe ff 1 2 3 4 5 6 7 8 9 a b c d e f 10 11 12 13
  //   14 15 16 17 18 19 1a 1b 1c 1d 1e 1f 20 21 22 23 24 25 26 27 28 29 2a 2b 2c 2d 2e 2f 30 31 32 33 34
  //   35 36 37 38 39 3a 3b 3c 3d 3e 3f 40 41 42 43 44 45 46 47 48 49 4a 4b 4c 4d 4e 4f 50 51 52 53 54 55
  //   56 57 58 59 5a 5b 5c 5d 5e 5f 60 61 62 63 64 65 66 67 68 69 6a 6b 6c 6d 6e 6f 70 71 72 73 74 75 76
  //   77 78 79 7a 7b 7c 7d 7e 7f 80 81 82 83 84 85 86 87 88 89 8a 8b 8c 8d 8e 8f 90 91 92 93 94 95 96 97
  //   98 99 9a 9b 9c 9d 9e 9f a0 a1 a2 a3 a4 a5 a6 a7 a8 a9 aa ab ac ad ae af b0 b1 b2 b3 b4 b5 b6 b7 b8
  //   b9 ba bb bc bd be bf c0 c1 c2 c3 c4 c5 c6 c7 c8 c9 ca cb cc cd ce cf d0 d1 d2 d3 d4 d5 d6 d7 d8 d9
  //   da db dc dd de df e0 e1 e2 e3 e4 e5 e6 e7 e8 e9 ea eb ec ed ee ef f0 f1 f2 f3 f4 f5 f6 f7 f8 f9 fa
  //   fb fc fd fe ff 0 2 3 4 5 6 7 8 9 a b c d e f 10 11 12 13 14 15 16 17 18 19 1a 1b 1c 1d 1e 1f 20 21
  //   22 23 24 25 26 27 28 29 2a 2b 2c 2d 2e 2f 30 31 32 33 34 35 36 37 38 39 3a 3b 3c 3d 3e 3f 40 41 42
  //   43 44 45 46 47 48 49 4a 4b 4c 4d 4e 4f 50 51 52 53 54 55 56 57 58 59 5a 5b 5c 5d 5e 5f 60 61 62 63
  //   64 65 66 67 68 69 6a 6b 6c 6d 6e 6f 70 71 72 73 74 75 76 77 78 79 7a 7b 7c 7d 7e 7f 80 81 82 83 84
  //   85 86 87 88 89 8a 8b 8c 8d 8e 8f 90 91 92 93 94 95 96 97 98 99 9a 9b 9c 9d 9e 9f a0 a1 a2 a3 a4 a5
  //   a6 a7 a8 a9 aa ab ac ad ae af b0 b1 b2 b3 b4 b5 b6 b7 b8 b9 ba bb bc bd be bf c0 c1 c2 c3 c4 c5 c6
  //   c7 c8 c9 ca cb cc cd ce cf d0 d1 d2 d3 d4 d5 d6 d7 d8 d9 da db dc dd de df e0 e1 e2 e3 e4 e5 e6 e7
  //   e8 e9 ea eb ec ed ee ef f0 f1 f2 f3 f4 f5 f6 f7 f8 f9 fa fb fc fd fe ff 0 1 3 4 5 6 7 8 9 a b c d e
  //   f 10 11 12 13 14 15 16 17 18 19 1a 1b 1c 1d 1e 1f 20 21 22 23 24 25 26 27 28 29 2a 2b 2c 2d 2e 2f 30
  //   31 32 33 34 35 36 37 38 39 3a 3b 3c 3d 3e 3f 40 41 42 43 44 45 46 47 48 49 4a 4b 4c 4d 4e 4f 50 51
  //   52 53 54 55 56 57 58 59 5a 5b 5c 5d 5e 5f 60 61 62 63 64 65 66 67 68 69 6a 6b 6c 6d 6e 6f 70 71 72
  //   73 74 75 76 77 78 79 7a 7b 7c 7d 7e 7f 80 81 82 83 84 85 86 87 88 89 8a 8b 8c 8d 8e 8f 90 91 92 93
  //   94 95 96 97 98 99 9a 9b 9c 9d 9e 9f a0 a1 a2 a3 a4 a5 a6 a7 a8 a9 aa ab ac ad ae af b0 b1 b2 b3 b4
  //   b5 b6 b7 b8 b9 ba bb bc bd be bf c0 c1 c2 c3 c4 c5 c6 c7 c8 c9 ca cb cc cd ce cf d0 d1 d2 d3 d4 d5
  //   d6 d7 d8 d9 da db dc dd de df e0 e1 e2 e3 e4 e5 e6 e7 e8 e9 ea eb ec ed ee ef f0 f1 f2 f3 f4 f5 f6
  //   f7 f8 f9 fa fb fc fd fe ff 0 1 2 4 5 6 7 8 9 a b c d e f 10 11 12 13 14 15 16 17 18 19 1a 1b 1c 1d
  //   1e 1f 20 21 22 23 24 25 26 27 28 29 2a 2b 2c 2d 2e 2f 30 31 32 33 34 35 36 37 38 39 3a 3b 3c 3d 3e
  //   3f 40 41 42 43 44 45 46 47 48 49 4a 4b 4c 4d 4e 4f 50 51 52 53 54 55 56 57 58 59 5a 5b 5c 5d 5e 5f
  //   60 61 62 63 64 65 66 67 68 69 6a 6b 6c 6d 6e 6f 70 71 72 73 74 75 76 77 78 79 7a 7b 7c 7d 7e 7f 80
  //   81 82 83 84 85 86 87 88 89 8a 8b 8c 8d 8e 8f 90 91 92 93 94 95 96 97 98 99 9a 9b 9c 9d 9e 9f a0 a1
  //   a2 a3 a4 a5 a6 a7 a8 a9 aa ab ac ad ae af b0 b1 b2 b3 b4 b5 b6 b7 b8 b9 ba bb bc bd be bf c0 c1 c2
  //   c3 c4 c5 c6 c7 c8 c9 ca cb cc cd ce cf d0 d1 d2 d3 d4 d5 d6 d7 d8 d9 da db dc dd de df e0 e1 e2 e3
  //   e4 e5 e6 e7 e8 e9 ea eb ec ed ee ef f0 f1 f2 f3 f4 f5 f6 f7 f8 f9 fa fb fc fd fe ff 0 1 2 3 5 6 7 8
  //   9 a b c d e f 10 11 12 13 14 15 16 17 18 19 1a 1b 1c 1d 1e 1f 20 21 22 23 24 25 26 27 28 29 2a 2b 2c
  //   2d 2e 2f 30 31 32 33 34 35 36 37 38 39 3a 3b 3c 3d 3e 3f 40 41 42 43 44 45 46 47 48 49 4a 4b 4c 4d
  //   4e 4f 50 51 52 53 54 55 56 57 58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
endmodule

module mmu (
  input  [7:0] data_in,
  input  [6:0] key_char,
  input  key_rdy,
  input  [23:0] addr,
  input  store,
  input  clk,
  output key_discard,
  output [6:0] ttydata,
  output ttyclk,
  output [7:0] data_out
);

  wire and_1_out, and_2_out, and_3_out, comparator_1_eq, comparator_1_gt, comparator_1_lt, not_1_out;
  wire [7:0] controlled_buffer_4_out;

  assign data_out = store ? data_in : 8'bz;  // Controlled_Buffer controlled_buffer_1
  Comparator #(.width(24)) comparator_1 (
    .a(24'h1), .b(addr), .gt(comparator_1_gt), .eq(comparator_1_eq), .lt(comparator_1_lt));
  not not_1 (not_1_out, store);
  assign data_out = and_1_out ? {key_rdy, key_char} : 8'bz;  // Controlled_Buffer controlled_buffer_2
  and and_1 (and_1_out, comparator_1_gt, not_1_out);
  assign data_out = and_2_out ? 8'hcc : 8'bz;  // Controlled_Buffer controlled_buffer_3
  and and_2 (and_2_out, comparator_1_eq, comparator_1_eq);
  assign controlled_buffer_4_out = store ? data_out : 8'bz;  // Controlled_Buffer controlled_buffer_4
  RAM #(.addrWidth(24)) ram_1 (
    .addr(addr), .data(controlled_buffer_4_out), .clk(clk), .ld(not_1_out));  // open: sel, clr
  assign data_out = and_3_out ? controlled_buffer_4_out : 8'bz;  // Controlled_Buffer controlled_buffer_5
  and and_3 (and_3_out, comparator_1_lt, not_1_out);
  and and_4 (key_discard, data_out[7], store, clk, comparator_1_gt);
  and and_5 (ttyclk, comparator_1_eq, store, clk);

  assign ttydata = data_out[6:0];

  // Notes on the sheet:
  //   addr == 1
  //   addr > 1
  //   addr == 0
endmodule

module key_ctrl (
  input  key_avail,
  input  discard,
  output key_clk,
  output key_read_en,
  output rdy
);

  wire and_1_out, and_2_out, and_4_out, clock_1_out, d_ff_1_q, d_ff_2_q, decoder_1_out0, decoder_1_out1,
       decoder_1_out2, decoder_1_out3, decoder_1_out4;
  wire [2:0] counter_1_q;

  Counter #(.max('h4), .trigger("falling"), .width(3)) counter_1 (
    .clk(clock_1_out), .Q(counter_1_q));  // open: clr, load, up, count, D, carry
  Clock clock_1 (.out(clock_1_out));
  Decoder #(.enable("false"), .select(3)) decoder_1 (
    .out0(decoder_1_out0), .out1(decoder_1_out1), .out2(decoder_1_out2), .out3(decoder_1_out3),
    .out4(decoder_1_out4), .sel(counter_1_q));  // open: out5, out6, out7
  D_Flip_Flop d_ff_1 (.D(1'b1), .clk(and_1_out), .Q(d_ff_1_q), .reset(and_4_out));  // open: Qn, preset
  or or_1 (key_clk, decoder_1_out0, and_1_out);
  and and_1 (and_1_out, decoder_1_out2, d_ff_2_q);
  or or_2 (key_read_en, decoder_1_out1, decoder_1_out2);
  D_Flip_Flop d_ff_2 (.D(1'b1), .clk(discard), .Q(d_ff_2_q), .reset(and_4_out));  // open: Qn, preset
  and and_2 (and_2_out, d_ff_1_q, decoder_1_out3);
  and and_3 (rdy, key_avail, ~and_2_out);  // AND_Gate
  and and_4 (and_4_out, d_ff_1_q, decoder_1_out4);
endmodule

module regs (
  input  [3:0] D,
  input  [3:0] index,
  input  W,
  input  R,
  input  ADDR_CLK,
  output [3:0] QLO,
  output [3:0] QHI,
  output [3:0] Q,
  output [23:0] extADDR,
  output [7:0] ADDR
);

  wire and_1_out, and_2_out, l_74ls156_13d76295_1_l_1y0_69bcf2ce, l_74ls156_13d76295_1_l_1y1_80d05f78,
       l_74ls156_13d76295_1_l_1y2_e2e6b1c4, l_74ls156_13d76295_1_l_1y3_4dbd67a8,
       l_74ls156_13d76295_1_l_2y0_75c407a5, l_74ls156_13d76295_1_l_2y1_6590c387,
       l_74ls156_13d76295_1_l_2y2_90435f67, l_74ls156_13d76295_1_l_2y3_3fbb4070, not_1_out;
  wire [1:1] undriven;

  L_74LS156_13d76295 l_74ls156_13d76295_1 (
    .L_1G_a10fd0cc(W), .L_1C_414f0e12(1'b1), .SEL({undriven[1], index[0]}), .L_2G_f1afdeec(R),
    .L_2C_763bb621(1'b1), .L_1Y0_69bcf2ce(l_74ls156_13d76295_1_l_1y0_69bcf2ce),
    .L_1Y1_80d05f78(l_74ls156_13d76295_1_l_1y1_80d05f78),
    .L_1Y2_e2e6b1c4(l_74ls156_13d76295_1_l_1y2_e2e6b1c4),
    .L_1Y3_4dbd67a8(l_74ls156_13d76295_1_l_1y3_4dbd67a8),
    .L_2Y0_75c407a5(l_74ls156_13d76295_1_l_2y0_75c407a5),
    .L_2Y1_6590c387(l_74ls156_13d76295_1_l_2y1_6590c387),
    .L_2Y2_90435f67(l_74ls156_13d76295_1_l_2y2_90435f67), .L_2Y3_3fbb4070(l_74ls156_13d76295_1_l_2y3_3fbb4070));
  and and_1 (and_1_out, l_74ls156_13d76295_1_l_1y3_4dbd67a8, l_74ls156_13d76295_1_l_2y1_6590c387);
  and and_2 (and_2_out, l_74ls156_13d76295_1_l_2y1_6590c387, l_74ls156_13d76295_1_l_2y1_6590c387);
  // L_74LS670_eb033b10 LO1: pin names not known; wires that end beside it: index[1], l_74ls156_13d76295_1_l_1y0_69bcf2ce, index[1], and_1_out, D, QLO
  // L_74LS670_eb033b10 HI1: pin names not known; wires that end beside it: index[1], l_74ls156_13d76295_1_l_1y1_80d05f78, index[1], and_1_out, D, QHI
  // L_74LS670_eb033b10 LO2: pin names not known; wires that end beside it: index[1], l_74ls156_13d76295_1_l_1y2_e2e6b1c4, index[1], and_2_out, D, QLO
  // L_74LS670_eb033b10 HI2: pin names not known; wires that end beside it: index[1], l_74ls156_13d76295_1_l_1y3_4dbd67a8, index[1], and_2_out, D, QHI
  Multiplexer #(.width(4)) multiplexer_1 (.in0(QLO), .in1(QHI), .out(D), .sel(index[0]), .en(not_1_out));
  not not_1 (not_1_out, R);
  L_74HCT377_ee285abe l_74hct377_ee285abe_1 (
    .D({QHI, QLO}), .EN_1fc52481(l_74ls156_13d76295_1_l_2y0_75c407a5), .CLK(ADDR_CLK), .Q(extADDR[7:0]));
  L_74HCT377_ee285abe l_74hct377_ee285abe_2 (
    .D({QHI, QLO}), .EN_1fc52481(l_74ls156_13d76295_1_l_2y1_6590c387), .CLK(ADDR_CLK), .Q(extADDR[15:8]));
  L_74HCT377_ee285abe l_74hct377_ee285abe_3 (
    .D({QHI, QLO}), .EN_1fc52481(l_74ls156_13d76295_1_l_2y2_90435f67), .CLK(ADDR_CLK), .Q(extADDR[23:16]));
  L_74HCT377_ee285abe l_74hct377_ee285abe_4 (
    .D({QHI, QLO}), .EN_1fc52481(l_74ls156_13d76295_1_l_2y3_3fbb4070), .CLK(ADDR_CLK), .Q(ADDR));
  // Pins of 2 and 4 bits meet at index

  assign Q = D;

  // Notes on the sheet:
  //   W: pull=up
  //   R: pull=up
endmodule

module L_74LS670_eb033b10 (
  input  [1:0] W,
  input  GW_8736aacc,
  input  [1:0] R,
  input  GR_85258d65,
  input  [3:0] in_5,
  output [3:0] IO
);

  wire decoder_1_out0, decoder_1_out1, decoder_1_out2, decoder_1_out3, decoder_2_out0, decoder_2_out1,
       decoder_2_out2, decoder_2_out3, not_1_out;
  wire [3:0] register_1_q, register_2_q, register_3_q, register_4_q;

  not not_1 (not_1_out, GR_85258d65);
  Decoder #(.enable("false"), .select(2)) decoder_1 (
    .out0(decoder_1_out0), .out1(decoder_1_out1), .out2(decoder_1_out2), .out3(decoder_1_out3), .sel(W));
  Decoder #(.select(2)) decoder_2 (
    .out0(decoder_2_out0), .out1(decoder_2_out1), .out2(decoder_2_out2), .out3(decoder_2_out3), .sel(R),
    .en(not_1_out));
  Register #(.width(4)) register_1 (.D(in_5), .en(decoder_1_out0), .Q(register_1_q), .clk(GW_8736aacc));  // open: clr
  Register #(.width(4)) register_2 (.D(in_5), .en(decoder_1_out1), .Q(register_2_q), .clk(GW_8736aacc));  // open: clr
  Register #(.width(4)) register_3 (.D(in_5), .en(decoder_1_out2), .Q(register_3_q), .clk(GW_8736aacc));  // open: clr
  Register #(.width(4)) register_4 (.D(in_5), .en(decoder_1_out3), .Q(register_4_q), .clk(GW_8736aacc));  // open: clr
  assign in_5 = decoder_2_out0 ? register_1_q : 4'bz;  // Controlled_Buffer controlled_buffer_1
  assign in_5 = decoder_2_out1 ? register_2_q : 4'bz;  // Controlled_Buffer controlled_buffer_2
  assign in_5 = decoder_2_out2 ? register_3_q : 4'bz;  // Controlled_Buffer controlled_buffer_3
  assign in_5 = decoder_2_out3 ? register_4_q : 4'bz;  // Controlled_Buffer controlled_buffer_4

  assign IO = in_5;
endmodule

module L_74LS156_13d76295 (
  input  L_1G_a10fd0cc,
  input  L_1C_414f0e12,
  input  [1:0] SEL,
  input  L_2G_f1afdeec,
  input  L_2C_763bb621,
  output L_1Y0_69bcf2ce,
  output L_1Y1_80d05f78,
  output L_1Y2_e2e6b1c4,
  output L_1Y3_4dbd67a8,
  output L_2Y0_75c407a5,
  output L_2Y1_6590c387,
  output L_2Y2_90435f67,
  output L_2Y3_3fbb4070
);

  wire and_1_out, and_2_out;

  and and_1 (and_1_out, ~L_1G_a10fd0cc, L_1C_414f0e12);  // AND_Gate
  and and_2 (and_2_out, ~L_2G_f1afdeec, L_2C_763bb621);  // AND_Gate
  Decoder #(.enable("false"), .select(2)) decoder_1 (
    .out0(and_1_out), .out1(and_1_out), .out2(and_1_out), .out3(and_1_out), .sel(SEL));
  Decoder #(.enable("false"), .select(2)) decoder_2 (
    .out0(and_2_out), .out1(and_2_out), .out2(and_2_out), .out3(and_2_out), .sel(SEL));
  Pull_Resistor #(.pull(1)) pull_resistor_1 (.node(L_1Y0_69bcf2ce));
  Pull_Resistor #(.pull(1)) pull_resistor_2 (.node(L_1Y1_80d05f78));
  Pull_Resistor #(.pull(1)) pull_resistor_3 (.node(L_1Y2_e2e6b1c4));
  assign L_1Y0_69bcf2ce = and_1_out ? ~and_1_out : 1'bz;  // Controlled_Inverter controlled_inverter_1
  assign L_1Y1_80d05f78 = and_1_out ? ~and_1_out : 1'bz;  // Controlled_Inverter controlled_inverter_2
  assign L_1Y2_e2e6b1c4 = and_1_out ? ~and_1_out : 1'bz;  // Controlled_Inverter controlled_inverter_3
  Pull_Resistor #(.pull(1)) pull_resistor_4 (.node(L_2Y0_75c407a5));
  Pull_Resistor #(.pull(1)) pull_resistor_5 (.node(L_2Y1_6590c387));
  Pull_Resistor #(.pull(1)) pull_resistor_6 (.node(L_2Y2_90435f67));
  assign L_2Y0_75c407a5 = and_2_out ? ~and_2_out : 1'bz;  // Controlled_Inverter controlled_inverter_4
  assign L_2Y1_6590c387 = and_2_out ? ~and_2_out : 1'bz;  // Controlled_Inverter controlled_inverter_5
  assign L_2Y2_90435f67 = and_2_out ? ~and_2_out : 1'bz;  // Controlled_Inverter controlled_inverter_6
  Pull_Resistor #(.pull(1)) pull_resistor_7 (.node(L_1Y3_4dbd67a8));
  assign L_1Y3_4dbd67a8 = and_1_out ? ~and_1_out : 1'bz;  // Controlled_Inverter controlled_inverter_7
  Pull_Resistor #(.pull(1)) pull_resistor_8 (.node(L_2Y3_3fbb4070));
  assign L_2Y3_3fbb4070 = and_2_out ? ~and_2_out : 1'bz;  // Controlled_Inverter controlled_inverter_8
endmodule

module L_74HCT377_ee285abe (
  input  [7:0] D,
  input  EN_1fc52481,
  input  CLK,
  output [7:0] Q
);

  wire not_1_out;

  not not_1 (not_1_out, EN_1fc52481);
  Register register_1 (.D(D), .en(not_1_out), .Q(Q), .clk(CLK));  // open: clr
endmodule

module L_74HCT299_ee0e0bad (
  input  [7:0] D,
  input  S0,
  input  S1,
  input  CP,
  input  L_MR_86c31974,
  input  L_OE1_38eafe72,
  input  L_OE2_bdbe0e0f,
  output [7:0] Q,
  output [7:0] peek
);

  wire and_1_out, nor_1_out, not_1_out;

  Pull_Resistor #(.pull(1)) pull_resistor_1 (.node(S0));
  Pull_Resistor #(.pull(1)) pull_resistor_2 (.node(S1));
  Pull_Resistor #(.pull(1)) pull_resistor_3 (.node(CP));
  Pull_Resistor #(.pull(1)) pull_resistor_4 (.node(L_MR_86c31974));
  Pull_Resistor #(.pull(1)) pull_resistor_5 (.node(L_OE1_38eafe72));
  Pull_Resistor #(.pull(1)) pull_resistor_6 (.node(L_OE2_bdbe0e0f));
  and and_1 (and_1_out, S0, S1);
  not not_1 (not_1_out, L_MR_86c31974);
  nor nor_1 (nor_1_out, L_OE1_38eafe72, and_1_out, L_OE2_bdbe0e0f);
  Register register_1 (.D(D), .en(and_1_out), .clk(CP), .Q(peek), .clr(not_1_out));
  assign Q = nor_1_out ? peek : 8'bz;  // Controlled_Buffer controlled_buffer_1
endmodule

// 74593
module L_74LS593_21dd63b5 (
  input  CCK,
  input  CCKEN,
  input  CCKEN_5c036e0c,
  input  CCLR_8a329eb0,
  input  CLOAD_ffa3f122,
  input  [7:0] IO_I_f0d4e37f,
  input  RCKEN_ccd78180,
  input  RCK,
  input  G,
  input  G_5b2d2516,
  output [7:0] rpeek,
  output [7:0] IO_O_57be0de8,
  output RCO_99259e83,
  output [7:0] peek
);

  wire and_1_out, and_2_out, and_3_out, and_4_out, and_5_out, and_6_out, and_7_out, and_8_out, and_9_out,
       and_10_out, and_11_out, and_12_out, and_13_out, and_14_out, and_15_out, and_16_out, comparator_1_eq,
       not_1_out, not_2_out, or_1_out, or_2_out, or_3_out, or_4_out, or_5_out, or_6_out, or_7_out, or_8_out,
       or_9_out, or_10_out;
  wire [7:0] adder_1_out;

  Pull_Resistor #(.pull(1)) pull_resistor_1 (.node(CLOAD_ffa3f122));
  Pull_Resistor #(.pull(1)) pull_resistor_2 (.node(RCKEN_ccd78180));
  not not_1 (not_1_out, RCKEN_ccd78180);
  Pull_Resistor #(.pull(1)) pull_resistor_3 (.node(RCK));
  Register register_1 (.D(IO_I_f0d4e37f), .en(not_1_out), .Q(rpeek), .clk(RCK));  // open: clr
  Pull_Resistor #(.pull(1)) pull_resistor_4 (.node(CCKEN));
  Pull_Resistor #(.pull(1)) pull_resistor_5 (.node(CCKEN_5c036e0c));
  Pull_Resistor #(.pull(1)) pull_resistor_6 (.node(CCLR_8a329eb0));
  and and_1 (and_1_out, rpeek[0], ~CLOAD_ffa3f122);  // AND_Gate
  and and_2 (and_2_out, ~rpeek[0], ~CLOAD_ffa3f122);  // AND_Gate
  and and_3 (and_3_out, rpeek[1], ~CLOAD_ffa3f122);  // AND_Gate
  and and_4 (and_4_out, ~rpeek[1], ~CLOAD_ffa3f122);  // AND_Gate
  and and_5 (and_5_out, rpeek[2], ~CLOAD_ffa3f122);  // AND_Gate
  and and_6 (and_6_out, ~rpeek[2], ~CLOAD_ffa3f122);  // AND_Gate
  and and_7 (and_7_out, rpeek[3], ~CLOAD_ffa3f122);  // AND_Gate
  and and_8 (and_8_out, ~rpeek[3], ~CLOAD_ffa3f122);  // AND_Gate
  and and_9 (and_9_out, rpeek[4], ~CLOAD_ffa3f122);  // AND_Gate
  and and_10 (and_10_out, ~rpeek[4], ~CLOAD_ffa3f122);  // AND_Gate
  and and_11 (and_11_out, rpeek[5], ~CLOAD_ffa3f122);  // AND_Gate
  and and_12 (and_12_out, ~rpeek[5], ~CLOAD_ffa3f122);  // AND_Gate
  and and_13 (and_13_out, rpeek[6], ~CLOAD_ffa3f122);  // AND_Gate
  and and_14 (and_14_out, ~rpeek[6], ~CLOAD_ffa3f122);  // AND_Gate
  and and_15 (and_15_out, rpeek[7], ~CLOAD_ffa3f122);  // AND_Gate
  and and_16 (and_16_out, ~rpeek[7], ~CLOAD_ffa3f122);  // AND_Gate
  Pull_Resistor #(.pull(1)) pull_resistor_7 (.node(CCK));
  or or_1 (or_1_out, CCKEN, ~CCKEN_5c036e0c);  // OR_Gate
  not not_2 (not_2_out, CCLR_8a329eb0);
  or or_2 (or_2_out, and_2_out, not_2_out);
  or or_3 (or_3_out, and_4_out, not_2_out);
  or or_4 (or_4_out, and_6_out, not_2_out);
  or or_5 (or_5_out, and_8_out, not_2_out);
  or or_6 (or_6_out, and_10_out, not_2_out);
  or or_7 (or_7_out, and_12_out, not_2_out);
  or or_8 (or_8_out, and_14_out, not_2_out);
  or or_9 (or_9_out, and_16_out, not_2_out);
  Register #(.width(1)) register_2 (.D(adder_1_out[0]), .en(or_1_out), .Q(peek[0]), .clk(CCK), .clr(or_2_out));
  Register #(.width(1)) register_3 (.D(adder_1_out[1]), .en(or_1_out), .Q(peek[1]), .clk(CCK), .clr(or_3_out));
  Register #(.width(1)) register_4 (.D(adder_1_out[2]), .en(or_1_out), .Q(peek[2]), .clk(CCK), .clr(or_4_out));
  Register #(.width(1)) register_5 (.D(adder_1_out[3]), .en(or_1_out), .Q(peek[3]), .clk(CCK), .clr(or_5_out));
  Register #(.width(1)) register_6 (.D(adder_1_out[4]), .en(or_1_out), .Q(peek[4]), .clk(CCK), .clr(or_6_out));
  Register #(.width(1)) register_7 (.D(adder_1_out[5]), .en(or_1_out), .Q(peek[5]), .clk(CCK), .clr(or_7_out));
  Register #(.width(1)) register_8 (.D(adder_1_out[6]), .en(or_1_out), .Q(peek[6]), .clk(CCK), .clr(or_8_out));
  Register #(.width(1)) register_9 (.D(adder_1_out[7]), .en(or_1_out), .Q(peek[7]), .clk(CCK), .clr(or_9_out));
  Adder adder_1 (.a(peek), .b(8'h1), .out(adder_1_out));  // open: cin, cout
  Pull_Resistor #(.pull(1)) pull_resistor_8 (.node(G));
  Pull_Resistor #(.pull(1)) pull_resistor_9 (.node(G_5b2d2516));
  assign IO_O_57be0de8 = or_10_out ? peek : 8'bz;  // Controlled_Buffer controlled_buffer_1
  or or_10 (or_10_out, G, ~G_5b2d2516);  // OR_Gate
  not not_3 (RCO_99259e83, comparator_1_eq);
  Comparator comparator_1 (.a(peek), .b({8{1'b1}}), .eq(comparator_1_eq));  // open: gt, lt

  // Notes on the sheet:
  //   G: pull=up
  //   G_5b2d2516: pull=up
  //   peek: pull=up
  //   IO_O_57be0de8: pull=up
  //   RCKEN_ccd78180: pull=up
  //   RCK: pull=up
  //   CLOAD_ffa3f122: pull=up
  //   rpeek: pull=up
  //   CCKEN: pull=up
  //   CCKEN_5c036e0c: pull=up
  //   CCLR_8a329eb0: pull=up
  //   CCK: pull=up
endmodule

// 574
module L_74HCT574_611e6db7 (
  input  [7:0] D,
  input  CP,
  input  OE_83629f7f,
  output [7:0] Q,
  output [7:0] Zpeek
);

  wire not_1_out;

  Register register_1 (.D(D), .clk(CP), .Q(Zpeek));  // open: en, clr
  not not_1 (not_1_out, OE_83629f7f);
  assign Q = not_1_out ? Zpeek : 8'bz;  // Controlled_Buffer controlled_buffer_1
endmodule

// RAM
module AS6C4008 (
  input  [18:0] A,
  input  [7:0] D,
  input  CE_0dd5e992,
  input  OE_83629f7f,
  input  WE_09c3d0b5,
  output [7:0] peek,
  output [7:0] Q
);

  wire and_1_out, and_2_out, and_3_out, not_1_out, not_2_out, not_3_out;

  not not_1 (not_1_out, OE_83629f7f);
  not not_2 (not_2_out, and_2_out);
  and and_1 (and_1_out, OE_83629f7f, ~CE_0dd5e992, not_3_out);  // AND_Gate
  and and_2 (and_2_out, not_1_out, ~CE_0dd5e992);  // AND_Gate
  not not_3 (not_3_out, WE_09c3d0b5);
  and and_3 (and_3_out, ~CE_0dd5e992, not_1_out);  // AND_Gate
  RAM #(.addrWidth(19), .asyncread("true")) ram_1 (
    .addr(A), .we(not_2_out), .oe(1'b1), .clk(and_1_out), .din(D), .dout(peek));
  assign D = and_3_out ? peek : 8'bz;  // Controlled_Buffer controlled_buffer_1

  assign Q = D;
endmodule

// 74138
module L_74HCT138_ff2bfe81 (
  input  E1_8073e2cf,
  input  E2_3ccbccd8,
  input  E3,
  input  [2:0] A,
  output Y0_36f069fd,
  output Y1_bf899b0a,
  output Y2_4c64a680,
  output Y3_0d3b75c7,
  output Y4_fc72c967,
  output Y5_164c4e51,
  output Y6_decf6708,
  output Y7_23027958
);

  wire and_1_out, decoder_1_out0, decoder_1_out1, decoder_1_out2, decoder_1_out3, decoder_1_out4,
       decoder_1_out5, decoder_1_out6, decoder_1_out7;

  and and_1 (and_1_out, ~E1_8073e2cf, ~E2_3ccbccd8, E3);  // AND_Gate
  not not_1 (Y0_36f069fd, decoder_1_out0);
  not not_2 (Y1_bf899b0a, decoder_1_out1);
  not not_3 (Y2_4c64a680, decoder_1_out2);
  not not_4 (Y3_0d3b75c7, decoder_1_out3);
  not not_5 (Y4_fc72c967, decoder_1_out4);
  not not_6 (Y5_164c4e51, decoder_1_out5);
  not not_7 (Y6_decf6708, decoder_1_out6);
  not not_8 (Y7_23027958, decoder_1_out7);
  Decoder #(.select(3)) decoder_1 (
    .out0(decoder_1_out0), .out1(decoder_1_out1), .out2(decoder_1_out2), .out3(decoder_1_out3),
    .out4(decoder_1_out4), .out5(decoder_1_out5), .out6(decoder_1_out6), .out7(decoder_1_out7), .sel(A),
    .en(and_1_out));
endmodule

// 74238
module L_74HCT238_2e8277f3 (
  input  E1_8073e2cf,
  input  E2_3ccbccd8,
  input  E3,
  input  [2:0] A,
  output Y0_36f069fd,
  output Y1_bf899b0a,
  output Y2_4c64a680,
  output Y3_0d3b75c7,
  output Y4_fc72c967,
  output Y5_164c4e51,
  output Y6_decf6708,
  output Y7_23027958
);

  wire and_1_out;

  and and_1 (and_1_out, ~E1_8073e2cf, ~E2_3ccbccd8, E3);  // AND_Gate
  Decoder #(.select(3)) decoder_1 (
    .out0(Y0_36f069fd), .out1(Y1_bf899b0a), .out2(Y2_4c64a680), .out3(Y3_0d3b75c7), .out4(Y4_fc72c967),
    .out5(Y5_164c4e51), .out6(Y6_decf6708), .out7(Y7_23027958), .sel(A), .en(and_1_out));
endmodule

// 299
module L_74HCT299_simplified_1381c5be (
  input  [7:0] D,
  input  L_OE_25175598,
  input  CP,
  output [7:0] Q,
  output [7:0] peek
);

  Pull_Resistor #(.pull(1)) pull_resistor_1 (.node(L_OE_25175598));
  L_74HCT299_ee0e0bad l_74hct299_ee0e0bad_1 (
    .peek(peek), .Q(Q), .S0(L_OE_25175598), .S1(L_OE_25175598), .CP(CP), .L_MR_86c31974(1'b1),
    .L_OE1_38eafe72(L_OE_25175598), .L_OE2_bdbe0e0f(L_OE_25175598), .D(D));
endmodule

module SST39SF040 (
  input  [7:0] ROM_D,
  input  CE_0dd5e992,
  input  OE_83629f7f,
  output [7:0] DQ
);

  wire and_1_out;

  and and_1 (and_1_out, ~CE_0dd5e992, ~OE_83629f7f);  // AND_Gate
  assign DQ = and_1_out ? ROM_D : 8'bz;  // Controlled_Buffer controlled_buffer_1
endmodule

module L_74HCT161_263709e2 (
  input  SPE_b95b37ae,
  input  [3:0] P,
  input  CP,
  input  PE,
  input  TE,
  input  MR_30eafd07,
  output [3:0] Q,
  output TC
);

  wire and_1_out, and_2_out, not_1_out, not_2_out, or_1_out;

  Pull_Resistor #(.pull(1)) pull_resistor_1 (.node(SPE_b95b37ae));
  not not_1 (not_1_out, SPE_b95b37ae);
  Pull_Resistor #(.pull(1)) pull_resistor_2 (.node(MR_30eafd07));
  not not_2 (not_2_out, MR_30eafd07);
  and and_1 (and_1_out, PE, TE);
  or or_1 (or_1_out, and_1_out, not_1_out);
  and and_2 (and_2_out, ~not_2_out, or_1_out);  // AND_Gate
  Counter #(.max('hf), .width(4)) counter_1 (
    .load(not_1_out), .D(P), .Q(Q), .carry(TC), .up(and_2_out), .clk(CP), .clr(not_2_out));  // open: count
endmodule
