// Digital circuit memory.dig as structural Verilog
module memory (
  input  MEM_CP,
  input  ADDR_OE,
  input  A0_CP,
  input  A1_CP,
  input  A2_CP,
  input  MEM_OE,
  input  [7:0] DATA_2,
  input  [23:0] ADDR_2,
  output [7:0] DATA,
  output [23:0] ADDR
);

  wire not_1_out, not_2_out, not_3_out, or_1_out;
  wire [7:0] ROM_d;

  // _74574 ADDR0: pin names not known; wires that end beside it: ADDR_OE, 1'b1
  // _74574 ADDR1: pin names not known; wires that end beside it: 1'b0, ADDR_OE, A0_CP, 1'b1
  // _74574 ADDR2: pin names not known; wires that end beside it: 1'b0, ADDR_OE, 1'b0, A1_CP, 1'b1, A2_CP
  not not_1 (not_1_out, MEM_CP);
  not not_2 (not_2_out, ADDR_2[19]);
  not not_3 (not_3_out, ADDR_2[19]);
  RAM ram_1 (.CE(not_2_out), .OE(MEM_OE), .WE(not_1_out), .A(ADDR_2[18:0]), .D(DATA_2));
  or or_1 (or_1_out, MEM_OE, ADDR_2[19]);
  ROM #(.AddrBits(19), .isProgramMemory("true"), .Bits(8)) ROM (.A(ADDR_2[18:0]), .sel(not_3_out), .D(ROM_d));
  assign DATA_2 = ~or_1_out ? ROM_d : 8'bz;  // DriverInvSel driverinvsel_1

  assign ADDR = ADDR_2;
  assign DATA = DATA_2;

  // Notes on the sheet:
  //   5A
  //   5Y
  //   6A
  //   6Y
  //   ROM
  //   ROM loads echo.asm.hex
endmodule

/* Test case A*:
ADDR    ADDR_OE_ MEM_OE_ $DATA A0_CP A1_CP A2_CP MEM_CP DATA
Z       1        1       0x03  C     0     0     0      0x03
Z       1        1       0x00  0     C     0     0      0x00
Z       1        1       0x00  0     0     C     0      0x00
0x3     0        0       Z     0     0     0     0      0x33
Z       1        1       0x08  0     0     C     0      0x08
0x80003 0        1       0xAA  0     0     0     C      0xAA
Z       1        1       0x02  C     0     0     0      0x02
0x80002 0        1       0xBB  0     0     0     C      0xBB
Z       1        1       0x03  C     0     0     0      0x03
0x80003 0        0       Z     0     0     0     0      0xAA
Z       1        1       0x02  C     0     0     0      0x02
0x80002 0        0       Z     0     0     0     0      0xBB
*/

/* Test case ADDR:
$ADDR    ADDR_OE_ MEM_OE_ $DATA MEM_CP ADDR    DATA
0x80007  1        1       0xAB  C      0x80007 0xAB
0x90001  1        1       0x34  C      0x90001 0x34
0x80007  1        0       Z     0      0x80007 0xAB
0x90001  1        0       Z     0      0x90001 0x34
*/
