// Digital circuit pc.dig as structural Verilog
module pc (
  input  PC_INC,
  input  RESET,
  input  PC_SPE,
  input  OE,
  input  [23:0] ADDR_IN,
  output [23:0] ADDR,
  output [23:0] PC
);

  wire PC0_pin15, PC1_pin15, PC2_pin15, PC3_pin15, PC4_pin15;

  _74161 PC0 (
    .pin1(RESET), .pin2(PC_INC), .pin3(ADDR_IN[0]), .pin4(ADDR_IN[1]), .pin5(ADDR_IN[2]), .pin6(ADDR_IN[3]),
    .pin7(1'b1), .pin8(1'b0), .pin9(PC_SPE), .pin10(1'b1), .pin11(PC[3]), .pin12(PC[2]), .pin13(PC[1]),
    .pin14(PC[0]), .pin15(PC0_pin15), .pin16(1'b1));
  _74161 PC1 (
    .pin1(RESET), .pin2(PC_INC), .pin3(ADDR_IN[4]), .pin4(ADDR_IN[5]), .pin5(ADDR_IN[6]), .pin6(ADDR_IN[7]),
    .pin7(PC0_pin15), .pin8(1'b0), .pin9(PC_SPE), .pin10(1'b1), .pin11(PC[7]), .pin12(PC[6]), .pin13(PC[5]),
    .pin14(PC[4]), .pin15(PC1_pin15), .pin16(1'b1));
  _74161 PC2 (
    .pin1(RESET), .pin2(PC_INC), .pin3(ADDR_IN[8]), .pin4(ADDR_IN[9]), .pin5(ADDR_IN[10]),
    .pin6(ADDR_IN[11]), .pin7(PC0_pin15), .pin8(1'b0), .pin9(PC_SPE), .pin10(PC1_pin15), .pin11(PC[11]),
    .pin12(PC[10]), .pin13(PC[9]), .pin14(PC[8]), .pin15(PC2_pin15), .pin16(1'b1));
  _74161 PC3 (
    .pin1(RESET), .pin2(PC_INC), .pin3(ADDR_IN[12]), .pin4(ADDR_IN[13]), .pin5(ADDR_IN[14]),
    .pin6(ADDR_IN[15]), .pin7(PC0_pin15), .pin8(1'b0), .pin9(PC_SPE), .pin10(PC2_pin15), .pin11(PC[15]),
    .pin12(PC[14]), .pin13(PC[13]), .pin14(PC[12]), .pin15(PC3_pin15), .pin16(1'b1));
  _74161 PC4 (
    .pin1(RESET), .pin2(PC_INC), .pin3(ADDR_IN[16]), .pin4(ADDR_IN[17]), .pin5(ADDR_IN[18]),
    .pin6(ADDR_IN[19]), .pin7(PC0_pin15), .pin8(1'b0), .pin9(PC_SPE), .pin10(PC3_pin15), .pin11(PC[19]),
    .pin12(PC[18]), .pin13(PC[17]), .pin14(PC[16]), .pin15(PC4_pin15), .pin16(1'b1));
  _74161 PC5 (
    .pin1(RESET), .pin2(PC_INC), .pin3(ADDR_IN[20]), .pin4(ADDR_IN[21]), .pin5(ADDR_IN[22]),
    .pin6(ADDR_IN[23]), .pin7(PC0_pin15), .pin8(1'b0), .pin9(PC_SPE), .pin10(PC4_pin15), .pin11(PC[23]),
    .pin12(PC[22]), .pin13(PC[21]), .pin14(PC[20]), .pin16(1'b1));  // open: pin15
  assign ADDR_IN = ~OE ? PC : 24'bz;  // DriverInvSel driverinvsel_1

  assign ADDR = ADDR_IN;
endmodule

/* Test case:
OE_ PC_SPE_ PC_INC RESET_ $ADDR_IN ADDR
X X X 0 Z X
0 1 0 1 Z 0
repeat(256) 0 1 C 1 Z (n+1)
loop (i, 7)
	1 0 C 1 ((1<<(4*i))-1) ((1<<(4*i))-1)
	0 1 0 1 Z ((1<<(4*i))-1)
	0 1 C 1 Z ((1<<(4*i))+0)
	0 1 C 1 Z ((1<<(4*i))+1)
end loop
*/
