// Digital circuit ps2.dig as structural Verilog
module ps2 (
  input  TTYIN_OE,
  input  CLK,
  input  TTYIN_CP
);

  wire _74161_1_pin9, _74161_1_pin15, _74299_1_pin18, and_1_out, and_2_out, comparator_1_gt, comparator_1_lt,
       counter_2_ovf, d_ff_1_q, nand_1_out, not_1_out, not_2_out, PS2_CLK, PS2_DATA, xor_1_out;
  wire [1:0] counter_1_out;
  wire [3:0] _74161_1_pin3, _74161_1_pin14, counter_2_out;
  wire [7:0] _74299_1_pin4, _74299_2_pin4, d_ff_2_q, multiplexer_1_out;
  wire [10:0] barrelshifter_1_out;
  wire [15:0] rom_1_d;

  Counter #(.Bits(2)) counter_1 (.en(1'b1), .C(comparator_1_lt), .clr(1'b0), .out(counter_1_out));  // open: ovf
  Counter #(.Bits(4)) counter_2 (.en(1'b1), .C(CLK), .clr(1'b0), .out(counter_2_out), .ovf(counter_2_ovf));
  ROM #(.Bits(16)) rom_1 (.A(counter_1_out), .sel(1'b1), .D(rom_1_d));
  not not_1 (not_1_out, CLK);
  D_FF d_ff_1 (.D(PS2_CLK), .C(counter_2_ovf), .Q(d_ff_1_q));  // open: nQ
  // Probe PS2_SENDBIT on counter_2_out
  Comparator #(.Bits(4)) comparator_1 (
    .a(4'b1011), .b(counter_2_out), .gt(comparator_1_gt), .lt(comparator_1_lt));  // open: eq
  BarrelShifter #(.Bits(11), .direction("right")) barrelshifter_1 (
    .in(rom_1_d[10:0]), .shift(counter_2_out), .out(barrelshifter_1_out));
  and and_1 (and_1_out, comparator_1_gt, d_ff_1_q, not_1_out);
  and and_2 (and_2_out, d_ff_1_q, ~barrelshifter_1_out[0]);  // And
  assign PS2_CLK = and_1_out ? 1'b0 : 1'bz;  // Driver driver_1
  assign PS2_DATA = and_2_out ? 1'b0 : 1'bz;  // Driver driver_2
  // Probe PS2_CLK on PS2_CLK
  // Probe PS2_DATA on PS2_DATA
  PullUp pullup_1 (.out(PS2_CLK));
  PullUp pullup_2 (.out(PS2_DATA));
  assign PS2_CLK = TTYIN_OE ? 1'b0 : 1'bz;  // Driver driver_3
  not not_2 (not_2_out, PS2_CLK);
  _74161 _74161_1 (
    .pin1(1'b1), .pin2(not_2_out), .pin3(_74161_1_pin3[0]), .pin4(_74161_1_pin3[1]), .pin5(_74161_1_pin3[2]),
    .pin6(_74161_1_pin3[3]), .pin7(1'b1), .pin8(1'b0), .pin9(_74161_1_pin9), .pin10(1'b1),
    .pin11(_74161_1_pin14[3]), .pin12(_74161_1_pin14[2]), .pin13(_74161_1_pin14[1]),
    .pin14(_74161_1_pin14[0]), .pin15(_74161_1_pin15), .pin16(1'b1));
  // Probe PS2_ROF on _74161_1_pin15
  // Probe PS2_RECVBIT on _74161_1_pin14
  not not_3 (_74161_1_pin9, _74161_1_pin15);
  assign PS2_CLK = ~nand_1_out ? 1'b0 : 1'bz;  // DriverInvSel driverinvsel_1
  nand nand_1 (nand_1_out, d_ff_2_q[7], _74161_1_pin15);
  _74299 _74299_1 (
    .pin1(1'b0), .pin2(1'b0), .pin3(1'b0), .pin4(_74299_1_pin4[6]), .pin5(_74299_1_pin4[4]),
    .pin6(_74299_1_pin4[2]), .pin7(_74299_1_pin4[0]), .pin9(1'b1), .pin10(1'b0), .pin11(1'b1),
    .pin12(not_2_out), .pin13(_74299_1_pin4[1]), .pin14(_74299_1_pin4[3]), .pin15(_74299_1_pin4[5]),
    .pin16(_74299_1_pin4[7]), .pin18(_74299_1_pin18), .pin19(1'b1), .pin20(1'b1));  // open: pin8, pin17
  _74299 _74299_2 (
    .pin1(1'b0), .pin2(1'b0), .pin3(1'b0), .pin4(_74299_2_pin4[6]), .pin5(_74299_2_pin4[4]),
    .pin6(_74299_2_pin4[2]), .pin7(_74299_2_pin4[0]), .pin8(_74299_1_pin18), .pin9(1'b1), .pin10(1'b0),
    .pin11(1'b1), .pin12(not_2_out), .pin13(_74299_2_pin4[1]), .pin14(_74299_2_pin4[3]),
    .pin15(_74299_2_pin4[5]), .pin16(_74299_2_pin4[7]), .pin18(PS2_DATA), .pin19(1'b1), .pin20(1'b1));  // open: pin17
  xor xor_1 (xor_1_out, _74161_1_pin15, TTYIN_CP);
  // Probe PS2_INCOMING on {_74299_2_pin4, _74299_1_pin4}
  // Probe PS2_START on _74299_1_pin4[5]
  // Probe PS2_DATA on {_74299_2_pin4[5:0], _74299_1_pin4[7:6]}
  // Probe PS2_PARITY on _74299_2_pin4[6]
  // Probe PS2_STOP on _74299_2_pin4[7]
  Multiplexer #(.Bits(8)) multiplexer_1 (
    .sel(d_ff_2_q[7]), .in_0({1'b1, _74299_2_pin4[4:0], _74299_1_pin4[7:6]}), .in_1({8{1'b0}}),
    .out(multiplexer_1_out));
  D_FF #(.Bits(8)) d_ff_2 (.D(multiplexer_1_out), .C(xor_1_out), .Q(d_ff_2_q));  // open: nQ
  // Probe PS2_RECEIVED on d_ff_2_q
  // also tied to GND on the sheet: {_74161_1_pin3[1], _74161_1_pin3[3]}
  // also tied to VCC on the sheet: {_74161_1_pin3[0], _74161_1_pin3[2]}

  // Notes on the sheet:
  //   TTYIN_OE: default 1
  //   CLK: Hz: 8
  //   contents of rom_1 (hex, n*v repeats v):
  //   4*406
endmodule

/* Test case TTYIN_OE_ inhibits:
            CLK TTYIN_OE_ PS2_CLK
repeat(100) C   1         0
*/

/* Test case e2e:
            CLK PS2_CLK TTYIN_OE_ TTYIN_CP PS2_READY PS2_RECEIVED
declare PS2_READY = (PS2_RECEIVED>>7)&1;          
            0   1       0         0        0         X
repeat(100) C   X       0         0        X         X
repeat(100) C   0       0         0        1         X
repeat(100) C   0       1         0        1         X
            0   0       1         C        0         0
repeat(100) C   X       0         0        X         X
repeat(100) C   0       0         0        1         0x83
*/
