// Digital circuit ram.dig as structural Verilog
module ram (
  input  CE,
  input  OE,
  input  WE,
  input  [18:0] A,
  output [7:0] D
);

  wire not_1_out, not_2_out, not_3_out;

  not not_1 (not_1_out, CE);
  not not_2 (not_2_out, OE);
  not not_3 (not_3_out, WE);
  RAMSinglePortSel #(.AddrBits(19), .Bits(8)) ramsingleportsel_1 (
    .A(A), .CS(not_1_out), .WE(not_3_out), .OE(not_2_out), .D(D));
endmodule

/* Test case RAM:
A CE_ OE_ WE_ D
0 1   X   X   Z
*/
