// Digital circuit reg.dig as structural Verilog
module \reg  (
  input  OE,
  input  CP,
  input  [7:0] DATA,
  output [7:0] IO
);

  _74299 _74299_1 (
    .pin1(OE), .pin2(OE), .pin3(OE), .pin4(DATA[6]), .pin5(DATA[4]), .pin6(DATA[2]), .pin7(DATA[0]),
    .pin9(1'b1), .pin10(1'b0), .pin11(1'b0), .pin12(CP), .pin13(DATA[1]), .pin14(DATA[3]), .pin15(DATA[5]),
    .pin16(DATA[7]), .pin18(1'b0), .pin19(OE), .pin20(1'b1));  // open: pin8, pin17
  BusSplitter #(.Bits(8)) bussplitter_1 (
    .D(IO), .OE(OE), .D0(DATA[0]), .D1(DATA[1]), .D2(DATA[2]), .D3(DATA[3]), .D4(DATA[4]), .D5(DATA[5]),
    .D6(DATA[6]), .D7(DATA[7]));
  // Probe on DATA[7]

  // Notes on the sheet:
  //   OE: default 1
endmodule

/* Test case:
$DATA OE_ CP IO
Z     1   0  Z
0xAB  1   C  Z
Z     0   0  0xAB
*/
