// Digital circuit uc.dig as structural Verilog
module uc (
  input  CLK,
  input  RESET,
  output [7:0] DATA,
  output ADDR_OE,
  output [2:0] ALU_OP,
  output PC_INC,
  output IN1_CP,
  output ALU_CP,
  output MEM_CP,
  output TTYIN_CP,
  output W_CP,
  output X_CP,
  output Y_CP,
  output Z_CP,
  output A0_CP,
  output A1_CP,
  output A2_CP,
  output TTYOUT_CP,
  output HALT,
  output ALU_OE,
  output MEM_OE,
  output TTYIN_OE,
  output PC_SPE,
  output W_OE,
  output X_OE,
  output Y_OE,
  output Z_OE,
  output [7:0] uIR0,
  output [7:0] uIR1,
  output [18:0] uAddr,
  output [7:0] uPC,
  output [1:0] stage,
  output [7:0] uData
);

  wire _74138_1_pin13, _74138_1_pin15, _74238_1_pin12, _74238_1_pin13, _74238_1_pin14, _74238_1_pin15,
       and_1_out, and_2_out, IR0_p4, IR0_p6, not_1_out, not_2_out, not_3_out, uPC1_pin10;
  wire [7:0] bitextender_1_out;

  not not_1 (not_1_out, and_1_out);
  and and_1 (and_1_out, not_2_out, _74238_1_pin14);
  not not_2 (not_2_out, _74138_1_pin15);
  and and_2 (and_2_out, RESET, not_1_out);
  _74161 uPC1 (
    .pin1(and_2_out), .pin2(CLK), .pin3(1'b0), .pin4(1'b0), .pin5(1'b0), .pin6(1'b0), .pin7(1'b1),
    .pin8(1'b0), .pin9(1'b1), .pin10(uPC1_pin10), .pin11(uAddr[6]), .pin12(uAddr[5]), .pin13(uAddr[4]),
    .pin14(uAddr[3]), .pin16(1'b1));  // open: pin15
  _74161 uPC0 (
    .pin1(and_2_out), .pin2(CLK), .pin3(1'b0), .pin4(1'b0), .pin5(1'b0), .pin6(1'b0), .pin7(1'b1),
    .pin8(1'b0), .pin9(1'b1), .pin10(1'b1), .pin11(uAddr[2]), .pin12(uAddr[1]), .pin13(stage[1]),
    .pin14(stage[0]), .pin15(uPC1_pin10), .pin16(1'b1));
  // _74574 FLAGS: pin names not known; wires that end beside it: 1'b0, 1'b1
  // _74574 IR0: pin names not known; wires that end beside it: 1'b0, 1'b0, 1'b0, IR0_p4, 1'b1, IR0_p6
  _74238 _74238_1 (
    .pin1(stage[0]), .pin2(stage[1]), .pin3(1'b0), .pin4(1'b0), .pin5(CLK), .pin6(1'b1), .pin8(1'b0),
    .pin12(_74238_1_pin12), .pin13(_74238_1_pin13), .pin14(_74238_1_pin14), .pin15(_74238_1_pin15),
    .pin16(1'b1));  // open: pin7, pin9, pin10, pin11
  ROM #(.AddrBits(19), .Bits(8)) uROM (.A({uAddr[18:1], stage[1]}), .sel(1'b1), .D(uData));
  not not_3 (not_3_out, _74238_1_pin12);
  // _74574 uIR1: pin names not known; wires that end beside it: 1'b0, 1'b0, 1'b1, _74238_1_pin13
  // _74574 uIR0: pin names not known; wires that end beside it: 1'b0, 1'b0, 1'b1, _74238_1_pin15
  BitExtender #(.inputBits(4), .outputBits(8)) bitextender_1 (.in(uIR1[7:4]), .out(bitextender_1_out));
  assign DATA = ~_74138_1_pin13 ? bitextender_1_out : 8'bz;  // DriverInvSel driverinvsel_1
  _74238 _74238_2 (
    .pin1(uIR1[0]), .pin2(uIR1[1]), .pin3(uIR1[2]), .pin4(not_3_out), .pin5(uIR1[3]), .pin6(1'b1),
    .pin7(IR0_p4), .pin8(1'b0), .pin10(TTYIN_CP), .pin11(MEM_CP), .pin12(ALU_CP), .pin13(IN1_CP),
    .pin14(IR0_p6), .pin15(PC_INC), .pin16(1'b1));  // open: pin9
  _74238 _74238_3 (
    .pin1(uIR1[0]), .pin2(uIR1[1]), .pin3(uIR1[2]), .pin4(1'b0), .pin5(not_3_out), .pin6(uIR1[3]),
    .pin7(TTYOUT_CP), .pin8(1'b0), .pin9(A2_CP), .pin10(A1_CP), .pin11(A0_CP), .pin12(Z_CP), .pin13(Y_CP),
    .pin14(X_CP), .pin15(W_CP), .pin16(1'b1));
  _74138 _74138_1 (
    .pin1(uIR0[0]), .pin2(uIR0[1]), .pin3(uIR0[2]), .pin4(1'b0), .pin5(uIR0[3]), .pin6(RESET), .pin8(1'b0),
    .pin9(PC_SPE), .pin10(TTYIN_OE), .pin11(MEM_OE), .pin12(ALU_OE), .pin13(_74138_1_pin13), .pin14(HALT),
    .pin15(_74138_1_pin15), .pin16(1'b1));  // open: pin7
  _74138 _74138_2 (
    .pin1(uIR0[0]), .pin2(uIR0[1]), .pin3(uIR0[2]), .pin4(1'b0), .pin5(1'b0), .pin6(uIR0[3]), .pin8(1'b0),
    .pin12(Z_OE), .pin13(Y_OE), .pin14(X_OE), .pin15(W_OE), .pin16(1'b1));  // open: pin7, pin9, pin10, pin11

  assign uAddr[0] = stage[1];
  assign uIR0[7:4] = {ADDR_OE, ALU_OP};
  assign uPC = {uAddr[6:1], stage};

  // Notes on the sheet:
  //   RESET: default 1
  //   2B
  //   1A
  //   1B
  //   1Y
  //   2Y
  //   2A
  //   uROM loads ucode.hex
  //   5A
  //   5Y
endmodule

/* Test case uc:
RESET_ HALT_
0      1
*/
